// Logisim project aaa_4.circ as structural Verilog
module main (
  input  in_1,
  input  [23:0] in_2,
  input  in_3,
  input  in_4,
  output [3:0] out_5
);

  wire clock_1_out, rgb_video_9_p4, rgb_video_9_p5;

  RAM #(.dataWidth(64)) ram_1 ();  // open: addr, we, oe, clk, din, dout
  // PlaRom plarom_1: pin names not known
  // RGB_Video #(.height(256), .scale(1), .width(256)) rgb_video_1: pin names not known
  // RGB_Video #(.height(256), .scale(1), .width(256)) rgb_video_2: pin names not known
  // RGB_Video #(.height(256), .scale(1), .width(256)) rgb_video_3: pin names not known
  // RGB_Video #(.height(256), .scale(1), .width(256)) rgb_video_4: pin names not known
  // RGB_Video #(.height(256), .scale(1), .width(256)) rgb_video_5: pin names not known
  // RGB_Video #(.height(256), .scale(1), .width(256)) rgb_video_6: pin names not known
  // RGB_Video #(.height(256), .scale(1), .width(256)) rgb_video_7: pin names not known
  // RGB_Video #(.height(256), .scale(1), .width(256)) rgb_video_8: pin names not known
  LedBar ledbar_1 ();  // open: led0, led1, led2, led3, led4, led5, led6, led7
  LED led_1 ();  // open: in
  // RGBLED rgbled_1: pin names not known
  Clock clock_1 (.out(clock_1_out));
  RAM #(.addrWidth(24), .dataWidth(32)) ram_2 ();  // open: addr, we, oe, clk, din, dout
  // RGB_Video #(.height(64), .scale(8), .width(64)) rgb_video_9: pin names not known; wires that end beside it: in_3, clock_1_out, in_4, rgb_video_9_p4, rgb_video_9_p5, in_2, rgb_video_9_p5, rgb_video_9_p4
  // RGB_Video #(.height(256), .scale(1), .width(256)) rgb_video_10: pin names not known
  // RGB_Video #(.height(256), .scale(1), .width(256)) rgb_video_11: pin names not known
  // RGB_Video #(.height(256), .scale(1), .width(256)) rgb_video_12: pin names not known
  // RGB_Video #(.height(256), .scale(1), .width(256)) rgb_video_13: pin names not known
  // RGB_Video #(.height(256), .scale(1), .width(256)) rgb_video_14: pin names not known
  // RGB_Video #(.height(256), .scale(1), .width(256)) rgb_video_15: pin names not known
  // RGB_Video #(.height(256), .scale(1), .width(256)) rgb_video_16: pin names not known
  // RGB_Video #(.height(256), .scale(1), .width(256)) rgb_video_17: pin names not known
  RAM #(.addrWidth(12), .dataWidth(32)) ram_3 ();  // open: addr, we, oe, clk, din, dout
  // RGB_Video #(.height(256), .scale(1), .width(256)) rgb_video_18: pin names not known
  // RGB_Video #(.height(256), .scale(1), .width(256)) rgb_video_19: pin names not known
  // RGB_Video #(.height(256), .scale(1), .width(256)) rgb_video_20: pin names not known
  // RGB_Video #(.height(256), .scale(1), .width(256)) rgb_video_21: pin names not known
  // RGB_Video #(.height(256), .scale(1), .width(256)) rgb_video_22: pin names not known
  // RGB_Video #(.height(256), .scale(1), .width(256)) rgb_video_23: pin names not known
  // RGB_Video #(.height(256), .scale(1), .width(256)) rgb_video_24: pin names not known
  // RGB_Video #(.height(256), .scale(1), .width(256)) rgb_video_25: pin names not known
  RAM #(.addrWidth(12), .dataWidth(32)) ram_4 ();  // open: addr, we, oe, clk, din, dout
  // RGB_Video #(.height(256), .scale(1), .width(256)) rgb_video_26: pin names not known
  // RGB_Video #(.height(256), .scale(1), .width(256)) rgb_video_27: pin names not known
  // RGB_Video #(.height(256), .scale(1), .width(256)) rgb_video_28: pin names not known
  // RGB_Video #(.height(256), .scale(1), .width(256)) rgb_video_29: pin names not known
  RAM #(.dataWidth(32)) ram_5 ();  // open: addr, we, oe, clk, din, dout
  // RGB_Video #(.height(256), .scale(1), .width(256)) rgb_video_30: pin names not known
  // RGB_Video #(.height(256), .scale(1), .width(256)) rgb_video_31: pin names not known
  // RGB_Video #(.height(256), .scale(1), .width(256)) rgb_video_32: pin names not known
  // RGB_Video #(.height(256), .scale(1), .width(256)) rgb_video_33: pin names not known
  RAM #(.addrWidth(14), .dataWidth(32)) ram_6 ();  // open: addr, we, oe, clk, din, dout
  RAM #(.addrWidth(18), .dataWidth(32)) ram_7 ();  // open: addr, we, oe, clk, din, dout
  ROM #(.addrWidth(18), .dataWidth(32)) rom_1 ();  // open: addr, data
  Priority_Encoder #(.select(4)) priority_encoder_1 (
    .in15(in_1), .out(out_5));  // open: in0, in1, in2, in3, in4, in5, in6, in7, in8, in9, in10, in11, in12, in13, in14, gs, en_out, en_in
  RAM #(.addrWidth(14), .dataWidth(32)) ram_8 ();  // open: addr, we, oe, clk, din, dout

  // Notes on the sheet:
  //   x
  //   32/4=8bit
  //   128m
  //   256
  //   *2^8
  //   2^3
  //   27
  //   x
  //   y
  //   15
  //   1280*768
  //   contents of rom_1 (hex, n*v repeats v):
  //   ffffff
  //   8+4+2+1
  //   -
endmodule

module RAM_128M (
  input  [23:0] dizhi,
  input  cunqishuru,
  input  cunshu,
  input  clock,
  input  [31:0] I,
  output [31:0] O
);

  RAM #(.addrWidth(24), .dataWidth(32)) ram_1 (
    .addr(dizhi), .we(cunqishuru), .oe(cunshu), .clk(clock), .din(I), .dout(O));

  // Notes on the sheet:
  //   input
  //   out
endmodule

module RAM_DRAM_2G_text (
  output [63:0] wu_0,
  output [63:0] wu_1
);

  wire clock_1_out;

  Clock clock_1 (.out(clock_1_out));
  RAM_128M ram_128m_1 ();  // open: dizhi, cunqishuru, cunshu, clock, I, O
  RAM_128M ram_128m_2 ();  // open: dizhi, cunqishuru, cunshu, clock, I, O
  RAM_128M ram_128m_3 ();  // open: dizhi, cunqishuru, cunshu, clock, I, O
  RAM_128M ram_128m_4 ();  // open: dizhi, cunqishuru, cunshu, clock, I, O
  RAM_128M ram_128m_5 (.clock(clock_1_out), .O(wu_0[31:0]));  // open: dizhi, cunqishuru, cunshu, I
  RAM_128M ram_128m_6 ();  // open: dizhi, cunqishuru, cunshu, clock, I, O
  RAM_128M ram_128m_7 ();  // open: dizhi, cunqishuru, cunshu, clock, I, O
  RAM_128M ram_128m_8 ();  // open: dizhi, cunqishuru, cunshu, clock, I, O
  RAM_128M ram_128m_9 ();  // open: dizhi, cunqishuru, cunshu, clock, I, O
  RAM_128M ram_128m_10 ();  // open: dizhi, cunqishuru, cunshu, clock, I, O
  RAM_128M ram_128m_11 ();  // open: dizhi, cunqishuru, cunshu, clock, I, O
  RAM_128M ram_128m_12 ();  // open: dizhi, cunqishuru, cunshu, clock, I, O
  RAM_128M ram_128m_13 (.O(wu_1[31:0]));  // open: dizhi, cunqishuru, cunshu, clock, I
  RAM_128M ram_128m_14 ();  // open: dizhi, cunqishuru, cunshu, clock, I, O
  RAM_128M ram_128m_15 ();  // open: dizhi, cunqishuru, cunshu, clock, I, O
  RAM_128M ram_128m_16 ();  // open: dizhi, cunqishuru, cunshu, clock, I, O
  RAM_128M ram_128m_17 ();  // open: dizhi, cunqishuru, cunshu, clock, I, O
  RAM_128M ram_128m_18 ();  // open: dizhi, cunqishuru, cunshu, clock, I, O
  RAM_128M ram_128m_19 ();  // open: dizhi, cunqishuru, cunshu, clock, I, O
  RAM_128M ram_128m_20 ();  // open: dizhi, cunqishuru, cunshu, clock, I, O
  RAM_128M ram_128m_21 (.clock(clock_1_out), .O(wu_0[63:32]));  // open: dizhi, cunqishuru, cunshu, I
  RAM_128M ram_128m_22 ();  // open: dizhi, cunqishuru, cunshu, clock, I, O
  RAM_128M ram_128m_23 ();  // open: dizhi, cunqishuru, cunshu, clock, I, O
  RAM_128M ram_128m_24 ();  // open: dizhi, cunqishuru, cunshu, clock, I, O
  RAM_128M ram_128m_25 ();  // open: dizhi, cunqishuru, cunshu, clock, I, O
  RAM_128M ram_128m_26 ();  // open: dizhi, cunqishuru, cunshu, clock, I, O
  RAM_128M ram_128m_27 ();  // open: dizhi, cunqishuru, cunshu, clock, I, O
  RAM_128M ram_128m_28 ();  // open: dizhi, cunqishuru, cunshu, clock, I, O
  RAM_128M ram_128m_29 (.O(wu_1[63:32]));  // open: dizhi, cunqishuru, cunshu, clock, I
  RAM_128M ram_128m_30 ();  // open: dizhi, cunqishuru, cunshu, clock, I, O
  RAM_128M ram_128m_31 ();  // open: dizhi, cunqishuru, cunshu, clock, I, O
  RAM_128M ram_128m_32 ();  // open: dizhi, cunqishuru, cunshu, clock, I, O

  // Notes on the sheet:
  //   0
  //   0
  //   2
  //   4
  //   6
  //   2
  //   4
  //   6
  //   1
  //   1
  //   2^4
  //   3
  //   7
  //   2^4
  //   5
  //   3
  //   5
  //   7
  //   8
  //   10
  //   14
  //   12
  //   8
  //   10
  //   12
  //   14
  //   9
  //   11
  //   13
  //   15
  //   9
  //   11
  //   13
  //   15
endmodule

module fff_x1920_y1080 (
);

  // RGB_Video rgb_video_1: pin names not known
endmodule

module fff_x1280_y768 (
  output out_1
);

  DipSwitch dipswitch_1 ();  // open: sw1, sw2, sw3, sw4, sw5, sw6, sw7, sw8
  // RGB_Video #(.height(256), .width(256)) rgb_video_1: pin names not known
  // RGB_Video #(.height(256), .width(256)) rgb_video_2: pin names not known
  // RGB_Video #(.height(256), .width(256)) rgb_video_3: pin names not known
  // RGB_Video #(.height(256), .width(256)) rgb_video_4: pin names not known
  RAM #(.addrWidth(16), .dataWidth(32)) ram_1 ();  // open: addr, we, oe, clk, din, dout
  // RGB_Video #(.height(256), .width(256)) rgb_video_5: pin names not known
  // RGB_Video #(.height(256), .width(256)) rgb_video_6: pin names not known
  // RGB_Video #(.height(256), .width(256)) rgb_video_7: pin names not known
  // RGB_Video #(.height(256), .width(256)) rgb_video_8: pin names not known
  // RGB_Video #(.height(256), .width(256)) rgb_video_9: pin names not known
  // RGB_Video #(.height(256), .width(256)) rgb_video_10: pin names not known
  // RGB_Video #(.height(256), .width(256)) rgb_video_11: pin names not known
  // RGB_Video #(.height(256), .width(256)) rgb_video_12: pin names not known
  // RGB_Video #(.height(256), .width(256)) rgb_video_13: pin names not known
  // RGB_Video #(.height(256), .width(256)) rgb_video_14: pin names not known
  // RGB_Video #(.height(256), .width(256)) rgb_video_15: pin names not known
  // RGB_Video #(.height(256), .width(256)) rgb_video_16: pin names not known
  // RGB_Video #(.height(256), .width(256)) rgb_video_17: pin names not known
  // RGB_Video #(.height(256), .width(256)) rgb_video_18: pin names not known
  // RGB_Video #(.height(256), .width(256)) rgb_video_19: pin names not known
  // RGB_Video #(.height(256), .width(256)) rgb_video_20: pin names not known
  // RGB_Video #(.height(256), .width(256)) rgb_video_21: pin names not known
  // RGB_Video #(.height(256), .width(256)) rgb_video_22: pin names not known
  // RGB_Video #(.height(256), .width(256)) rgb_video_23: pin names not known
  // RGB_Video #(.height(256), .width(256)) rgb_video_24: pin names not known
  // RGB_Video #(.height(256), .width(256)) rgb_video_25: pin names not known
  // RGB_Video #(.height(256), .width(256)) rgb_video_26: pin names not known
  // RGB_Video #(.height(256), .width(256)) rgb_video_27: pin names not known
  // RGB_Video #(.height(256), .width(256)) rgb_video_28: pin names not known
  // RGB_Video #(.height(256), .width(256)) rgb_video_29: pin names not known
  // RGB_Video #(.height(256), .width(256)) rgb_video_30: pin names not known
  // RGB_Video #(.height(256), .width(256)) rgb_video_31: pin names not known
  // RGB_Video #(.height(256), .width(256)) rgb_video_32: pin names not known
  // RGB_Video rgb_video_33: pin names not known
  RAM #(.addrWidth(20), .dataWidth(32), .\type ("nonvolatile")) ram_2 ();  // open: addr, we, oe, clk, din, dout
  RAM #(.addrWidth(24), .dataWidth(32), .\type ("nonvolatile")) ram_3 ();  // open: addr, we, oe, clk, din, dout
  RAM #(.addrWidth(16), .dataWidth(32)) ram_4 ();  // open: addr, we, oe, clk, din, dout
  RAM #(.addrWidth(21), .dataWidth(32), .\type ("nonvolatile")) ram_5 ();  // open: addr, we, oe, clk, din, dout

  // Notes on the sheet:
  //   x_2
  //   sfasfddd
  //   y_2
  //   2048*1024
  //   512*256
  //   *2^1*2^5*2^6
  //   16+12
  //   2^4
  //   *8*t(s)
  //   *t(s)/2^2
  //   64
endmodule

module f_x16_y16 (
  input  in_1,
  input  in_2,
  input  in_3,
  input  in_4,
  input  [23:0] in_5,
  input  in_6,
  input  [23:0] in_7,
  input  in_8,
  input  in_9,
  input  in_10,
  input  in_11,
  input  in_12,
  input  in_13,
  input  [3:0] in_14,
  input  in_15,
  input  [23:0] in_16,
  input  in_17,
  input  [3:0] in_18,
  input  in_19,
  input  in_20,
  input  in_21,
  input  [7:0] in_22,
  input  in_23,
  input  [23:0] in_24,
  output out_25,
  output [3:0] out_26
);

  wire cl, clock_2_out, clock_3_out, clock_4_out, clock_5_out, clock_6_out, multiplexer_3_out,
       shift_register_1_p1, undriven, undriven_2, undriven_4, undriven_5, undriven_6;
  wire [3:0] adder_1_out, and_1_out, register_1_q, shift_register_1_p2;
  wire [7:0] d, ram_1_dout_2, register_2_q, rgb_video_1_p3;
  wire [15:1] undriven_3;
  wire [23:0] i, ram_1_dout, ram_6_dout, rgb_video_2_p7, undriven_7;

  // Shift_Register shift_register_1: pin names not known; wires that end beside it: shift_register_1_p1, shift_register_1_p2
  Random random_1 ();  // open: clr, next, clk, out
  Counter #(.max('hf), .width(4)) counter_1 (
    .clr(in_10), .load(in_11), .up(undriven_2), .count(undriven), .clk(shift_register_1_p1),
    .D(shift_register_1_p2));  // open: carry, Q
  Clock clock_1 (.out(cl));
  Clock clock_2 (.out(clock_2_out));
  Clock clock_3 (.out(clock_3_out));
  // RGB_Video #(.scale(1)) rgb_video_1: pin names not known; wires that end beside it: undriven_3[15:4], in_5, rgb_video_1_p3
  // RGB_Video #(.height(16), .scale(8), .width(16)) rgb_video_2: pin names not known; wires that end beside it: in_8, clock_2_out, in_9, d[3:0], d[7:4], i, rgb_video_2_p7
  D_Flip_Flop d_ff_1 ();  // open: D, clk, Q, Qn, preset, reset
  Register #(.width(4)) register_1 (.D(adder_1_out), .en(in_12), .clk(clock_3_out), .Q(register_1_q), .clr(in_13));
  Adder #(.width(4)) adder_1 (.a(register_1_q), .b(in_14), .out(adder_1_out));  // open: cin, cout
  assign and_1_out = {3'b000, in_17} & {4{in_20}};  // AND_Gate and_1, 4 bits wide
  // RGB_Video #(.height(256), .scale(1), .width(256)) rgb_video_3: pin names not known
  Clock clock_4 (.out(clock_4_out));
  Multiplexer #(.width(24)) multiplexer_1 (.in0(in_5), .in1(ram_1_dout), .out(rgb_video_2_p7), .sel(in_6));
  Multiplexer #(.width(4)) multiplexer_2 (.in0(in_14), .in1(and_1_out), .out(out_26), .sel(in_15));
  RAM #(.dataWidth(32), .\type ("nonvolatile")) ram_1 (
    .addr(d), .we(in_2), .oe(in_4), .clk(clock_4_out), .dout({ram_1_dout_2, ram_1_dout}));  // open: din
  Clock #(.highDuration(2048)) clock_5 (.out(clock_5_out));
  Multiplexer multiplexer_3 (.in0(clock_5_out), .in1(clock_6_out), .out(multiplexer_3_out), .sel(in_23));
  RAM #(.addrWidth(6), .dataWidth(4)) ram_2 ();  // open: addr, we, oe, clk, din, dout
  Clock clock_6 (.out(clock_6_out));
  RAM #(.dataWidth(24)) ram_3 ();  // open: addr, we, oe, clk, din, dout
  Register register_2 (.D(d), .en(in_19), .clk(multiplexer_3_out), .Q(register_2_q), .clr(in_21));
  RAM #(.addrWidth(12), .dataWidth(32)) ram_4 ();  // open: addr, we, oe, clk, din, dout
  Adder adder_2 (.a(register_2_q), .b(in_22), .out(d));  // open: cin, cout
  RAM #(.addrWidth(12), .dataWidth(32)) ram_5 ();  // open: addr, we, oe, clk, din, dout
  // Probe on undriven_7
  RAM #(.addrWidth(24), .dataWidth(24), .\type ("nonvolatile")) ram_6 (
    .addr(undriven_7), .we(undriven_5), .oe(undriven_4), .clk(undriven_6), .din(in_16), .dout(ram_6_dout));
  RAM #(.addrWidth(24), .dataWidth(24), .\type ("nonvolatile")) ram_7 (
    .addr({{16{1'b0}}, d}), .we(in_1), .oe(in_3), .clk(cl), .din(in_24), .dout(i));
  // Pins of 1 and 16 bits meet at {undriven_3, 1'b0}

  // Other names for the same wires on the sheet: cu = in_1; d_8_24[7:0] = d; data[7:0] = d; data_2[7:0] = d;
  //   x[3:0] = d[3:0]; y[3:0] = d[7:4]; load = in_3

  // Notes on the sheet:
  //   in_5: initial=0xb70034
endmodule

module f_x256_y256 (
  input  in_1,
  input  in_2,
  input  in_3,
  input  in_4,
  input  [23:0] in_5,
  input  [23:0] in_6,
  input  in_7,
  input  in_8,
  input  in_9,
  input  in_10,
  input  in_11,
  input  in_12,
  input  in_13,
  input  in_14,
  input  in_15,
  input  in_16,
  input  [7:0] in_17,
  input  in_18,
  input  in_19,
  input  in_20,
  input  [7:0] in_21,
  input  [7:0] in_22,
  input  in_23,
  input  in_24,
  input  in_25,
  input  in_26,
  input  [15:0] in_27,
  input  in_28
);

  wire a, clock_1_out, clock_2_out, clock_3_out, clock_4_out, clock_8_out, clock_9_out, clock_11_out,
       clock_12_out, digital_oscilloscope_1_p1, digital_oscilloscope_1_p3, digital_oscilloscope_1_p4,
       digital_oscilloscope_2_p2, multiplexer_2_out, multiplexer_3_out, multiplexer_4_out, multiplexer_6_out,
       switch_1_p1, switch_1_p2;
  wire [7:0] d, ram_1_dout_2, ram_2_dout_2, register_1_q, register_2_q, register_4_q, x_256_0, y_256_0;
  wire [15:0] d_16, register_3_q;
  wire [23:0] ram_1_dout, ram_2_dout, rgb_video_1_p6, rgb_video_2_p7;

  Clock clock_1 (.out(clock_1_out));
  // RGB_Video #(.height(16), .scale(8), .width(16)) rgb_video_1: pin names not known; wires that end beside it: in_8, clock_1_out, in_11, d[3:0], d[7:4], rgb_video_1_p6
  Clock clock_2 (.out(clock_2_out));
  Multiplexer #(.width(24)) multiplexer_1 (.in0(in_5), .in1(ram_1_dout), .out(rgb_video_1_p6), .sel(in_7));
  Multiplexer multiplexer_2 (.in0(clock_3_out), .in1(clock_4_out), .out(multiplexer_2_out), .sel(in_18));
  RAM #(.dataWidth(32), .\type ("nonvolatile")) ram_1 (
    .addr(d), .we(in_1), .oe(in_2), .clk(clock_2_out), .dout({ram_1_dout_2, ram_1_dout}));  // open: din
  Clock #(.highDuration(2048)) clock_3 (.out(clock_3_out));
  Clock clock_4 (.out(clock_4_out));
  Register register_1 (.D(d), .en(in_13), .clk(multiplexer_2_out), .Q(register_1_q), .clr(in_16));
  Adder adder_1 (.a(register_1_q), .b(in_17), .out(d));  // open: cin, cout
  // Switch switch_1: pin names not known; wires that end beside it: switch_1_p1, switch_1_p2
  // Digital_Oscilloscope digital_oscilloscope_1: pin names not known; wires that end beside it: digital_oscilloscope_1_p1, switch_1_p2, digital_oscilloscope_1_p3, digital_oscilloscope_1_p4
  // Switch switch_2: pin names not known; wires that end beside it: digital_oscilloscope_1_p4, digital_oscilloscope_1_p3
  Clock clock_5 (.out(digital_oscilloscope_1_p1));
  // Digital_Oscilloscope digital_oscilloscope_2: pin names not known; wires that end beside it: a, digital_oscilloscope_2_p2, digital_oscilloscope_2_p2
  // RGB_Video #(.height(256), .scale(1), .width(256)) rgb_video_2: pin names not known; wires that end beside it: digital_oscilloscope_1_p1, in_10, digital_oscilloscope_1_p1, in_12, d_16[7:0], d_16[15:8], rgb_video_2_p7
  Clock #(.highDuration(2048)) clock_6 (.out(switch_1_p1));
  Multiplexer multiplexer_3 (.in0(switch_1_p1), .in1(digital_oscilloscope_1_p3), .out(multiplexer_3_out), .sel(in_23));
  Clock clock_7 (.out(digital_oscilloscope_1_p3));
  Multiplexer multiplexer_4 (.in0(clock_8_out), .in1(clock_9_out), .out(multiplexer_4_out), .sel(in_28));
  Clock #(.highDuration(2048)) clock_8 (.out(clock_8_out));
  Clock clock_9 (.out(clock_9_out));
  Slider slider_1 ();  // open: out
  Register register_2 (.D(x_256_0), .en(in_14), .clk(multiplexer_3_out), .Q(register_2_q), .clr(in_19));
  Adder adder_2 (.a(register_2_q), .b(in_21), .out(x_256_0));  // open: cin, cout
  Register #(.width(16)) register_3 (.D(d_16), .en(in_25), .clk(multiplexer_4_out), .Q(register_3_q), .clr(in_26));
  Clock clock_10 (.out(a));
  Multiplexer #(.width(24)) multiplexer_5 (.in0(in_6), .in1(ram_2_dout), .out(rgb_video_2_p7), .sel(in_9));
  Adder #(.width(16)) adder_3 (.a(register_3_q), .b(in_27), .out(d_16));  // open: cin, cout
  RAM #(.addrWidth(16), .dataWidth(32), .\type ("nonvolatile")) ram_2 (
    .addr(d_16), .we(in_3), .oe(in_4), .clk(a), .dout({ram_2_dout_2, ram_2_dout}));  // open: din
  Multiplexer multiplexer_6 (.in0(clock_11_out), .in1(clock_12_out), .out(multiplexer_6_out), .sel(in_24));
  Clock #(.highDuration(2048)) clock_11 (.out(clock_11_out));
  Clock clock_12 (.out(clock_12_out));
  Register register_4 (.D(y_256_0), .en(in_15), .clk(multiplexer_6_out), .Q(register_4_q), .clr(in_20));
  Adder adder_4 (.a(register_4_q), .b(in_22), .out(y_256_0));  // open: cin, cout

  // Other names for the same wires on the sheet: x[3:0] = d[3:0]; y[3:0] = d[7:4]; x_256[7:0] = d_16[7:0];
  //   x_y_256[15:0] = d_16; y_256[7:0] = d_16[15:8]

  // Notes on the sheet:
  //   in_6: initial=0xb70034
  //   in_5: initial=0xb70034
endmodule

module x2560_y2560_text (
  input  [7:0] in_1,
  input  in_2,
  output [7:0] out_3,
  output out_4
);

  // RGB_Video #(.height(256), .scale(1), .width(256)) rgb_video_1: pin names not known
  // RGB_Video #(.height(256), .scale(1), .width(256)) rgb_video_2: pin names not known
  // RGB_Video #(.height(256), .scale(1), .width(256)) rgb_video_3: pin names not known
  // RGB_Video #(.height(256), .scale(1), .width(256)) rgb_video_4: pin names not known
  // RGB_Video #(.height(256), .scale(1), .width(256)) rgb_video_5: pin names not known
  // RGB_Video #(.height(256), .scale(1), .width(256)) rgb_video_6: pin names not known
  // RGB_Video #(.height(256), .scale(1), .width(256)) rgb_video_7: pin names not known
  // RGB_Video #(.height(256), .scale(1), .width(256)) rgb_video_8: pin names not known
  // RGB_Video rgb_video_9: pin names not known
  // RGB_Video rgb_video_10: pin names not known
  // RGB_Video rgb_video_11: pin names not known
  // RGB_Video rgb_video_12: pin names not known
  // RGB_Video rgb_video_13: pin names not known
  // RGB_Video rgb_video_14: pin names not known
  // RGB_Video rgb_video_15: pin names not known
  // RGB_Video rgb_video_16: pin names not known
  // RGB_Video #(.height(256), .scale(1), .width(256)) rgb_video_17: pin names not known
  // RGB_Video #(.height(256), .scale(1), .width(256)) rgb_video_18: pin names not known
  // RGB_Video #(.height(256), .scale(1), .width(256)) rgb_video_19: pin names not known
  // RGB_Video #(.height(256), .scale(1), .width(256)) rgb_video_20: pin names not known
  // RGB_Video #(.height(256), .scale(1), .width(256)) rgb_video_21: pin names not known
  // RGB_Video #(.height(256), .scale(1), .width(256)) rgb_video_22: pin names not known
  // RGB_Video #(.height(256), .scale(1), .width(256)) rgb_video_23: pin names not known
  // RGB_Video #(.height(256), .scale(1), .width(256)) rgb_video_24: pin names not known
  // RGB_Video rgb_video_25: pin names not known
  // RGB_Video rgb_video_26: pin names not known
  // RGB_Video rgb_video_27: pin names not known
  // RGB_Video rgb_video_28: pin names not known
  // RGB_Video rgb_video_29: pin names not known
  // RGB_Video rgb_video_30: pin names not known
  // RGB_Video rgb_video_31: pin names not known
  // RGB_Video rgb_video_32: pin names not known
  // RGB_Video #(.height(256), .scale(1), .width(256)) rgb_video_33: pin names not known
  // RGB_Video #(.height(256), .scale(1), .width(256)) rgb_video_34: pin names not known
  // RGB_Video #(.height(256), .scale(1), .width(256)) rgb_video_35: pin names not known
  // RGB_Video #(.height(256), .scale(1), .width(256)) rgb_video_36: pin names not known
  // RGB_Video #(.height(256), .scale(1), .width(256)) rgb_video_37: pin names not known
  // RGB_Video #(.height(256), .scale(1), .width(256)) rgb_video_38: pin names not known
  // RGB_Video #(.height(256), .scale(1), .width(256)) rgb_video_39: pin names not known
  // RGB_Video #(.height(256), .scale(1), .width(256)) rgb_video_40: pin names not known
  // RGB_Video rgb_video_41: pin names not known
  // RGB_Video rgb_video_42: pin names not known
  // RGB_Video rgb_video_43: pin names not known
  // RGB_Video rgb_video_44: pin names not known
  // RGB_Video rgb_video_45: pin names not known
  // RGB_Video rgb_video_46: pin names not known
  // RGB_Video rgb_video_47: pin names not known
  // RGB_Video rgb_video_48: pin names not known
  // RGB_Video #(.height(256), .scale(1), .width(256)) rgb_video_49: pin names not known
  // RGB_Video #(.height(256), .scale(1), .width(256)) rgb_video_50: pin names not known
  // RGB_Video #(.height(256), .scale(1), .width(256)) rgb_video_51: pin names not known
  // RGB_Video #(.height(256), .scale(1), .width(256)) rgb_video_52: pin names not known
  // RGB_Video #(.height(256), .scale(1), .width(256)) rgb_video_53: pin names not known
  // RGB_Video #(.height(256), .scale(1), .width(256)) rgb_video_54: pin names not known
  // RGB_Video #(.height(256), .scale(1), .width(256)) rgb_video_55: pin names not known
  // RGB_Video #(.height(256), .scale(1), .width(256)) rgb_video_56: pin names not known
  // RGB_Video rgb_video_57: pin names not known
  // RGB_Video rgb_video_58: pin names not known
  // RGB_Video rgb_video_59: pin names not known
  // RGB_Video rgb_video_60: pin names not known
  // RGB_Video rgb_video_61: pin names not known
  // RGB_Video rgb_video_62: pin names not known
  // RGB_Video rgb_video_63: pin names not known
  // RGB_Video rgb_video_64: pin names not known
  POR por_1 (.out(out_4));
  // RGB_Video #(.height(256), .scale(1), .width(256)) rgb_video_65: pin names not known
  // RGB_Video #(.height(256), .scale(1), .width(256)) rgb_video_66: pin names not known
  // RGB_Video #(.height(256), .scale(1), .width(256)) rgb_video_67: pin names not known
  // RGB_Video #(.height(256), .scale(1), .width(256)) rgb_video_68: pin names not known
  // RGB_Video #(.height(256), .scale(1), .width(256)) rgb_video_69: pin names not known
  // RGB_Video #(.height(256), .scale(1), .width(256)) rgb_video_70: pin names not known
  // RGB_Video #(.height(256), .scale(1), .width(256)) rgb_video_71: pin names not known
  // RGB_Video #(.height(256), .scale(1), .width(256)) rgb_video_72: pin names not known
  // PortIO portio_1: pin names not known; wires that end beside it: in_2, in_1, out_3
  // PortIO a: pin names not known
  // RGB_Video rgb_video_73: pin names not known
  // RGB_Video rgb_video_74: pin names not known
  // RGB_Video rgb_video_75: pin names not known
  // RGB_Video rgb_video_76: pin names not known
  // RGB_Video rgb_video_77: pin names not known
  // RGB_Video rgb_video_78: pin names not known
  // RGB_Video rgb_video_79: pin names not known
  // RGB_Video rgb_video_80: pin names not known
  // RGB_Video #(.height(256), .scale(1), .width(256)) rgb_video_81: pin names not known
  // RGB_Video #(.height(256), .scale(1), .width(256)) rgb_video_82: pin names not known
  // RGB_Video #(.height(256), .scale(1), .width(256)) rgb_video_83: pin names not known
  // RGB_Video #(.height(256), .scale(1), .width(256)) rgb_video_84: pin names not known
  // RGB_Video #(.height(256), .scale(1), .width(256)) rgb_video_85: pin names not known
  // RGB_Video #(.height(256), .scale(1), .width(256)) rgb_video_86: pin names not known
  // RGB_Video #(.height(256), .scale(1), .width(256)) rgb_video_87: pin names not known
  // RGB_Video #(.height(256), .scale(1), .width(256)) rgb_video_88: pin names not known
  Transistor transistor_1 ();  // open: in, out, gate
  // RGB_Video rgb_video_89: pin names not known
  // RGB_Video rgb_video_90: pin names not known
  // RGB_Video rgb_video_91: pin names not known
  // RGB_Video rgb_video_92: pin names not known
  // RGB_Video rgb_video_93: pin names not known
  // RGB_Video rgb_video_94: pin names not known
  // RGB_Video rgb_video_95: pin names not known
  // RGB_Video rgb_video_96: pin names not known
  // RGB_Video #(.height(256), .scale(1), .width(256)) rgb_video_97: pin names not known
  // RGB_Video #(.height(256), .scale(1), .width(256)) rgb_video_98: pin names not known
  // RGB_Video #(.height(256), .scale(1), .width(256)) rgb_video_99: pin names not known
  // RGB_Video #(.height(256), .scale(1), .width(256)) rgb_video_100: pin names not known
  // RGB_Video #(.height(256), .scale(1), .width(256)) rgb_video_101: pin names not known
  // RGB_Video #(.height(256), .scale(1), .width(256)) rgb_video_102: pin names not known
  // RGB_Video #(.height(256), .scale(1), .width(256)) rgb_video_103: pin names not known
  // RGB_Video #(.height(256), .scale(1), .width(256)) rgb_video_104: pin names not known
  // RGB_Video rgb_video_105: pin names not known
  // RGB_Video rgb_video_106: pin names not known
  // RGB_Video rgb_video_107: pin names not known
  // RGB_Video rgb_video_108: pin names not known
  // RGB_Video rgb_video_109: pin names not known
  // RGB_Video rgb_video_110: pin names not known
  // RGB_Video rgb_video_111: pin names not known
  // RGB_Video rgb_video_112: pin names not known
  // RGB_Video #(.height(256), .scale(1), .width(256)) rgb_video_113: pin names not known
  // RGB_Video #(.height(256), .scale(1), .width(256)) rgb_video_114: pin names not known
  // RGB_Video #(.height(256), .scale(1), .width(256)) rgb_video_115: pin names not known
  // RGB_Video #(.height(256), .scale(1), .width(256)) rgb_video_116: pin names not known
  // RGB_Video #(.height(256), .scale(1), .width(256)) rgb_video_117: pin names not known
  // RGB_Video #(.height(256), .scale(1), .width(256)) rgb_video_118: pin names not known
  // RGB_Video #(.height(256), .scale(1), .width(256)) rgb_video_119: pin names not known
  // RGB_Video #(.height(256), .scale(1), .width(256)) rgb_video_120: pin names not known
  RAM #(.addrWidth(22), .dataWidth(32)) ram_1 ();  // open: addr, we, oe, clk, din, dout
  // RGB_Video rgb_video_121: pin names not known
  // RGB_Video rgb_video_122: pin names not known
  // RGB_Video rgb_video_123: pin names not known
  // RGB_Video rgb_video_124: pin names not known
  // RGB_Video rgb_video_125: pin names not known
  // RGB_Video rgb_video_126: pin names not known
  // RGB_Video rgb_video_127: pin names not known
  // RGB_Video rgb_video_128: pin names not known
  // RGB_Video #(.height(256), .scale(1), .width(256)) rgb_video_129: pin names not known
  // RGB_Video #(.height(256), .scale(1), .width(256)) rgb_video_130: pin names not known
  // RGB_Video #(.height(256), .scale(1), .width(256)) rgb_video_131: pin names not known
  // RGB_Video #(.height(256), .scale(1), .width(256)) rgb_video_132: pin names not known
  // RGB_Video #(.height(256), .scale(1), .width(256)) rgb_video_133: pin names not known
  // RGB_Video #(.height(256), .scale(1), .width(256)) rgb_video_134: pin names not known
  // RGB_Video #(.height(256), .scale(1), .width(256)) rgb_video_135: pin names not known
  // RGB_Video #(.height(256), .scale(1), .width(256)) rgb_video_136: pin names not known
  // RGB_Video rgb_video_137: pin names not known
  // RGB_Video rgb_video_138: pin names not known
  // RGB_Video rgb_video_139: pin names not known
  // RGB_Video rgb_video_140: pin names not known
  // RGB_Video rgb_video_141: pin names not known
  // RGB_Video rgb_video_142: pin names not known
  // RGB_Video rgb_video_143: pin names not known
  // RGB_Video rgb_video_144: pin names not known
  // RGB_Video #(.height(256), .scale(1), .width(256)) rgb_video_145: pin names not known
  // RGB_Video #(.height(256), .scale(1), .width(256)) rgb_video_146: pin names not known
  // RGB_Video #(.height(256), .scale(1), .width(256)) rgb_video_147: pin names not known
  // RGB_Video #(.height(256), .scale(1), .width(256)) rgb_video_148: pin names not known
  // RGB_Video #(.height(256), .scale(1), .width(256)) rgb_video_149: pin names not known
  // RGB_Video #(.height(256), .scale(1), .width(256)) rgb_video_150: pin names not known
  // RGB_Video #(.height(256), .scale(1), .width(256)) rgb_video_151: pin names not known
  // RGB_Video #(.height(256), .scale(1), .width(256)) rgb_video_152: pin names not known
  RAM #(.addrWidth(23), .dataWidth(32)) ram_2 ();  // open: addr, we, oe, clk, din, dout
  // RGB_Video rgb_video_153: pin names not known
  // RGB_Video rgb_video_154: pin names not known
  // RGB_Video rgb_video_155: pin names not known
  // RGB_Video rgb_video_156: pin names not known
  // RGB_Video rgb_video_157: pin names not known
  // RGB_Video rgb_video_158: pin names not known
  // RGB_Video rgb_video_159: pin names not known
  // RGB_Video rgb_video_160: pin names not known
  // RGB_Video #(.height(256), .scale(1), .width(256)) rgb_video_161: pin names not known
  // RGB_Video #(.height(256), .scale(1), .width(256)) rgb_video_162: pin names not known
  // RGB_Video #(.height(256), .scale(1), .width(256)) rgb_video_163: pin names not known
  // RGB_Video #(.height(256), .scale(1), .width(256)) rgb_video_164: pin names not known
  // RGB_Video #(.height(256), .scale(1), .width(256)) rgb_video_165: pin names not known
  // RGB_Video #(.height(256), .scale(1), .width(256)) rgb_video_166: pin names not known
  // RGB_Video #(.height(256), .scale(1), .width(256)) rgb_video_167: pin names not known
  // RGB_Video #(.height(256), .scale(1), .width(256)) rgb_video_168: pin names not known
  // RGB_Video rgb_video_169: pin names not known
  // RGB_Video rgb_video_170: pin names not known
  // RGB_Video rgb_video_171: pin names not known
  // RGB_Video rgb_video_172: pin names not known
  // RGB_Video rgb_video_173: pin names not known
  // RGB_Video rgb_video_174: pin names not known
  // RGB_Video rgb_video_175: pin names not known
  // RGB_Video rgb_video_176: pin names not known
  // RGB_Video #(.height(256), .scale(1), .width(256)) rgb_video_177: pin names not known
  // RGB_Video #(.height(256), .scale(1), .width(256)) rgb_video_178: pin names not known
  // RGB_Video #(.height(256), .scale(1), .width(256)) rgb_video_179: pin names not known
  // RGB_Video #(.height(256), .scale(1), .width(256)) rgb_video_180: pin names not known
  // RGB_Video #(.height(256), .scale(1), .width(256)) rgb_video_181: pin names not known
  // RGB_Video #(.height(256), .scale(1), .width(256)) rgb_video_182: pin names not known
  // RGB_Video #(.height(256), .scale(1), .width(256)) rgb_video_183: pin names not known
  // RGB_Video #(.height(256), .scale(1), .width(256)) rgb_video_184: pin names not known
  // RGB_Video rgb_video_185: pin names not known
  // RGB_Video rgb_video_186: pin names not known
  // RGB_Video rgb_video_187: pin names not known
  // RGB_Video rgb_video_188: pin names not known
  // RGB_Video rgb_video_189: pin names not known
  // RGB_Video rgb_video_190: pin names not known
  // RGB_Video rgb_video_191: pin names not known
  // RGB_Video rgb_video_192: pin names not known
  // RGB_Video #(.height(256), .scale(1), .width(256)) rgb_video_193: pin names not known
  // RGB_Video #(.height(256), .scale(1), .width(256)) rgb_video_194: pin names not known
  // RGB_Video #(.height(256), .scale(1), .width(256)) rgb_video_195: pin names not known
  // RGB_Video #(.height(256), .scale(1), .width(256)) rgb_video_196: pin names not known
  // RGB_Video #(.height(256), .scale(1), .width(256)) rgb_video_197: pin names not known
  // RGB_Video #(.height(256), .scale(1), .width(256)) rgb_video_198: pin names not known
  // RGB_Video #(.height(256), .scale(1), .width(256)) rgb_video_199: pin names not known
  // RGB_Video #(.height(256), .scale(1), .width(256)) rgb_video_200: pin names not known
  // RGB_Video rgb_video_201: pin names not known
  // RGB_Video rgb_video_202: pin names not known
  // RGB_Video rgb_video_203: pin names not known
  // RGB_Video rgb_video_204: pin names not known
  // RGB_Video rgb_video_205: pin names not known
  // RGB_Video rgb_video_206: pin names not known
  // RGB_Video rgb_video_207: pin names not known
  // RGB_Video rgb_video_208: pin names not known
  // RGB_Video #(.height(256), .scale(1), .width(256)) rgb_video_209: pin names not known
  // RGB_Video #(.height(256), .scale(1), .width(256)) rgb_video_210: pin names not known
  // RGB_Video #(.height(256), .scale(1), .width(256)) rgb_video_211: pin names not known
  // RGB_Video #(.height(256), .scale(1), .width(256)) rgb_video_212: pin names not known
  // RGB_Video #(.height(256), .scale(1), .width(256)) rgb_video_213: pin names not known
  // RGB_Video #(.height(256), .scale(1), .width(256)) rgb_video_214: pin names not known
  // RGB_Video #(.height(256), .scale(1), .width(256)) rgb_video_215: pin names not known
  // RGB_Video #(.height(256), .scale(1), .width(256)) rgb_video_216: pin names not known
  RAM #(.addrWidth(24), .dataWidth(32)) ram_3 ();  // open: addr, we, oe, clk, din, dout
  // RGB_Video rgb_video_217: pin names not known
  // RGB_Video rgb_video_218: pin names not known
  // RGB_Video rgb_video_219: pin names not known
  // RGB_Video rgb_video_220: pin names not known
  // RGB_Video rgb_video_221: pin names not known
  // RGB_Video rgb_video_222: pin names not known
  // RGB_Video rgb_video_223: pin names not known
  // RGB_Video rgb_video_224: pin names not known
  // RGB_Video #(.height(256), .scale(1), .width(256)) rgb_video_225: pin names not known
  // RGB_Video #(.height(256), .scale(1), .width(256)) rgb_video_226: pin names not known
  // RGB_Video #(.height(256), .scale(1), .width(256)) rgb_video_227: pin names not known
  // RGB_Video #(.height(256), .scale(1), .width(256)) rgb_video_228: pin names not known
  // RGB_Video #(.height(256), .scale(1), .width(256)) rgb_video_229: pin names not known
  // RGB_Video #(.height(256), .scale(1), .width(256)) rgb_video_230: pin names not known
  // RGB_Video #(.height(256), .scale(1), .width(256)) rgb_video_231: pin names not known
  // RGB_Video #(.height(256), .scale(1), .width(256)) rgb_video_232: pin names not known
  RAM #(.addrWidth(24), .dataWidth(32)) ram_4 ();  // open: addr, we, oe, clk, din, dout
  // RGB_Video rgb_video_233: pin names not known
  // RGB_Video rgb_video_234: pin names not known
  // RGB_Video rgb_video_235: pin names not known
  // RGB_Video rgb_video_236: pin names not known
  // RGB_Video rgb_video_237: pin names not known
  // RGB_Video rgb_video_238: pin names not known
  // RGB_Video rgb_video_239: pin names not known
  // RGB_Video rgb_video_240: pin names not known
  // RGB_Video #(.height(256), .scale(1), .width(256)) rgb_video_241: pin names not known
  // RGB_Video #(.height(256), .scale(1), .width(256)) rgb_video_242: pin names not known
  // RGB_Video #(.height(256), .scale(1), .width(256)) rgb_video_243: pin names not known
  // RGB_Video #(.height(256), .scale(1), .width(256)) rgb_video_244: pin names not known
  // RGB_Video #(.height(256), .scale(1), .width(256)) rgb_video_245: pin names not known
  // RGB_Video #(.height(256), .scale(1), .width(256)) rgb_video_246: pin names not known
  // RGB_Video #(.height(256), .scale(1), .width(256)) rgb_video_247: pin names not known
  // RGB_Video #(.height(256), .scale(1), .width(256)) rgb_video_248: pin names not known
  RAM #(.addrWidth(24), .dataWidth(32)) ram_5 ();  // open: addr, we, oe, clk, din, dout
  // RGB_Video rgb_video_249: pin names not known
  // RGB_Video rgb_video_250: pin names not known
  // RGB_Video rgb_video_251: pin names not known
  // RGB_Video rgb_video_252: pin names not known
  // RGB_Video rgb_video_253: pin names not known
  // RGB_Video rgb_video_254: pin names not known
  // RGB_Video rgb_video_255: pin names not known
  // RGB_Video rgb_video_256: pin names not known
  RAM #(.addrWidth(24), .dataWidth(32)) ram_6 ();  // open: addr, we, oe, clk, din, dout

  // Notes on the sheet:
  //   y
  //   -6*256^2
  //   +2^16
  //   x
endmodule

module x2560_y1600_x1280_y768 (
  input  in_1,
  input  in_2,
  input  [7:0] in_3,
  input  in_4,
  input  in_5,
  input  in_6,
  input  in_7,
  input  in_8,
  input  [7:0] in_9,
  input  in_10,
  input  in_11,
  input  in_12,
  input  [15:0] in_13,
  input  in_14,
  input  in_15,
  input  in_16,
  input  [1:0] in_17,
  output out_18,
  output out_19,
  output out_20
);

  wire clock_1_out, clock_2_out, clock_3_out, clock_5_out, clock_6_out, clock_9_out, clock_10_out,
       clock_11_out, digital_oscilloscope_1_p5, multiplexer_1_out, multiplexer_3_out, rgb_video_12_p1,
       rgb_video_12_p2, rgb_video_12_p6, rgb_video_12_p8, rgb_video_12_p10, rgb_video_13_p4, rgb_video_13_p6,
       rgb_video_14_p7, rgb_video_15_p6, rgb_video_16_p6;
  wire [3:0] and_2_out;
  wire [3:3] clock_7_out, clock_8_out;
  wire [7:0] adder_1_out, register_1_q;
  wire [15:0] d_16, register_2_q;
  wire [31:0] ram_8_dout;

  DotMatrix dotmatrix_1 ();  // open: col0, col1, col2, col3, col4
  // Shift_Register shift_register_1: pin names not known
  RAM #(.addrWidth(23), .dataWidth(32)) ram_1 ();  // open: addr, we, oe, clk, din, dout
  DipSwitch #(.number(3)) abc ();  // open: sw1, sw2, sw3
  RAM #(.addrWidth(23), .dataWidth(32)) ram_2 ();  // open: addr, we, oe, clk, din, dout
  // RGB_Video rgb_video_1: pin names not known
  // RGB_Video #(.height(16), .scale(4), .width(16)) rgb_video_2: pin names not known
  // RGB_Video #(.height(16), .scale(4), .width(16)) rgb_video_3: pin names not known
  Clock #(.lowDuration(255)) clock_1 (.out(clock_1_out));
  RAM #(.addrWidth(22), .dataWidth(32)) ram_3 ();  // open: addr, we, oe, clk, din, dout
  // RGB_Video #(.height(16), .scale(4), .width(16)) rgb_video_4: pin names not known
  // RGB_Video #(.height(16), .scale(4), .width(16)) rgb_video_5: pin names not known
  Clock #(.highDuration(255)) clock_2 (.out(clock_2_out));
  Clock #(.lowDuration(256)) clock_3 (.out(clock_3_out));
  RAM #(.addrWidth(24), .dataWidth(32)) ram_4 ();  // open: addr, we, oe, clk, din, dout
  RAM #(.addrWidth(22), .dataWidth(32)) ram_5 ();  // open: addr, we, oe, clk, din, dout
  // Digital_Oscilloscope digital_oscilloscope_1: pin names not known; wires that end beside it: out_18, clock_1_out, clock_2_out, clock_3_out, digital_oscilloscope_1_p5
  Clock #(.highDuration(256)) clock_4 (.out(digital_oscilloscope_1_p5));
  Demultiplexer demultiplexer_1 (.out0(out_19), .out1(out_20), .in(in_5), .sel(in_6));
  // RGB_Video #(.height(32), .scale(4), .width(32)) rgb_video_6: pin names not known
  Clock #(.highDuration(2048)) clock_5 (.out(clock_5_out));
  Multiplexer multiplexer_1 (.in0(clock_5_out), .in1(clock_6_out), .out(multiplexer_1_out), .sel(in_10));
  Clock clock_6 (.out(clock_6_out));
  RAM #(.addrWidth(23), .dataWidth(64)) ram_6 ();  // open: addr, we, oe, clk, din, dout
  // RGB_Video rgb_video_7: pin names not known
  // RGB_Video rgb_video_8: pin names not known
  // RGB_Video #(.scale(1)) rgb_video_9: pin names not known
  and and_1 (out_18, and_2_out[0], and_2_out[1], and_2_out[2], and_2_out[3]);
  Register register_1 (.D(adder_1_out), .en(in_4), .clk(multiplexer_1_out), .Q(register_1_q), .clr(in_8));
  Adder adder_1 (.a(register_1_q), .b(in_9), .out(adder_1_out));  // open: cin, cout
  // RGB_Video rgb_video_10: pin names not known
  // RGB_Video rgb_video_11: pin names not known
  // Probe on and_2_out
  assign and_2_out = adder_1_out[3:0] & adder_1_out[7:4];  // AND_Gate and_2, 4 bits wide
  RAM #(.addrWidth(24), .dataWidth(32)) ram_7 ();  // open: addr, we, oe, clk, din, dout
  // Probe on adder_1_out
  // Probe on adder_1_out
  // Switch #(.width(8)) switch_1: pin names not known; wires that end beside it: {8{1'b1}}, adder_1_out, in_3, {8{1'b1}}
  Multiplexer #(.width(8)) multiplexer_2 (.in0(adder_1_out), .in1(register_1_q), .sel(in_7));  // open: out
  Clock clock_7 (.out(clock_7_out[3]));
  Clock clock_8 (.out(clock_8_out[3]));
  Clock clock_9 (.out(clock_9_out));
  // RGB_Video #(.height(256), .scale(1), .width(256)) rgb_video_12: pin names not known; wires that end beside it: rgb_video_12_p1, rgb_video_12_p2, rgb_video_12_p1, clock_9_out, rgb_video_12_p2, rgb_video_12_p6, rgb_video_12_p6, rgb_video_12_p8, rgb_video_12_p8, rgb_video_12_p10, rgb_video_12_p10
  // RGB_Video #(.height(256), .scale(1), .width(256)) rgb_video_13: pin names not known; wires that end beside it: in_1, clock_8_out[3], in_2, rgb_video_13_p4, d_16[15:8], rgb_video_13_p6
  // RGB_Video #(.height(256), .scale(1), .width(256)) rgb_video_14: pin names not known; wires that end beside it: in_1, clock_8_out[3], in_2, d_16[7:0], d_16[7:0], d_16[15:8], rgb_video_14_p7
  RAM #(.addrWidth(20), .dataWidth(32)) ram_8 (.dout(ram_8_dout));  // open: addr, we, oe, clk, din
  RAM #(.addrWidth(23), .dataWidth(32)) ram_9 ();  // open: addr, we, oe, clk, din, dout
  RAM #(.addrWidth(21), .dataWidth(32)) ram_10 ();  // open: addr, we, oe, clk, din, dout
  // RGB_Video #(.height(256), .scale(1), .width(256)) rgb_video_15: pin names not known; wires that end beside it: in_1, clock_8_out[3], in_2, rgb_video_13_p4, d_16[15:8], rgb_video_15_p6
  // RGB_Video #(.height(256), .scale(1), .width(256)) rgb_video_16: pin names not known; wires that end beside it: in_1, clock_8_out[3], in_2, d_16[7:0], d_16[15:8], rgb_video_16_p6
  RAM #(.addrWidth(22), .dataWidth(32)) ram_11 ();  // open: addr, we, oe, clk, din, dout
  Multiplexer multiplexer_3 (.in0(clock_10_out), .in1(clock_11_out), .out(multiplexer_3_out), .sel(in_14));
  Clock #(.highDuration(2048)) clock_10 (.out(clock_10_out));
  Clock clock_11 (.out(clock_11_out));
  Register #(.width(16)) register_2 (.D(d_16), .en(in_11), .clk(multiplexer_3_out), .Q(register_2_q), .clr(in_12));
  Adder #(.width(16)) adder_2 (.a(register_2_q), .b(in_13), .out(d_16));  // open: cin, cout

  // Other names for the same wires on the sheet: x_256_41[7:0] = d_16[7:0]; x_y_256[15:0] = d_16;
  //   y_256_41[7:0] = d_16[15:8]

  // Notes on the sheet:
  //   in_3: initial=0xff
  //   32
  //   128
  //   2^3-2+1/4*1+2^4-6-1
  //   6.25
  //   32mb
  //   23.4mb
  //   24mb
  //   10
endmodule

module gpu_text (
);

  GH100 gh100_1 ();  // open: in_1, in_2
endmodule

module GH100 (
  input  in_1,
  input  in_2
);
endmodule

module NVIDIA_tesla_H100_SXM5_80G (
);

  wire undriven, undriven_2;
  wire [7:0] undriven_3, undriven_4;

  GH100 gh100_1 (.in_1(undriven), .in_2(undriven_2));
  mi mi_1 ();  // open: in_1, in_2, w_1, in_4, in_5, chong_zhi_1, in_7, in_8, in_9, in_10, in_11, ci, in_13, in_14, in_15, out_16, out_17, out_18
  for_i_in_range_n for_i_in_range_n_1 (
    .n_0(undriven_3), .n_1(undriven_3), .s_1_0(undriven_4));  // open: in_1, in_2, in_3, in_5, in_6, in_7, in_8, in_9, in_11, in_12, in_13, cu, in_15, in_16, in_17, in_18, in_19, in_20, in_21, in_23, in_24, in_25, in_26, in_27, in_28, out_29, out_30, out_31, out_32, out_33, out_34, out_35, out_36, out_37
endmodule

module mi (
  input  [7:0] in_1,
  input  [2:0] in_2,
  input  w_1,
  input  [7:0] in_4,
  input  [7:0] in_5,
  input  chong_zhi_1,
  input  [7:0] in_7,
  input  [63:0] in_8,
  input  in_9,
  input  in_10,
  input  in_11,
  input  [63:0] ci,
  input  in_13,
  input  [63:0] in_14,
  input  in_15,
  output out_16,
  output [7:0] out_17,
  output [63:0] out_18
);

  wire c, clock_1_out, clock_2_out, undriven;
  wire [7:0] plarom_1_p1;
  wire [15:0] undriven_3;
  wire [31:0] and_1_out, or_1_out;
  wire [63:0] for_n_q, m_1, m_o_0, multiplier_1_out, multiplier_2_out, multiplier_3_out, multiplier_4_out,
       multiplier_5_out, multiplier_6_out, n_q, undriven_2;

  D_Flip_Flop d_ff_1 ();  // open: D, clk, Q, Qn, preset, reset
  Counter counter_1 ();  // open: clr, load, up, count, clk, D, carry, Q
  Register #(.width(64)) s_s_1 (.D(in_8));  // open: en, clk, Q, clr
  PLA pla_1 ();  // open: in, out
  assign or_1_out = in_8[31:0] | in_8[63:32];  // OR_Gate or_1, 32 bits wide
  assign and_1_out = in_8[31:0] & in_8[63:32];  // AND_Gate and_1, 32 bits wide
  // Probe on in_14
  BitSelector bitselector_1 (.in(in_1), .out(out_16), .sel(in_2));
  Clock clock_1 (.out(clock_1_out));
  Clock clock_2 (.out(clock_2_out));
  Register #(.width(64)) for_n (.D(in_8), .en(in_9), .clk(clock_1_out), .Q(for_n_q), .clr(in_10));
  Clock clock_3 (.out(c));
  // Digital_Oscilloscope digital_oscilloscope_1: pin names not known; wires that end beside it: clock_2_out, clock_1_out, c
  Register #(.width(64)) sum (.D(multiplier_2_out), .en(w_1), .clk(clock_2_out), .Q(m_1), .clr(chong_zhi_1));
  Register #(.width(64)) n (.D(ci), .en(undriven), .clk(c), .Q(n_q), .clr(in_13));
  Divider divider_1 ();  // open: a, b, out, upper, rem
  Multiplier #(.width(64)) multiplier_1 (.a(64'h1), .b(in_14), .out(multiplier_1_out));  // open: cin, cout
  Multiplier #(.width(64)) multiplier_2 (.a(m_o_0), .b(for_n_q), .out(multiplier_2_out));  // open: cin, cout
  Multiplexer #(.width(64)) multiplexer_1 ();  // open: in0, in1, out, sel
  Multiplier #(.width(64)) multiplier_3 (.a(multiplier_1_out), .b(in_14), .out(multiplier_3_out));  // open: cin, cout
  Multiplier #(.width(64)) multiplier_4 (.a(multiplier_3_out), .b(in_14), .out(multiplier_4_out));  // open: cin, cout
  Multiplier #(.width(64)) multiplier_5 (.a(multiplier_4_out), .b(in_14), .out(multiplier_5_out));  // open: cin, cout
  Multiplexer #(.width(64)) multiplexer_2 (.in0(in_8), .in1(m_1), .out(m_o_0), .sel(in_11));
  Multiplier #(.width(64)) multiplier_6 (.a(multiplier_5_out), .b(in_14), .out(multiplier_6_out));  // open: cin, cout
  // AND_Gate and_2 has open pins: in0=undriven_3, out=open
  // AND_Gate and_3 has open pins: in0=undriven_2[15:0], in1=undriven_2[31:16], in2=undriven_2[47:32], in3=undriven_2[63:48], out=open
  // Probe on out_18
  Multiplier #(.width(64)) multiplier_7 (.a(multiplier_6_out), .b(in_14), .out(out_18));  // open: cin, cout
  // PlaRom #(.Contents("2*4 1*4 2*4 1*4 0 1 0 1 1 0 1 0 0 1 0 1 1 0 1 0")) plarom_1: pin names not known; wires that end beside it: plarom_1_p1
  Multiplier multiplier_8 (.a(in_4), .b(in_5), .out(out_17), .cin(plarom_1_p1), .cout(in_7));
  RAM #(.addrWidth(24)) ram_1 ();  // open: addr, we, oe, clk, din, dout

  // Other names for the same wires on the sheet: m_0[63:0] = in_8
endmodule

module for_i_in_range_n (
  input  [63:0] in_1,
  input  [7:0] in_2,
  input  [63:0] in_3,
  input  [7:0] n_0,
  input  [63:0] in_5,
  input  in_6,
  input  in_7,
  input  in_8,
  input  [7:0] in_9,
  input  [7:0] n_1,
  input  [7:0] in_11,
  input  in_12,
  input  in_13,
  input  [7:0] cu,
  input  [7:0] in_15,
  input  in_16,
  input  [7:0] in_17,
  input  in_18,
  input  in_19,
  input  in_20,
  input  in_21,
  input  [7:0] s_1_0,
  input  in_23,
  input  [63:0] in_24,
  input  in_25,
  input  [7:0] in_26,
  input  [7:0] in_27,
  input  [7:0] in_28,
  output [31:0] out_29,
  output [63:0] out_30,
  output [63:0] out_31,
  output [63:0] out_32,
  output [63:0] out_33,
  output out_34,
  output [63:0] out_35,
  output out_36,
  output out_37
);

  wire and_2_out, clock_2_out, clock_3_out, clock_4_out, clock_5_out, clock_6_out, comparator_1_gt,
       inttofp_1_p2, multiplexer_2_out, multiplexer_3_out, o_n, undriven_3, undriven_4, undriven_6;
  wire [2:0] x_n;
  wire [3:0] undriven, undriven_2;
  wire [7:0] adder_2_out, adder_3_out, and_4_out, chenghou_xing_hao, i_n, inttofp_2_p3, multiplexer_1_out,
       multiplexer_4_out, multiplexer_5_out, n_q, reptarlb_1_p2, s_1_q, sum_q, undriven_5, undriven_7,
       undriven_8, undriven_9, x;

  Clock clock_1 ();  // open: out
  Clock clock_2 (.out(clock_2_out));
  and and_1 (out_34, in_9[0], in_9[1], in_9[2], in_9[3], in_9[4], in_9[5], in_9[6], in_9[7]);
  BitSelector bitselector_1 (.in(in_11), .out(out_36), .sel(x_n));
  Random random_1 ();  // open: clr, next, clk, out
  Random #(.width(3)) random_2 (.clr(in_18), .next(in_21), .clk(clock_2_out), .out(x_n));
  // Odd_Parity odd_parity_1 is placed but not wired
  // Even_Parity even_parity_1 is placed but not wired
  and and_2 (and_2_out, undriven[0], undriven[1], undriven[2], undriven[3], undriven_2[0], undriven_2[1], undriven_2[2], undriven_2[3]);
  Register i ();  // open: D, en, clk, Q, clr
  Multiplexer #(.width(8)) multiplexer_1 (
    .in0(cu), .in1(multiplexer_5_out), .out(multiplexer_1_out), .sel(comparator_1_gt));
  Register sum (.D(multiplexer_1_out), .en(multiplexer_2_out), .clk(clock_3_out), .Q(sum_q), .clr(in_19));
  Multiplexer multiplexer_2 (.in0(1'b1), .in1(1'b0), .out(multiplexer_2_out), .sel(o_n));
  Clock clock_3 (.out(clock_3_out));
  // Probe on in_2
  Clock clock_4 (.out(clock_4_out));
  Clock clock_5 (.out(clock_5_out));
  Comparator comparator_1 (.a(sum_q), .b(in_15), .gt(comparator_1_gt));  // open: eq, lt
  Register s_1 (.D(s_1_0), .en(in_23), .clk(clock_4_out), .Q(s_1_q));  // open: clr
  // Probe on out_29
  // IntToFP inttofp_1: pin names not known; wires that end beside it: in_2, inttofp_1_p2, out_29, in_8, out_29, inttofp_1_p2
  Register n (.D(n_0), .en(in_6), .clk(clock_5_out), .Q(n_q));  // open: clr
  Multiplexer multiplexer_3 (.in0(undriven_4), .in1(undriven_3), .out(multiplexer_3_out));  // open: sel
  assign i_n = multiplexer_4_out & x;  // AND_Gate and_3, 8 bits wide
  Multiplier multiplier_1 (.a(sum_q), .b(s_1_q), .out(chenghou_xing_hao));  // open: cin, cout
  Multiplexer #(.width(8)) multiplexer_4 (.in0(n_q), .in1(n_1), .out(multiplexer_4_out), .sel(in_13));
  assign and_4_out = undriven_5 & chenghou_xing_hao;  // AND_Gate and_4, 8 bits wide
  // Probe on in_1
  Multiplexer #(.width(8)) multiplexer_5 (.in0(chenghou_xing_hao), .in1({8{1'b0}}), .out(multiplexer_5_out), .sel(o_n));
  // IntToFP #(.fpwidth(64), .width(64)) inttofp_2: pin names not known; wires that end beside it: in_1, out_30, inttofp_2_p3
  // AND_Gate and_5 has open pins: in0=x, in1=multiplexer_4_out, out=open
  Multiplexer multiplexer_6 (.in0(1'b0), .in1(undriven_6), .out(out_37), .sel(in_20));
  // AND_Gate and_6 is placed but not wired
  Clock clock_6 (.out(clock_6_out));
  Adder adder_1 (.a(undriven_8), .b(in_17), .out(inttofp_2_p3));  // open: cin, cout
  and and_7 (o_n, i_n[3], i_n[2], i_n[1], i_n[0], i_n[7], i_n[6], i_n[5], i_n[4]);
  Adder adder_2 (.b(in_27), .out(adder_2_out));  // open: a, cin, cout
  Adder adder_3 (.a(undriven_7), .b(in_28), .out(adder_3_out));  // open: cin, cout
  // Probe on out_30
  Register i_2B_hex_1 (.D(x), .en(in_7), .clk(clock_6_out), .Q(x), .clr(in_25));
  // ReptarLB reptarlb_1: pin names not known; wires that end beside it: x, reptarlb_1_p2
  Adder adder_4 (.a(undriven_9), .b(in_26), .out(reptarlb_1_p2));  // open: cin, cout
  TTY tty_1 ();  // open: data, clk, we, clr

  assign out_31 = in_3;
  assign out_32 = in_3;
  assign out_33 = in_5;
  assign out_35 = in_5;

  // Other names for the same wires on the sheet: c_0 = in_25; x_2[7:0] = x

  // Notes on the sheet:
  //   数据位：8/8
  //   _
  //   _
  //   a
  //   a
  //   动前
endmodule
