// Logisim project intel_test.circ as structural Verilog
module main (
);

  wire undriven;
  wire [63:0] i9_14980hx_1_p1, i9_14980hx_1_p2, i9_14980hx_1_p3, i9_14980hx_1_p4, i9_14980hx_1_p5,
       i9_14980hx_1_p6, i9_14980hx_1_p7, i9_14980hx_1_p8, i9_14980hx_1_p9, i9_14980hx_1_p10,
       i9_14980hx_1_p11, i9_14980hx_1_p12, i9_14980hx_1_p13, i9_14980hx_1_p14, i9_14980hx_1_p15,
       i9_14980hx_1_p16, i9_14980hx_1_p17, i9_14980hx_1_p18, i9_14980hx_1_p19, i9_14980hx_1_p20,
       i9_14980hx_1_p21, i9_14980hx_1_p22, i9_14980hx_1_p23, i9_14980hx_1_p24, i9_14980hx_1_p25;

  // i9_14980HX i9_14980hx_1: pin names not known; wires that end beside it: i9_14980hx_1_p1, i9_14980hx_1_p2, i9_14980hx_1_p3, i9_14980hx_1_p4, i9_14980hx_1_p5, i9_14980hx_1_p6, i9_14980hx_1_p7, i9_14980hx_1_p8, i9_14980hx_1_p9, i9_14980hx_1_p10, i9_14980hx_1_p11, i9_14980hx_1_p12, i9_14980hx_1_p13, i9_14980hx_1_p14, i9_14980hx_1_p15, i9_14980hx_1_p16, i9_14980hx_1_p17, i9_14980hx_1_p18, i9_14980hx_1_p19, i9_14980hx_1_p20, i9_14980hx_1_p21, i9_14980hx_1_p22, i9_14980hx_1_p23, i9_14980hx_1_p24, i9_14980hx_1_p25
  i9_14980hx_core i9_14980hx_core_1 (.in_12(undriven));  // open: in_10, in_6, in_7, in_4, in_5, in_9, in_8, in_11, in_13, in_3, in_1, in_2, out_15, out_16, out_17, out_14
  a a_1 ();  // open: X, Y, Z
  processor processor_1 ();  // open: clk_i, reset_i, miso_i, cs, sclk_o, mosi_o, TX, LED, BLUE, GREEN, RED, HS, VS
  s s_1 ();  // open: clk_i, reset_i, rd_i, wr_i, continue_i, addr_i, data_i, hndShk_i, miso_i, data_o, busy_o, hndShk_o, error_o, LED, cs_bo, sclk_o, mosi_o
  v v_1 ();  // open: CLK_50MHz, VS, HS, RED, GREEN, BLUE
  p_e_core p_e_core_1 ();
  sdc sdc_1 ();  // open: clk_i, reset_i, rd_i, wr_i, continue_i, addr_i, data_i, hndShk_i, miso_i, data_o, busy_o, hndShk_o, error_o, LED, cs_bo, sclk_o, mosi_o
endmodule

module CPU (
  input  [63:0] A,
  input  [63:0] B
);

  Demultiplexer demultiplexer_1 ();  // open: out0, out1, in, sel
endmodule

module ALU (
  input  [63:0] A,
  input  [63:0] B,
  input  [4:0] ALUSEL,
  output [63:0] out_4
);

  wire comparator_1_lt, comparator_2_lt;
  wire [4:0] priority_encoder_1_out;
  wire [31:0] decoder_1_out0;
  wire [63:0] adder_1_out, and_1_out, bit_extender_1_out, bit_extender_2_out, multiplier_1_out, not_1_out,
       or_1_out, shifter_1_out, shifter_2_out, shifter_3_out, subtractor_1_out, xor_1_out;

  Demultiplexer demultiplexer_1 ();  // open: out0, out1, in, sel
  Adder #(.width(64)) adder_1 (.a(A), .b(B), .out(adder_1_out));  // open: cin, cout
  Subtractor #(.width(64)) subtractor_1 (.a(A), .b(B), .out(subtractor_1_out));  // open: bin, bout
  Comparator #(.width(64)) comparator_1 (.a(A), .b(B), .lt(comparator_1_lt));  // open: gt, eq
  Comparator #(.mode("unsigned"), .width(64)) comparator_2 (.a(A), .b(B), .lt(comparator_2_lt));  // open: gt, eq
  assign or_1_out = A | B;  // OR_Gate or_1, 64 bits wide
  assign and_1_out = A & B;  // AND_Gate and_1, 64 bits wide
  assign xor_1_out = A ^ B;  // XOR_Gate xor_1, 64 bits wide
  assign not_1_out = ~A;  // NOT_Gate not_1, 64 bits wide
  Shifter #(.shift("ar"), .width(64)) shifter_1 (.in(A), .\dist (B[5:0]), .out(shifter_1_out));
  Shifter #(.width(64)) shifter_2 (.in(A), .\dist (B[5:0]), .out(shifter_2_out));
  Shifter #(.shift("lr"), .width(64)) shifter_3 (.in(A), .\dist (B[5:0]), .out(shifter_3_out));
  Multiplier #(.width(64)) multiplier_1 (.a(A), .b(B), .out(multiplier_1_out));  // open: cin, cout
  Decoder #(.select(5)) decoder_1 (
    .out0(decoder_1_out0[0]), .out1(decoder_1_out0[1]), .out2(decoder_1_out0[2]), .out3(decoder_1_out0[3]),
    .out4(decoder_1_out0[4]), .out5(decoder_1_out0[5]), .out6(decoder_1_out0[6]), .out7(decoder_1_out0[7]),
    .out8(decoder_1_out0[8]), .out9(decoder_1_out0[9]), .out10(decoder_1_out0[10]),
    .out11(decoder_1_out0[11]), .out12(decoder_1_out0[12]), .out13(decoder_1_out0[13]),
    .out14(decoder_1_out0[14]), .out15(decoder_1_out0[15]), .out16(decoder_1_out0[16]),
    .out17(decoder_1_out0[17]), .out18(decoder_1_out0[18]), .out19(decoder_1_out0[19]),
    .out20(decoder_1_out0[20]), .out21(decoder_1_out0[21]), .out22(decoder_1_out0[22]),
    .out23(decoder_1_out0[23]), .out24(decoder_1_out0[24]), .out25(decoder_1_out0[25]),
    .out26(decoder_1_out0[26]), .out27(decoder_1_out0[27]), .out28(decoder_1_out0[28]),
    .out29(decoder_1_out0[29]), .out30(decoder_1_out0[30]), .out31(decoder_1_out0[31]), .sel(A[4:0]),
    .en(1'b1));
  Priority_Encoder #(.select(5)) priority_encoder_1 (
    .in0(A[0]), .in1(A[1]), .in2(A[2]), .in3(A[3]), .in4(A[4]), .in5(A[5]), .in6(A[6]), .in7(A[7]),
    .in8(A[8]), .in9(A[9]), .in10(A[10]), .in11(A[11]), .in12(A[12]), .in13(A[13]), .in14(A[14]),
    .in15(A[15]), .in16(A[16]), .in17(A[17]), .in18(A[18]), .in19(A[19]), .in20(A[20]), .in21(A[21]),
    .in22(A[22]), .in23(A[23]), .in24(A[24]), .in25(A[25]), .in26(A[26]), .in27(A[27]), .in28(A[28]),
    .in29(A[29]), .in30(A[30]), .in31(A[31]), .out(priority_encoder_1_out));  // open: gs, en_out, en_in
  assign bit_extender_1_out = {{63{1'b0}}, comparator_1_lt};  // Bit_Extender bit_extender_1
  assign bit_extender_2_out = {{63{1'b0}}, comparator_2_lt};  // Bit_Extender bit_extender_2
  Multiplexer #(.enable("true"), .select(5), .width(64)) multiplexer_1 (
    .in0(adder_1_out), .in1(subtractor_1_out), .in2(bit_extender_1_out), .in3(bit_extender_2_out),
    .in4(or_1_out), .in5(and_1_out), .in6(xor_1_out), .in7(not_1_out), .in8(shifter_1_out),
    .in9(shifter_2_out), .in10(shifter_3_out), .in11(multiplier_1_out), .in12({{32{1'b0}}, decoder_1_out0}),
    .in13({{59{1'b0}}, priority_encoder_1_out}), .out(out_4), .sel(ALUSEL), .en(1'b1));  // open: in14, in15, in16, in17, in18, in19, in20, in21, in22, in23, in24, in25, in26, in27, in28, in29, in30, in31
  // Probe on ALUSEL

  // Notes on the sheet:
  //   14
endmodule

module i9_14980HX (
  input  [63:0] in_1,
  input  [63:0] in_2,
  input  [63:0] in_3,
  input  [63:0] in_4,
  input  [63:0] in_5,
  input  [63:0] in_6,
  input  [63:0] in_7,
  input  [63:0] in_8,
  input  [63:0] in_9,
  input  [63:0] in_10,
  input  [63:0] in_11,
  input  [63:0] in_12,
  input  [63:0] in_13,
  input  [63:0] in_14,
  input  [63:0] in_15,
  input  [63:0] in_16,
  input  [63:0] in_17,
  input  [63:0] in_18,
  input  [63:0] in_19,
  input  [63:0] in_20,
  input  [63:0] in_21,
  input  [63:0] in_22,
  input  [63:0] in_23,
  input  [63:0] in_24,
  input  [63:0] in_25,
  input  [63:0] in_26,
  input  [63:0] in_27,
  input  [63:0] in_28,
  input  [63:0] in_29,
  input  [63:0] in_30,
  input  [63:0] in_31,
  input  [63:0] in_32,
  input  [63:0] in_33,
  input  [63:0] in_34,
  input  [63:0] in_35,
  input  [63:0] in_36,
  input  [63:0] in_37,
  input  [63:0] in_38,
  input  [63:0] in_39,
  input  [63:0] in_40,
  input  [63:0] in_41,
  input  [63:0] in_42,
  input  [63:0] in_43,
  input  [63:0] in_44,
  input  [63:0] in_45,
  input  [63:0] in_46,
  input  [63:0] in_47,
  input  [63:0] in_48,
  input  [63:0] in_49,
  input  [63:0] in_50,
  input  [63:0] in_51,
  input  [63:0] in_52,
  input  [63:0] in_53,
  input  [63:0] in_54,
  input  [63:0] in_55,
  input  [63:0] in_56,
  input  [63:0] in_57,
  input  [63:0] in_58,
  input  [63:0] in_59,
  input  [63:0] in_60,
  input  [63:0] in_61,
  input  [63:0] in_62,
  input  [63:0] in_63,
  input  [63:0] in_64
);
endmodule

module ALU_4_0 (
  input  [2:0] in_1,
  input  [63:0] in_2,
  input  [3:0] in_3,
  input  [2:0] in_4,
  input  [1:0] in_5,
  input  in_6,
  input  in_7,
  input  in_8,
  input  in_9,
  input  in_10,
  output [1:0] out_11,
  output [3:0] out_12,
  output [1:0] out_13,
  output [1:0] out_14,
  output [63:0] out_15,
  output out_16,
  output out_17,
  output out_18,
  output out_19
);

  wire comparator_1_lt, comparator_2_lt;
  wire [1:1] undriven, undriven_2;
  wire [63:0] multiplier_1_out, multiplier_2_out, multiplier_3_out;

  Multiplier #(.width(64)) multiplier_1 (.a(in_2), .b(in_2), .out(multiplier_1_out));  // open: cin, cout
  // Probe on in_2
  Multiplier #(.width(64)) multiplier_2 (.a(multiplier_1_out), .b(in_2), .out(multiplier_2_out));  // open: cin, cout
  // Probe on out_15
  Multiplier #(.width(64)) multiplier_3 (.a(multiplier_2_out), .b(in_2), .out(multiplier_3_out));  // open: cin, cout
  Multiplier #(.width(64)) multiplier_4 (.a(multiplier_3_out), .b(in_2), .out(out_15));  // open: cin, cout
  Adder #(.width(64)) adder_1 ();  // open: a, b, out, cin, cout
  Subtractor #(.width(64)) subtractor_1 ();  // open: a, b, out, bin, bout
  Multiplier #(.width(64)) multiplier_5 ();  // open: a, b, out, cin, cout
  Divider #(.width(64)) divider_1 ();  // open: a, b, out, upper, rem
  Negator #(.width(64)) negator_1 ();  // open: in, out
  Comparator #(.width(64)) comparator_1 (.lt(comparator_1_lt));  // open: a, b, gt, eq
  Comparator #(.mode("unsigned"), .width(64)) comparator_2 (.lt(comparator_2_lt));  // open: a, b, gt, eq
  Shifter #(.shift("ar"), .width(64)) shifter_1 ();  // open: in, dist, out
  Shifter #(.width(64)) shifter_2 ();  // open: in, dist, out
  Shifter #(.shift("lr"), .width(64)) shifter_3 ();  // open: in, dist, out
  BitAdder #(.width(64)) bitadder_1 ();  // open: in0, out
  BitFinder bitfinder_1 ();  // open: in, index, found
  FPAdder fpadder_1 ();  // open: a, b, out
  FPSubtractor fpsubtractor_1 ();  // open: a, b, out
  FPMultiplier fpmultiplier_1 ();  // open: a, b, out
  FPDivider fpdivider_1 ();  // open: a, b, out
  // FPNegator fpnegator_1: pin names not known
  // FPComparator fpcomparator_1: pin names not known
  // FPToInt fptoint_1: pin names not known
  // IntToFP inttofp_1: pin names not known
  // AND_Gate and_1 is placed but not wired
  // OR_Gate or_1 is placed but not wired
  // XOR_Gate xor_1 is placed but not wired
  // NOT_Gate not_1 is placed but not wired
  Bit_Extender #(.in_width(1), .out_width(64), .\type ("zero")) bit_extender_1 (.in(comparator_1_lt));  // open: out
  PLA #(.\table ("00 00\n11 11")) pla_1 ();  // open: in, out
  Bit_Extender #(.in_width(1), .out_width(64), .\type ("zero")) bit_extender_2 (.in(comparator_2_lt));  // open: out
  // PlaRom #(.Contents("2*4 1*4 2*3 0 2 1*3 0 2*4 0 1 2 1 0 0 1 2 0 1 2 1 2 2 1 0 1 2 0*3 1 0 1 0 2 0 0 2 2 1 1 0 1 1 0 2 1 0 0 1 1 0 0 1 0 1 1 2 0 2 0*3 2 1 0 1 0 0 1 0 1 0 1 2 0 2 2 0 2 2 0 0 1 2 2 1 2 1 2 1 2*4 1*3 2 0 2 0 1 0 2 0 1 0 2*3 0 1 0 1 1 1 0 1 0 1 0 0 1 0 1 0 1 1 0 1 0 0 1 0 1 0 1 0 0 1 1 0 1 0 0 1 0 0 1 0*3 1 0*4 1 0 1 0 1 0 0 1 1 0 0 1 0 0 1 0 0 1 0 1 0*4 1 0 0 1 0 0 1 0 1 0 0 1 0*5 1 1 0 1 0 0 1 0 0 1 0 0 1 0 1 0*4 1 0 0 1 1 0 0 1 0 1 0 0 1 0 0 1 0 0 1 0 0 1 0 1 0 0"), .\and (32)) plarom_1: pin names not known; wires that end beside it: in_3, in_3, out_12
  // PlaRom #(.Contents("1 2 2 1 2 2 1 0 1 0 0 1"), .\and (3), .outputs(2)) plarom_2: pin names not known; wires that end beside it: in_5, out_14
  // PlaRom #(.Contents("1 2 0 2 1 0 2 2 0 0 1 2 0 2 1 0 2 2 1 0 1 0 0 1 1 0 1 0 0 1"), .\and (6), .outputs(2)) plarom_3: pin names not known
  Multiplexer #(.select(5)) multiplexer_1 ();  // open: in0, in1, in2, in3, in4, in5, in6, in7, in8, in9, in10, in11, in12, in13, in14, in15, in16, in17, in18, in19, in20, in21, in22, in23, in24, in25, in26, in27, in28, in29, in30, in31, out, sel
  // PlaRom #(.Contents("1 2 0 2 1 0*13 0*12"), .\and (6), .outputs(2)) plarom_4: pin names not known; wires that end beside it: in_1, out_11
  // PlaRom #(.Contents("0 1 2 0 2 1 0 2 2 1 2 0 2 1 0 2 2 0 1 0 1 0 1 0 1 0 1 0 1 0"), .\and (6), .outputs(2)) plarom_5: pin names not known
  // PlaRom #(.Contents("1 2 2 1 2 2 1 0 1 0 0 1"), .\and (3), .outputs(2)) plarom_6: pin names not known; wires that end beside it: {in_8, in_7}
  // PlaRom #(.Contents("1 2 2 1 2 2 1 0 1 0 0 1"), .\and (3), .outputs(2)) plarom_7: pin names not known; wires that end beside it: in_9
  // PlaRom #(.Contents("1 2 0 2 1 0 2*3 0 1 2 0 2 1 2*3 1 0 1 0 0 1 1 0 1 0 0 1"), .\and (6), .outputs(2)) plarom_8: pin names not known; wires that end beside it: in_4, out_13
  // PlaRom #(.Contents("1 2 2 1 2 2 1 0 1 0 0 1"), .\and (3), .outputs(2)) plarom_9: pin names not known
  // PlaRom #(.Contents("1 2 2 1 2 2 1 0 1 0 0 1"), .\and (3), .outputs(2)) plarom_10: pin names not known
  or or_2 (out_17, undriven_2[1], undriven[1]);
endmodule

module ALU_4_1 (
  input  [63:0] in_1,
  input  [63:0] in_2,
  input  [4:0] ALUSEL,
  output [63:0] out_4
);

  wire comparator_1_lt, comparator_2_lt;
  wire [63:0] a_7, adder_1_out, and_1_out, b_8, bit_extender_1_out, divider_1_out, fpnegator_1_p1,
       fpnegator_1_p2, fpnegator_1_p3, fpnegator_1_p4, fpnegator_1_p5, fpnegator_1_p6, multiplier_1_out,
       negator_1_out, not_1_out, or_1_out, shifter_1_out, shifter_2_out, shifter_3_out, subtractor_1_out,
       undriven, undriven_2, undriven_3, undriven_4, undriven_5, undriven_6, xor_1_out;

  Adder #(.width(64)) adder_1 (.a(in_1), .b(in_2), .out(adder_1_out));  // open: cin, cout
  Subtractor #(.width(64)) subtractor_1 (.a(in_1), .b(in_2), .out(subtractor_1_out));  // open: bin, bout
  Multiplier #(.width(64)) multiplier_1 (.a(in_1), .b(in_2), .out(multiplier_1_out));  // open: cin, cout
  Divider #(.width(64)) divider_1 (.a(in_1), .b(in_2), .out(divider_1_out));  // open: upper, rem
  Negator #(.width(64)) negator_1 (.in(in_1), .out(negator_1_out));
  Comparator #(.width(64)) comparator_1 (.a(in_1), .b(in_2), .lt(comparator_1_lt));  // open: gt, eq
  Comparator #(.mode("unsigned"), .width(64)) comparator_2 (.a(in_1), .b(in_2), .lt(comparator_2_lt));  // open: gt, eq
  Shifter #(.shift("ar"), .width(64)) shifter_1 (.in(in_1), .out(shifter_1_out));  // open: dist
  Shifter #(.width(64)) shifter_2 (.in(in_1), .out(shifter_2_out));  // open: dist
  Shifter #(.shift("lr"), .width(64)) shifter_3 (.in(in_1), .out(shifter_3_out));  // open: dist
  BitAdder #(.width(64)) bitadder_1 (.in0(in_1));  // open: out
  BitFinder bitfinder_1 ();  // open: in, index, found
  FPAdder fpadder_1 ();  // open: a, b, out
  FPSubtractor fpsubtractor_1 ();  // open: a, b, out
  FPMultiplier fpmultiplier_1 ();  // open: a, b, out
  FPDivider fpdivider_1 ();  // open: a, b, out
  // FPNegator fpnegator_1: pin names not known; wires that end beside it: fpnegator_1_p1, fpnegator_1_p2, fpnegator_1_p3, fpnegator_1_p4, fpnegator_1_p5, fpnegator_1_p6
  // FPComparator fpcomparator_1: pin names not known
  // FPToInt fptoint_1: pin names not known
  // IntToFP inttofp_1: pin names not known
  assign and_1_out = in_1 & in_2;  // AND_Gate and_1, 64 bits wide
  assign or_1_out = in_1 | in_2;  // OR_Gate or_1, 64 bits wide
  assign xor_1_out = in_1 ^ in_2;  // XOR_Gate xor_1, 64 bits wide
  assign not_1_out = ~in_1;  // NOT_Gate not_1, 64 bits wide
  assign bit_extender_1_out = {{63{1'b0}}, comparator_1_lt};  // Bit_Extender bit_extender_1
  assign a_7 = {{63{1'b0}}, comparator_2_lt};  // Bit_Extender bit_extender_2
  Multiplexer #(.enable("true"), .select(5), .width(64)) multiplexer_1 (
    .in0(adder_1_out), .in1(subtractor_1_out), .in2(multiplier_1_out), .in3(divider_1_out),
    .in4(negator_1_out), .in5(bit_extender_1_out), .in6(a_7), .in7(b_8), .in8(shifter_1_out),
    .in9(shifter_2_out), .in10(shifter_3_out), .in11(undriven), .in12(fpnegator_1_p1), .in13(fpnegator_1_p2),
    .in14(fpnegator_1_p3), .in15(fpnegator_1_p4), .in16(fpnegator_1_p5), .in17(fpnegator_1_p6),
    .in18(undriven_2), .in19(undriven_3), .in20(undriven_4), .in21(and_1_out), .in22(or_1_out),
    .in23(xor_1_out), .in24(not_1_out), .in25(undriven_5), .in31(undriven_6), .out(out_4), .sel(ALUSEL),
    .en(1'b1));  // open: in26, in27, in28, in29, in30

  // Notes on the sheet:
  //   31_32
  //   25_26
endmodule

module ALU_4_2 (
  input  [63:0] in_1,
  input  [63:0] in_2,
  input  [4:0] ALUSEL,
  output [63:0] out_4
);

  wire comparator_1_lt, comparator_2_lt;
  wire [63:0] a_7, adder_1_out, and_1_out, b_8, bit_extender_1_out, divider_1_out, fpnegator_1_p1,
       fpnegator_1_p2, fpnegator_1_p3, fpnegator_1_p4, fpnegator_1_p5, fpnegator_1_p6, multiplier_1_out,
       negator_1_out, not_1_out, or_1_out, shifter_2_out, shifter_3_out, subtractor_1_out, undriven,
       undriven_2, undriven_3, undriven_4, undriven_5, undriven_6, undriven_7, undriven_8, xor_1_out;

  Adder #(.width(64)) adder_1 (.a(in_1), .b(in_2), .out(adder_1_out));  // open: cin, cout
  Subtractor #(.width(64)) subtractor_1 (.a(in_1), .b(in_2), .out(subtractor_1_out));  // open: bin, bout
  Multiplier #(.width(64)) multiplier_1 (.a(in_1), .b(in_2), .out(multiplier_1_out));  // open: cin, cout
  Divider #(.width(64)) divider_1 (.a(in_1), .b(in_2), .out(divider_1_out));  // open: upper, rem
  Negator #(.width(64)) negator_1 (.in(in_1), .out(negator_1_out));
  Comparator #(.width(64)) comparator_1 (.a(in_1), .b(in_2), .lt(comparator_1_lt));  // open: gt, eq
  Comparator #(.mode("unsigned"), .width(64)) comparator_2 (.a(in_1), .b(in_2), .lt(comparator_2_lt));  // open: gt, eq
  Shifter #(.shift("ar"), .width(64)) shifter_1 (.in(in_1), .out(b_8));  // open: dist
  Shifter #(.width(64)) shifter_2 (.in(in_1), .out(shifter_2_out));  // open: dist
  Shifter #(.shift("lr"), .width(64)) shifter_3 (.in(in_1), .out(shifter_3_out));  // open: dist
  BitAdder #(.width(64)) bitadder_1 (.in0(in_1));  // open: out
  BitFinder bitfinder_1 ();  // open: in, index, found
  FPAdder fpadder_1 ();  // open: a, b, out
  FPSubtractor fpsubtractor_1 ();  // open: a, b, out
  FPMultiplier fpmultiplier_1 ();  // open: a, b, out
  FPDivider fpdivider_1 ();  // open: a, b, out
  // FPNegator fpnegator_1: pin names not known; wires that end beside it: fpnegator_1_p1, fpnegator_1_p2, fpnegator_1_p3, fpnegator_1_p4, fpnegator_1_p5, fpnegator_1_p6
  // FPComparator fpcomparator_1: pin names not known
  // FPToInt fptoint_1: pin names not known
  // IntToFP inttofp_1: pin names not known
  assign and_1_out = in_1 & in_2;  // AND_Gate and_1, 64 bits wide
  assign or_1_out = in_1 | in_2;  // OR_Gate or_1, 64 bits wide
  assign xor_1_out = in_1 ^ in_2;  // XOR_Gate xor_1, 64 bits wide
  assign not_1_out = ~in_1;  // NOT_Gate not_1, 64 bits wide
  assign bit_extender_1_out = {{63{1'b0}}, comparator_1_lt};  // Bit_Extender bit_extender_1
  assign a_7 = {{63{1'b0}}, comparator_2_lt};  // Bit_Extender bit_extender_2
  Multiplexer #(.enable("true"), .select(5), .width(64)) multiplexer_1 (
    .in0(adder_1_out), .in1(subtractor_1_out), .in2(multiplier_1_out), .in3(divider_1_out),
    .in4(negator_1_out), .in5(bit_extender_1_out), .in6(a_7), .in7(b_8), .in9(undriven), .in10(undriven_2),
    .in11(undriven_3), .in12(undriven_4), .in13(fpnegator_1_p1), .in14(fpnegator_1_p2),
    .in15(fpnegator_1_p3), .in16(fpnegator_1_p4), .in17(fpnegator_1_p5), .in18(fpnegator_1_p6),
    .in19(undriven_5), .in20(undriven_6), .in21(undriven_7), .in22(and_1_out), .in23(or_1_out),
    .in24(xor_1_out), .in25(not_1_out), .in31(undriven_8), .out(out_4), .sel(ALUSEL), .en(1'b1));  // open: in8, in26, in27, in28, in29, in30
  // Probe on ALUSEL

  // Notes on the sheet:
  //   31_32
  //   25_26
endmodule

module ALU_5_0 (
  input  [63:0] in_1,
  input  [63:0] in_2,
  input  [4:0] ALUSEL,
  output [63:0] out_4
);

  wire comparator_1_lt, comparator_2_lt;
  wire [63:0] a_7, adder_1_out, and_1_out, b_8, bit_extender_1_out, divider_1_out, fpnegator_1_p1,
       fpnegator_1_p2, fpnegator_1_p3, fpnegator_1_p4, fpnegator_1_p5, fpnegator_1_p6, multiplier_1_out,
       negator_1_out, not_1_out, or_1_out, shifter_2_out, shifter_3_out, subtractor_1_out, undriven,
       undriven_2, undriven_3, undriven_4, undriven_5, undriven_6, xor_1_out;

  Adder #(.width(64)) adder_1 (.a(in_1), .b(in_2), .out(adder_1_out));  // open: cin, cout
  Subtractor #(.width(64)) subtractor_1 (.a(in_1), .b(in_2), .out(subtractor_1_out));  // open: bin, bout
  Multiplier #(.width(64)) multiplier_1 (.a(in_1), .b(in_2), .out(multiplier_1_out));  // open: cin, cout
  Divider #(.width(64)) divider_1 (.a(in_1), .b(in_2), .out(divider_1_out));  // open: upper, rem
  Negator #(.width(64)) negator_1 (.in(in_1), .out(negator_1_out));
  Comparator #(.width(64)) comparator_1 (.a(in_1), .b(in_2), .lt(comparator_1_lt));  // open: gt, eq
  Comparator #(.mode("unsigned"), .width(64)) comparator_2 (.a(in_1), .b(in_2), .lt(comparator_2_lt));  // open: gt, eq
  Shifter #(.shift("ar"), .width(64)) shifter_1 (.in(in_1), .out(b_8));  // open: dist
  Shifter #(.width(64)) shifter_2 (.in(in_1), .out(shifter_2_out));  // open: dist
  Shifter #(.shift("lr"), .width(64)) shifter_3 (.in(in_1), .out(shifter_3_out));  // open: dist
  BitAdder #(.width(64)) bitadder_1 (.in0(in_1));  // open: out
  BitFinder bitfinder_1 ();  // open: in, index, found
  FPAdder fpadder_1 ();  // open: a, b, out
  FPSubtractor fpsubtractor_1 ();  // open: a, b, out
  FPMultiplier fpmultiplier_1 ();  // open: a, b, out
  FPDivider fpdivider_1 ();  // open: a, b, out
  // FPNegator fpnegator_1: pin names not known; wires that end beside it: fpnegator_1_p1, fpnegator_1_p2, fpnegator_1_p3, fpnegator_1_p4, fpnegator_1_p5, fpnegator_1_p6
  // FPComparator fpcomparator_1: pin names not known
  // FPToInt fptoint_1: pin names not known
  // IntToFP inttofp_1: pin names not known
  assign and_1_out = in_1 & in_2;  // AND_Gate and_1, 64 bits wide
  assign or_1_out = in_1 | in_2;  // OR_Gate or_1, 64 bits wide
  assign xor_1_out = in_1 ^ in_2;  // XOR_Gate xor_1, 64 bits wide
  assign not_1_out = ~in_1;  // NOT_Gate not_1, 64 bits wide
  assign bit_extender_1_out = {{63{1'b0}}, comparator_1_lt};  // Bit_Extender bit_extender_1
  assign a_7 = {{63{1'b0}}, comparator_2_lt};  // Bit_Extender bit_extender_2
  Multiplexer #(.enable("true"), .select(5), .width(64)) multiplexer_1 (
    .in0(adder_1_out), .in1(subtractor_1_out), .in2(multiplier_1_out), .in3(divider_1_out),
    .in4(negator_1_out), .in5(bit_extender_1_out), .in6(a_7), .in7(b_8), .in9(shifter_2_out),
    .in10(shifter_3_out), .in11(undriven), .in12(fpnegator_1_p1), .in13(fpnegator_1_p2),
    .in14(fpnegator_1_p3), .in15(fpnegator_1_p4), .in16(fpnegator_1_p5), .in17(fpnegator_1_p6),
    .in18(undriven_2), .in19(undriven_3), .in20(undriven_4), .in21(and_1_out), .in22(or_1_out),
    .in23(xor_1_out), .in24(not_1_out), .in25(undriven_5), .in31(undriven_6), .out(out_4), .sel(ALUSEL),
    .en(1'b1));  // open: in8, in26, in27, in28, in29, in30
  // Probe on ALUSEL

  // Notes on the sheet:
  //   31_32
  //   25_26
endmodule

module ALU_5_2 (
  input  [63:0] A,
  input  [63:0] B,
  input  [4:0] ALUSEL,
  input  [3:0] in_4,
  input  [3:0] in_5,
  input  [3:0] in_6,
  input  [1:0] in_7,
  input  [63:0] in_8,
  input  [63:0] in_9,
  input  fu,
  input  in_11,
  input  [63:0] in_12,
  input  [1:0] in_13,
  input  in_14,
  input  [63:0] in_15,
  input  in_16,
  input  [63:0] in_17,
  output [63:0] I,
  output [63:0] out_19
);

  wire bitfinder_1_found, clock_1_out, clock_2_out, comparator_1_lt, comparator_2_lt, fpcomparator_1_p3,
       fpnegator_1_p3, fpnegator_1_p4, fpnegator_1_p5, fpnegator_1_p6, fpnegator_1_p7, fpnegator_1_p9,
       fptoint_1_p1, fptoint_1_p2, inttofp_1_p1, inttofp_1_p2;
  wire [3:3] bitfinder_2_found;
  wire [5:0] bitfinder_1_index, bitfinder_2_index;
  wire [6:0] bitadder_1_out;
  wire [63:0] a_7, adder_1_out, and_1_out, b_8, bit_extender_1_out, divider_1_out, fpadder_1_out,
       fpdivider_1_out, fpmultiplier_1_out, fpnegator_1_p21, fpnegator_1_p22, fpnegator_1_p23,
       fpnegator_1_p24, fpnegator_1_p25, fpsubtractor_1_out, multiplier_1_out, negator_1_out, not_1_out,
       or_1_out, rom_1_data, shifter_2_out, shifter_3_out, subtractor_1_out, undriven, undriven_2,
       undriven_3, undriven_4, undriven_5, undriven_6, xor_1_out;

  // Probe on in_8
  // Probe on in_8
  // Probe on in_9
  // Probe on in_4
  // Probe on in_5
  BitFinder #(.width(64)) bitfinder_1 (.in(A), .index(bitfinder_1_index), .found(bitfinder_1_found));
  // Probe on {{58{1'b0}}, bitfinder_1_index}
  // Probe on in_12
  Adder #(.width(64)) adder_1 (.a(A), .b(B), .out(adder_1_out));  // open: cin, cout
  Subtractor #(.width(64)) subtractor_1 (.a(A), .b(B), .out(subtractor_1_out));  // open: bin, bout
  Multiplier #(.width(64)) multiplier_1 (.a(A), .b(B), .out(multiplier_1_out));  // open: cin, cout
  Divider #(.width(64)) divider_1 (.a(A), .b(B), .out(divider_1_out));  // open: upper, rem
  Negator #(.width(64)) negator_1 (.in(A), .out(negator_1_out));
  Comparator #(.width(64)) comparator_1 (.a(A), .b(B), .lt(comparator_1_lt));  // open: gt, eq
  Comparator #(.mode("unsigned"), .width(64)) comparator_2 (.a(A), .b(B), .lt(comparator_2_lt));  // open: gt, eq
  Shifter #(.shift("ar"), .width(64)) shifter_1 (.in(A), .\dist (B[5:0]), .out(b_8));
  Shifter #(.width(64)) shifter_2 (.in(A), .\dist (B[5:0]), .out(shifter_2_out));
  Shifter #(.shift("lr"), .width(64)) shifter_3 (.in(A), .\dist (B[5:0]), .out(shifter_3_out));
  BitAdder #(.width(64)) bitadder_1 (.in0(A), .out(bitadder_1_out));
  // Probe on bitfinder_2_index
  BitFinder #(.width(64)) bitfinder_2 (.in(A), .index(bitfinder_2_index), .found(bitfinder_2_found[3]));
  FPAdder #(.fpwidth(64)) fpadder_1 (.a(A), .b(B), .out(fpadder_1_out));
  FPSubtractor #(.fpwidth(64)) fpsubtractor_1 (.a(A), .b(B), .out(fpsubtractor_1_out));
  FPMultiplier #(.fpwidth(64)) fpmultiplier_1 (.a(A), .b(B), .out(fpmultiplier_1_out));
  FPDivider #(.fpwidth(64)) fpdivider_1 (.a(A), .b(B), .out(fpdivider_1_out));
  // FPNegator #(.fpwidth(64)) fpnegator_1: pin names not known; wires that end beside it: bitfinder_1_found, A, fpnegator_1_p3, fpnegator_1_p4, fpnegator_1_p5, fpnegator_1_p6, fpnegator_1_p7, in_6, fpnegator_1_p9, {57{1'b1}}, fpnegator_1_p3, fpsubtractor_1_out, fpnegator_1_p4, fpmultiplier_1_out, fpnegator_1_p5, fpdivider_1_out, fpnegator_1_p6, fpnegator_1_p9, fpnegator_1_p7, fpadder_1_out, fpnegator_1_p21, fpnegator_1_p22, fpnegator_1_p23, fpnegator_1_p24, fpnegator_1_p25
  // FPComparator #(.fpwidth(64)) fpcomparator_1: pin names not known; wires that end beside it: A, B, fpcomparator_1_p3, fpcomparator_1_p3
  // FPToInt fptoint_1: pin names not known; wires that end beside it: fptoint_1_p1, fptoint_1_p2, fptoint_1_p2, fptoint_1_p1
  // IntToFP inttofp_1: pin names not known; wires that end beside it: inttofp_1_p1, inttofp_1_p2, inttofp_1_p2, inttofp_1_p1
  assign and_1_out = A & B;  // AND_Gate and_1, 64 bits wide
  assign or_1_out = A | B;  // OR_Gate or_1, 64 bits wide
  assign xor_1_out = A ^ B;  // XOR_Gate xor_1, 64 bits wide
  assign not_1_out = ~A;  // NOT_Gate not_1, 64 bits wide
  Clock clock_1 (.out(clock_1_out));
  // Probe on {fu, {10{1'b0}}, in_11, {52{1'b0}}}
  assign bit_extender_1_out = {{63{1'b0}}, comparator_1_lt};  // Bit_Extender bit_extender_1
  assign a_7 = {{63{1'b0}}, comparator_2_lt};  // Bit_Extender bit_extender_2
  // Digital_Oscilloscope digital_oscilloscope_1: pin names not known; wires that end beside it: clock_1_out, fu
  // Probe on in_17
  // Probe on {bitfinder_2_found[3], {57{1'b0}}, bitfinder_2_index}
  // Probe on bitfinder_2_found[3]
  Multiplexer #(.enable("true"), .select(5), .width(64)) multiplexer_1 (
    .in0(adder_1_out), .in1(subtractor_1_out), .in2(multiplier_1_out), .in3(divider_1_out),
    .in4(negator_1_out), .in5(bit_extender_1_out), .in6(a_7), .in7(b_8), .in8(shifter_2_out),
    .in9(shifter_3_out), .in10({{57{1'b0}}, bitadder_1_out}),
    .in11({bitfinder_2_found[3], {57{1'b0}}, bitfinder_2_index}), .in12(fpnegator_1_p21),
    .in13(fpnegator_1_p22), .in14(fpnegator_1_p23), .in15(fpnegator_1_p24), .in16(fpnegator_1_p25),
    .in17(undriven), .in18(undriven_2), .in19(undriven_3), .in20(and_1_out), .in21(or_1_out),
    .in22(xor_1_out), .in23(not_1_out), .in24(undriven_6), .in25(undriven_4), .in31(undriven_5), .out(I),
    .sel(ALUSEL), .en(1'b1));  // open: in26, in27, in28, in29, in30
  // Probe on ALUSEL
  ROM #(.addrWidth(2), .dataWidth(64)) rom_1 (.addr(in_7), .data(rom_1_data));
  // Probe on in_15
  Clock clock_2 (.out(clock_2_out));
  RAM #(.addrWidth(2), .dataWidth(64)) aaaaa (
    .addr(in_13), .we(in_14), .oe(in_16), .clk(clock_2_out), .din(in_15), .dout(out_19));

  // Notes on the sheet:
  //   31_32
  //   24_25
  //   25_26
  //   contents of rom_1 (hex, n*v repeats v):
  //   13213231
endmodule

module C_P_U (
  input  [63:0] in_1,
  input  [63:0] in_2,
  input  [4:0] in_3,
  output [63:0] out_4
);

  ALU_5_2 alu_5_2_1 (
    .A(in_1), .B(in_2), .ALUSEL(in_3), .I(out_4));  // open: in_9, in_13, in_14, in_16, fu, in_12, in_4, in_5, in_11, in_6, in_17, in_8, in_7, in_15, out_19
endmodule

module i9_14980hx_core (
  input  in_1,
  input  [31:0] in_2,
  input  [31:0] in_3,
  input  in_4,
  input  in_5,
  input  in_6,
  input  in_7,
  input  in_8,
  input  in_9,
  input  in_10,
  input  in_11,
  input  in_12,
  input  [3:0] in_13,
  output [31:0] out_14,
  output out_15,
  output out_16,
  output [3:0] out_17
);

  wire clock_1_out, clock_2_out, n7411_1_pin6, n7411_1_pin8, n7411_1_pin12, nios2_1_p1, socbus_1_p1,
       socjtaguart_1_p6, socjtaguart_1_p8, socjtaguart_1_p10, socjtaguart_1_p11;
  wire [6:0] a, socjtaguart_1_p9;

  Keyboard keyboard_1 ();  // open: clk, re, clr, avail, data
  // RGBLED rgbled_1: pin names not known
  _7_Segment_Display u_7_segment_display_1 ();  // open: g, f, a, b, e, d, c, dp
  DotMatrix dotmatrix_1 ();  // open: col0, col1, col2, col3, col4
  Button button_1 ();  // open: out
  DipSwitch dipswitch_1 ();  // open: sw1, sw2, sw3, sw4, sw5, sw6, sw7, sw8
  Joystick joystick_1 ();  // open: x, y
  LED led_1 ();  // open: in
  LedBar ledbar_1 ();  // open: led0, led1, led2, led3, led4, led5, led6, led7
  Hex_Digit_Display hex_digit_display_1 ();  // open: value, dp
  Clock clock_1 (.out(clock_1_out));
  DipSwitch #(.number(3)) raid ();  // open: sw1, sw2, sw3
  _7411 u_7411_1 (
    .pin6(n7411_1_pin6), .pin12(n7411_1_pin12), .pin8(n7411_1_pin8));  // open: pin1, pin2, pin3, pin4, pin5, pin13, pin11, pin10, pin9
  // Rv32im rv32im_1: pin names not known; wires that end beside it: n7411_1_pin12, n7411_1_pin6
  // SocBus #(.SocBusIdentifier('h0000018B2B40DDAC6f82c57e)) socbus_1: pin names not known; wires that end beside it: socbus_1_p1, socbus_1_p1, socbus_1_p1
  // Rv32im #(.SocBusSelection('h0000018B2B40DDAC6f82c57e)) rv32im_2: pin names not known
  // SocBus #(.SocBusIdentifier('h0000018B2B219DDB6c88b0af)) socbus_2: pin names not known; wires that end beside it: in_6, in_4, clock_1_out
  // SocPio #(.SocBusSelection('h0000018B2B40DDAC6f82c57e), .width(16)) socpio_1: pin names not known; wires that end beside it: in_7
  // SocJtagUart #(.SocBusSelection('h0000018B2B40DDAC6f82c57e)) socjtaguart_1: pin names not known; wires that end beside it: n7411_1_pin8, in_10, clock_1_out, in_9, in_8, socjtaguart_1_p6, a, socjtaguart_1_p8, socjtaguart_1_p9, socjtaguart_1_p10, socjtaguart_1_p11
  _7421 u_7421_1 (.pin8(socjtaguart_1_p8));  // open: pin1, pin2, pin3, pin4, pin5, pin6, pin13, pin12, pin11, pin10, pin9
  Keyboard keyboard_2 (.clk(clock_1_out), .re(in_9), .clr(in_8), .avail(socjtaguart_1_p6), .data(a));
  // Probe on socjtaguart_1_p9
  _7402 u_7402_1 ();  // open: pin1, pin2, pin3, pin4, pin5, pin6, pin13, pin12, pin11, pin10, pin9, pin8
  TTY tty_1 (.data(socjtaguart_1_p9), .clk(clock_1_out), .we(socjtaguart_1_p10), .clr(socjtaguart_1_p11));
  Clock clock_2 (.out(clock_2_out));
  // RGB_Video rgb_video_1: pin names not known
  // Nios2 #(.SocBusSelection('h0000018B2B40DDAC6f82c57e)) nios2_1: pin names not known; wires that end beside it: nios2_1_p1, in_3, in_2, in_1
  // Socmem #(.SocBusSelection('h0000018B2B40DDAC6f82c57e)) socmem_1: pin names not known; wires that end beside it: in_5
  // SocVga #(.DisplayMode("640x480"), .SocBusSelection('h0000018B2B40DDAC6f82c57e)) socvga_1: pin names not known
  // a a_1: pin names not known; wires that end beside it: clock_2_out, in_13, in_12, out_17
  // ReptarLB reptarlb_1: pin names not known
  // PortIO portio_1: pin names not known

  assign out_15 = in_9;

  // Notes on the sheet:
  //   |
  //   |
  //   |
  //   |
  //   |
  //   |
  //   |
  //   |
  //   G
  //   内控
  //   DDR
  //   低功率岛
  //   E-core
  //   soc tile
  //   wifi 6e
  //   NPU
  //   显示
  //   e_core
  //   e_core
  //   e_core
  //   e_core
  //   e_core
  //   e_core
  //   e_core
  //   e_core
  //   p_core
  //   p_core
  //   p_core
  //   cpu tile
  //   p_core
  //   i/o
  //   雷电4
  //   p_core
  //   p_core
  //   pcie gen5
  //   p_core
  //   p_core
endmodule

// VHDL entity a, as the project stores it:
library IEEE;
use IEEE.STD_LOGIC_1164.ALL;
use IEEE.STD_LOGIC_ARITH.ALL;
use IEEE.STD_LOGIC_UNSIGNED.ALL;

entity pla_pow is
    Port ( X : in  STD_LOGIC_VECTOR (3 downto 0);
           Y : in  STD_LOGIC_VECTOR (3 downto 0);
           Z : out STD_LOGIC_VECTOR (7 downto 0));
end pla_pow;

architecture Behavioral of pla_pow is
    signal count : STD_LOGIC_VECTOR (4 downto 0);
    signal temp : STD_LOGIC_VECTOR (7 downto 0);
begin
    process (X, Y)
    begin
        temp(3 downto 0) <= X;
        temp(7 downto 4) <= "0000";
        count <= "0000";
        while (temp(3 downto 0) /= "1111") loop
            if (temp(3 downto 0) = X) then
                count <= count + 1;
                if (count = Y) then
                    Z <= temp;
                    exit;
                end if;
            end if;
            temp <= temp * 2;
        end loop;
    end process;
end Behavioral;

// VHDL entity processor, as the project stores it:
------------------------------< In The Name Of GOD >-------------------------------
-- Company: Dalmif
-- Engineer: Ali Fallah
-- 
-- Create Date:    19:53:17 05/28/2017 
-- Design Name: 		Processor (enshaallah)
-- Module Name:    processor - Behavioral 
-- Project Name: 
-- Target Devices: 
-- Tool versions: 
-- Description: 
--
-- Dependencies: 
--
-- Revision: 
-- Revision 0.01 - File Created
-- Additional Comments: 
--
----------------------------------------------------------------------------------
library IEEE;
use IEEE.STD_LOGIC_1164.ALL;
use IEEE.NUMERIC_STD.ALL;
 
entity processor is
    Port ( clk_i   : in  STD_LOGIC;
			  reset_i : in  STD_LOGIC;
			  cs      : out STD_LOGIC;
			  sclk_o  : out STD_LOGIC;
			  mosi_o  : out STD_LOGIC;
			  miso_i  : in  STD_LOGIC;
			  TX 		 : out STD_LOGIC; -- UART
			  LED 	 : out STD_LOGIC_VECTOR (3 downto 0);
  ---------<VGA Signal>--------------------
			  BLUE    : out std_logic;
			  GREEN   : out std_logic;
			  RED     : out std_logic;
			  HS		 : out std_logic;
  			  VS 	    : out std_logic
	 );
end processor;

architecture Behavioral of processor is

COMPONENT MainMemory
  PORT (
    clka : IN STD_LOGIC;
    wea : IN STD_LOGIC_VECTOR(0 DOWNTO 0);
    addra : IN STD_LOGIC_VECTOR(8 DOWNTO 0);
    dina : IN STD_LOGIC_VECTOR(7 DOWNTO 0);
    douta : OUT STD_LOGIC_VECTOR(7 DOWNTO 0)
  );
END COMPONENT;

component UART_TX port (
    CLK     : in  STD_LOGIC;
	 SendKey   : in  STD_LOGIC;
	 Tx     : out  STD_LOGIC;
	 data : in  STD_LOGIC_VECTOR (7 downto 0));
	end component;

component MYVGA    port ( 
			CLK_50MHz: in std_logic;
			Xchar : std_logic_vector(6 downto 0);
			Ychar : std_logic_vector(4 downto 0);
			char : std_logic_vector(6 downto 0);
         VS: out std_logic;
			HS: out std_logic;
			RED: out std_logic;
			GREEN: out std_logic;
			BLUE: out std_logic
  );
	end component;

	
component SdCardCtrl is
    port (
      clk_i      : in  std_logic;       -- Master clock.
      reset_i    : in  std_logic                     ;  -- active-high, synchronous  reset.
      rd_i       : in  std_logic                     ;  -- active-high read block request.
      wr_i       : in  std_logic                     ;  -- active-high write block request.
      continue_i : in  std_logic                     ;  -- If true, inc address and continue R/W.
      addr_i     : in  std_logic_vector(31 downto 0) ;  -- Block address.
      data_i     : in  std_logic_vector(7 downto 0)  ;  -- Data to write to block.
      data_o     : out std_logic_vector(7 downto 0)  ;  -- Data read from block.
      busy_o     : out std_logic;  -- High when controller is busy performing some operation.
      hndShk_i   : in  std_logic;  -- High when host has data to give or has taken data.
      hndShk_o   : out std_logic;  -- High when controller has taken data or has data to give.
      error_o    : out std_logic_vector(15 downto 0) ;
      -- I/O signals to the external SD card.
      cs_bo      : out std_logic                    ;  -- Active-low chip-select.
      sclk_o     : out std_logic                    ;  -- Serial clock to SD card.
      mosi_o     : out std_logic                     ;  -- Serial data output to SD card.
      miso_i     : in  std_logic                       -- Serial data input from SD card.
      );
  end component;
  
  signal NOTreset_i       : std_logic;	-- Enable read
  signal sd_read_en       : std_logic	:= '1';	-- Enable read
  signal sd_write_en       : std_logic	:= '0';	-- Enable Write
  signal sd_read_continue : std_logic	:= '0';	-- continue read sector
  signal sd_is_busy	  : std_logic;	-- sd card is busy
  signal sd_h_hndShk	  : std_logic; -- host Hande Shake
  signal sd_c_hndShk	  : std_logic;-- clinet Hande Shake
  signal sd_address    : std_logic_vector(31 downto 0):= (others =>'0');	-- address to read / write
  signal sd_data_in    :  std_logic_vector(7 downto 0);-- data to wirte
  signal sd_data_out    :  std_logic_vector(7 downto 0); -- data to read
  signal sd_error    :  std_logic_vector(15 downto 0); -- sd card error message
  signal CounterPulse    :  std_logic_vector(15 downto 0); -- sd card error message
  signal main_mem_wr_en	: std_logic_vector (0 downto 0); -- Enable Write Pin Memory
  signal main_mem_addr	: std_logic_vector (8 downto 0); -- Address of MAin mamory to read / write
  signal main_mem_data_in	: std_logic_vector (7 downto 0); -- data to Write on Main Mamory
  signal main_mem_data_out	: std_logic_vector (7 downto 0); -- data read from Main Mamory
  
  signal tx_char   	: std_logic_vector (7 downto 0); -- char send to tx
  signal uart_tx_b	: std_logic; -- boolean send char
  signal ClockPulse : std_logic_vector (15 downto 0);
  signal CLKPorcessor : std_logic;
	
  signal Xchar : std_logic_vector(6 downto 0);
  signal Ychar : std_logic_vector(4 downto 0);
  signal char  : std_logic_vector(6 downto 0);

	
begin

 mian_mem : MainMemory
  PORT MAP (
    clka => clk_i,
    wea => main_mem_wr_en,
    addra => main_mem_addr,
    dina => main_mem_data_in,
    douta => main_mem_data_out
  );
  
  
 VGA : MYVGA
  PORT MAP (
    CLK_50MHz => clk_i,
	 Xchar => Xchar ,
	 Ychar => Ychar,
	 char  => Char,
    VS => VS,
    HS => HS,
    RED => RED,
    GREEN => GREEN,
    BLUE => BLUE
  );

  
 HDD : SdCardCtrl port map (
		clk_i      => clk_i,
      reset_i    => NOTreset_i,
      rd_i       => sd_read_en,
      wr_i       => sd_write_en,
      continue_i => sd_read_continue,
      addr_i     => sd_address,
      data_i     => sd_data_in,
      data_o     => sd_data_out,
      busy_o     => sd_is_busy,
      hndShk_i   => sd_h_hndShk,
      hndShk_o   => sd_c_hndShk,
      error_o    => sd_error,
      -- I/O signals to the external SD card.
      cs_bo      => cs,
      sclk_o     =>sclk_o,
      mosi_o     =>mosi_o,
      miso_i     =>miso_i
 );
 
UART : UART_TX port map (
    CLK     => clk_i,
	 SendKey   => uart_tx_b,
	 Tx => TX,
    data  => tx_char
);


	instruction : process (CLKPorcessor)
	type State_type is (    -- States of the SD card controller FSM.
      READ_BYTE,  -- Send initialization clock pulses to the deselected SD card.    
		Read_Sector, -- Read first sector
		detect_inst,
		INTRRUPT,
		Next_Byte,
		detect_gpr1,
		detect_addr,
		read_addr_mem,
		const_to_mem,
		detect_operate,
		WRITE_BYTE,
		set_reg_h,
		set_val_reg,
		halt,
		jump,
		detect_gpr4,
		detect_gpr5,
		Cond_Jump,
		Call,
		RET,
		POPF,
		MOVS,
		CMPS,
		COMP,
		REP,
		POP,
		show_char,
		Init			-- redy to start
      );

	variable State     : State_type := Init;  -- Current state of the FSM.
	variable RTNstate  : State_type := Init;  -- Next    state of the FSM.
	variable EXstate   : State_type := Init;  -- Extera  state of the FSM.
			
	type SubState_type is (    -- States of the SD card controller FSM.
			adder,
			adcer,
			suber,
			muler,
			ander,
			xorer,
			orer,
			mover,
			incer,
			decer,
			pusher,
			sbber,
			poper
      );
					
	variable Sub_State     : SubState_type;  -- Current state of the FSM.
	
	type Intrupt_Type is (
	int_LED
	);
	
	subtype NUMBER_MEMORY_BIT is std_logic_vector(8 downto 0);-- 2^9 = 512byte
	 
	variable int : Intrupt_Type;
	variable cnt_bit : natural range 0 to 512;  -- Counter of bits
	variable num_byte : natural range 0 to 4;  -- Number of byte to read
	variable num_byte_v : natural range 0 to 4;  -- Number of byte to read
	variable addr_mem_rw : std_logic_vector (15 downto 0);
	variable ram_rw_en : std_logic ;		-- Enable other address to read write (else IP)
	variable val_const_bit : std_logic ;		-- it show constant value (e.g. mov [bx]+3,'j')

	variable AX  : std_logic_vector (15 downto 0);  -- AX Regester
	variable BX  : std_logic_vector (15 downto 0);  -- BX Regester
	variable CX  : std_logic_vector (15 downto 0);  -- CX Regester
	variable DX  : std_logic_vector (15 downto 0);  -- DX Regester
	
	variable CS  : std_logic_vector (15 downto 0);  -- Code Segment Regester
	variable DS  : std_logic_vector (15 downto 0);  -- Data Segment Regester
	variable ES  : std_logic_vector (15 downto 0);  -- ExtraSegment Regester
	variable SS  : std_logic_vector (15 downto 0);  -- Stack Segment Regester
	variable IP  : std_logic_vector (15 downto 0);  -- Instruction Pointer Regester
	
	variable SP  : std_logic_vector (15 downto 0);  -- Stack Pointer Regester
	variable BP  : std_logic_vector (15 downto 0);  -- Base Pointer Regester
	variable SI  : std_logic_vector (15 downto 0);  -- Source Index Regester
	variable DI  : std_logic_vector (15 downto 0);  -- Destination Index Regester
	
	alias AL: std_logic_vector (7 downto 0) is AX (7 downto 0);
	alias AH: std_logic_vector (7 downto 0) is AX (15 downto 8);
	alias CL: std_logic_vector (7 downto 0) is CX (7 downto 0);
	alias CH: std_logic_vector (7 downto 0) is CX (15 downto 8);
	alias DL: std_logic_vector (7 downto 0) is DX (7 downto 0);
	alias DH: std_logic_vector (7 downto 0) is DX (15 downto 8);	
	alias BL: std_logic_vector (7 downto 0) is BX (7 downto 0);
	alias BH: std_logic_vector (7 downto 0) is BX (15 downto 8);
	
	variable flag	: std_logic_vector (7 downto 0);	-- DF, IF, AF, PF, OF, SF, ZF, CF
	alias carry_flag:    std_logic  is flag(0);	-- carry_flag bit show
	alias zero_flag:     std_logic  is flag(1);	-- zero_flag bit show
	alias sign_flag:     std_logic  is flag(2);	-- sign_flag bit show
	alias overflow_flag: std_logic  is flag(3);	-- overflow_flag bit show
	alias parity_flag:   std_logic  is flag(4);	-- parity_flag bit show
	alias adjust_flag:   std_logic  is flag(5);	-- adjust_flag bit show
	alias intrrupt_flag: std_logic  is flag(6);	-- intrrupt_flag bit show
	alias direction_flag:std_logic  is flag(7);	-- direction_flag bit show


	variable byte0	: std_logic_vector (7 downto 0);	-- Save instruction Code
	variable byte1	: std_logic_vector (7 downto 0);	-- Save instruction Code
	variable byte2	: std_logic_vector (7 downto 0);	-- Save instruction Code
	variable byte3	: std_logic_vector (7 downto 0);	-- Save instruction Code
	
	variable reg_h	: std_logic_vector (16 downto 0);	-- Complementary register - the MSB bit is carry_flag bit
	alias m_reg_0 : std_logic_vector (1 downto 0) is byte0 (7 downto 6);	-- MODE of Addressing (e.g. "11" means reg to reg)
	
	variable m_reg : std_logic_vector (1 downto 0);	-- MODE of Addressing (e.g. "11" means reg to reg)
	
	variable rm_t	: std_logic_vector (2 downto 0);	-- register / memory address
	variable reg_t	: std_logic_vector (2 downto 0);	-- register address
	
	variable repnz_en	: std_logic;	-- repnz enable
	variable repz_en	: std_logic;	-- repz enable
	variable compare	: std_logic;	-- compare : dont operate on byte and reg
	variable S_reg	: std_logic;	-- THE Parameter is Word (16bit)
	variable W_reg	: std_logic;	-- THE Regester is Word (16bit)
	variable D_reg	: std_logic;	-- Direction (1: R/M to reg	0: reg to R/M)
	
	variable bool	: std_logic;	-- boolean 
	variable cheng_reg_h_byte	: std_logic;	-- it Makes it : byte val -> reg_h val (in detect_operate case)
	
   variable LED_v	   : std_logic_vector (3 downto 0);	-- Save Addressing (parametr)
	
	constant iAX,iAL  : std_logic_vector(2 downto 0) := "000";
	constant iCX,iCL  : std_logic_vector(2 downto 0) := "001";
	constant iDX,iDL  : std_logic_vector(2 downto 0) := "010";
	constant iBX,iBL  : std_logic_vector(2 downto 0) := "011";
	constant iSP,iAH  : std_logic_vector(2 downto 0) := "100";
	constant iBP,iCH  : std_logic_vector(2 downto 0) := "101";
	constant iSI,iDH  : std_logic_vector(2 downto 0) := "110";
	constant iDI,iBH  : std_logic_vector(2 downto 0) := "111";
	constant zeros_16 : std_logic_vector(AX'range) 	 := (others => '0');	
	constant zeros_8 	: std_logic_vector(AH'range) 	 := (others => '0');	
	variable reg1_t : std_logic_vector(2 downto 0);
	
	begin
		if rising_edge(CLKPorcessor) then
		 if (NOTreset_i =  '1') then
		  state := Init;
		 else
		  case state is
			when READ_BYTE =>		-- Read One Byte From Main Memory ----------------------<Read Byte>--------------------
			 if (num_byte_v/= num_byte) then
				 case num_byte_v is
				  when 0 =>
					byte0 := main_mem_data_out;
				  when 1 =>
					byte1 := main_mem_data_out;
				  when 2 =>
					byte2 := main_mem_data_out;
				  when 3 =>
					byte3 := main_mem_data_out;
				  when others => null;
				  end case;
				  num_byte_v	:= num_byte_v+1;
				  if (ram_rw_en = '1') then addr_mem_rw	:= std_logic_vector (unsigned(addr_mem_rw) +1); else  
				  IP	:= std_logic_vector (unsigned(IP) +1);
				  end if;
			  else 
			   num_byte_v	:=0;
				state	:= rtnstate;
				ram_rw_en		:= '0';
				tx_char	<= byte0;
				uart_tx_b <= not uart_tx_b;
			end if;
			
			when WRITE_BYTE =>		-- Write One Byte From Main Memory ---------------------<Write Byte>--------------------
				main_mem_wr_en (0) <= '1';
				ram_rw_en	:= '1';
				if (num_byte_v/= num_byte) then
				 case num_byte_v is
				  when 0 =>
					main_mem_data_in <= byte0;
				  when 1 =>
					main_mem_data_in <= byte1;
				  when 2 =>
					main_mem_data_in <= byte2;
				  when 3 =>
					main_mem_data_in <= byte3;
				  when others => null;
				  end case;
				  num_byte_v	:= num_byte_v+1;
				  addr_mem_rw	:= std_logic_vector (unsigned(addr_mem_rw) +1);
			  else 
			   num_byte_v	:=0;
				state	:= rtnstate;
				main_mem_wr_en (0) <= '0';
				ram_rw_en		:= '0';
			end if;

			when detect_inst =>	 -------------------------------<Detection Instruction>-----------------------------
			  case byte0 is
			  ------------------< MOV AL,BL,CL,DL, number>------------------------
				 when "1011----" =>			-- Mov Al,Num
					 w_reg 	 := byte0 (3);
				    if (w_reg = '1') then num_byte := 2; else num_byte := 1; end if; -- parameter is byte or word
					 reg1_t	 := byte0 (2 downto 0);  -- dest reg is AL
					 state 	 := READ_BYTE;
					 d_reg    := '1';
					 sub_state:= mover;
					 rtnstate := set_reg_h;

			-----------------<Intrrupt>---------------------
				 when x"CD" =>		-- intrrupt
					 num_byte := 1;
				    state 	:= READ_BYTE;
				    rtnstate	:= intrrupt;
			-----------------<ADD>---------------------
				 when "0000010-" =>	--0x04 0x05   -- Add Al,AX <- num
					 w_reg 	 := byte0 (0);
				    if (w_reg = '1') then num_byte := 2; else num_byte := 1; end if; -- parameter is byte or word
					 reg1_t	:= iAx;  -- dest reg is AL or AX (depend w_reg)
					 state 	:= READ_BYTE;
					 d_reg := '1';
					 sub_state := adder;
					 rtnstate := set_reg_h;
					 
				 when "000000--"=>	--0x00 0x03   -- Add ABCD L/H/X <- ABCD L/H/X		 
					 W_reg	:= byte0 (0); 
					 D_reg	:= byte0 (1); 
					 num_byte := 1;	-- read Argument Addressing
					 state 	:= READ_BYTE;
					 sub_state := adder;
					 rtnstate := detect_addr; 
					 exstate    := set_reg_h;
			-----------------<ADC>---------------------
				 when "0001010-" =>	--0x14 0x15   -- Adc Al,AX <- num
					 w_reg 	 := byte0 (0);
				    if (w_reg = '1') then num_byte := 2; else num_byte := 1; end if; -- parameter is byte or word
					 reg1_t	:= iAx;  -- dest reg is AL or AX (depend w_reg)
					 state 	:= READ_BYTE;
					 d_reg := '1';
					 sub_state := adcer;
					 rtnstate := set_reg_h;
					 
				 when "000100--"=>	--0x10 0x13   -- Adc ABCD L/H/X <- ABCD L/H/X		 
					 W_reg	:= byte0 (0); 
					 D_reg	:= byte0 (1); 
					 num_byte := 1;	-- read Argument Addressing
					 state 	:= READ_BYTE;
					 sub_state := adcer;
					 rtnstate := detect_addr; 	
					 exstate    := set_reg_h;
					 
			-----------------<SUB>---------------------
				 when "0010110-" =>		 --0x2C 0x2D  -- SUB Al,AX <- num
				 	 w_reg 	 := byte0 (0);
				    if (w_reg = '1') then num_byte := 2; else num_byte := 1; end if; -- parameter is byte or word
					 reg1_t	:= iAx;  -- dest reg is AL or AX (depend w_reg)
					 state 	:= READ_BYTE;
					 d_reg := '1';
					 sub_state := suber;
					 rtnstate := set_reg_h;
								 
				 when "001010--" =>	--0x28 0x2b   -- sub BCD L/H/X <- BCD L/H/X		 
					 W_reg	:= byte0 (0); 
					 D_reg	:= byte0 (1); 
					 num_byte := 1;	-- read Argument Addressing
					 state 	:= READ_BYTE;
					 sub_state := suber;
					 rtnstate := detect_addr; 
					 exstate    := set_reg_h;
					 
			-----------------<SBB>---------------------
				 when "0001110-" =>		 --0x1C 0x1D  -- SUB Al,AX <- num
				 	 w_reg 	 := byte0 (0);
				    if (w_reg = '1') then num_byte := 2; else num_byte := 1; end if; -- parameter is byte or word
					 reg1_t	:= iAx;  -- dest reg is AL or AX (depend w_reg)
					 state 	:= READ_BYTE;
					 d_reg := '1';
					 sub_state := sbber;
					 rtnstate := set_reg_h;
								 
				 when "000110--" =>	--0x18 0x1b   -- sub BCD L/H/X <- BCD L/H/X		 
					 W_reg	:= byte0 (0); 
					 D_reg	:= byte0 (1); 
					 num_byte := 1;	-- read Argument Addressing
					 state 	:= READ_BYTE;
					 sub_state := sbber;
					 rtnstate := detect_addr; 
					 exstate    := set_reg_h;					 
			-----------------<CMP>---------------------
				 when "0011110-" =>		 --0x3C 0x3D  -- CMP Al,AX <- num
				 	 w_reg 	 := byte0 (0);
				    if (w_reg = '1') then num_byte := 2; else num_byte := 1; end if; -- parameter is byte or word
					 reg1_t	:= iAx;  -- dest reg is AL or AX (depend w_reg)
					 state 	:= READ_BYTE;
					 d_reg := '1';
					 sub_state:= suber;
					 rtnstate := set_reg_h;
					 compare  := '1';
								 
				 when "001110--" =>	--0x38 0x3b   -- CMP BCD L/H/X <- BCD L/H/X		 
					 W_reg	:= byte0 (0); 
					 D_reg	:= byte0 (1); 
					 num_byte := 1;	-- read Argument Addressing
					 state 	:= READ_BYTE;
					 sub_state := suber;
					 rtnstate := detect_addr; 
					 exstate    := set_reg_h;	
					 compare  := '1';
			-----------------<AND>---------------------
				when "0010010-" =>	--0x24 0x25   -- And Al,AX <- num
					 w_reg 	 := byte0 (0);
				    if (w_reg = '1') then num_byte := 2; else num_byte := 1; end if; -- parameter is byte or word
					 reg1_t	:= iAx;  -- dest reg is AL or AX (depend w_reg)
					 d_reg := '1';
					 sub_state := ander;
					 rtnstate := set_reg_h;
					 
				 when "001000--" =>	--0x20 0x23   -- And BCD L/H/X <- BCD L/H/X		 
					 W_reg	:= byte0 (0); 
					 D_reg	:= byte0 (1); 
					 num_byte := 1;	-- read Argument Addressing
					 state 	:= READ_BYTE;
					 rtnstate := detect_addr; 
					 exstate    := set_reg_h;
					 sub_state := ander;
					 
			-----------------<Test>---------------------
				when "1010100-" =>	--0xA8 0xA9   -- TEST Al,AX <- num
					 w_reg 	 := byte0 (0);
				    if (w_reg = '1') then num_byte := 2; else num_byte := 1; end if; -- parameter is byte or word
					 reg1_t	:= iAx;  -- dest reg is AL or AX (depend w_reg)
					 d_reg := '1';
					 sub_state := ander;
					 rtnstate := set_reg_h;
					 compare  := '1';
					 
				 when "1000010-" =>	--0x84 0x85   -- Test BCD L/H/X <- BCD L/H/X		 
					 W_reg	:= byte0 (0); 
					 D_reg	:= byte0 (1); 
					 num_byte := 1;	-- read Argument Addressing
					 state 	:= READ_BYTE;
					 rtnstate := detect_addr; 
					 exstate    := set_reg_h;
					 sub_state := ander;			
					 compare  := '1';
					 
			-----------------<XOR>---------------------
				when "0011010-" =>	--0x34 0x35   -- And Al,AX <- num
					 w_reg 	 := byte0 (0);
				    if (w_reg = '1') then num_byte := 2; else num_byte := 1; end if; -- parameter is byte or word
					 reg1_t	:= iAx;  -- dest reg is AL or AX (depend w_reg)
					 d_reg := '1';
					 sub_state := xorer;
					 rtnstate := set_reg_h;
					 
				 when "001100--" =>	--0x30 0x33   -- And BCD L/H/X <- BCD L/H/X		 
					 W_reg	:= byte0 (0); 
					 D_reg	:= byte0 (1); 
					 num_byte := 1;	-- read Argument Addressing
					 state 	:= READ_BYTE;
					 rtnstate := detect_addr; 
					 exstate    := set_reg_h;
					 sub_state := xorer;
					 
			-----------------<CALL>---------------------
				when x"E8" =>	 -- CALL (2byte parameter - show offset of routin from current IP) - should push next IP	 
					 num_byte := 2;	-- read Argument Addressing
					 w_reg := '1';
					 state 	:= READ_BYTE;
					 rtnstate := CALL;
					 
		 -----------------<INC>---------------------
				when "01000---" =>	--0x40 0x47   -- inc AX,BX,CX,DX,SP,BP,SI,DI
					 w_reg 	 := '1'; -- it is for ax,bx,cx,dx,sp,bp,si,di
					 reg1_t	:= byte0(2 downto 0);  -- dest reg is AL or AX (depend w_reg)
					 sub_state := incer;
					 state 	  := set_reg_h;
					 
			-----------------<DEC>---------------------
				when "01001---" =>	--0x48 0x4f   -- dec AX,BX,CX,DX,SP,BP,SI,DI
					 w_reg 	 := '1'; -- it is for ax,bx,cx,dx,sp,bp,si,di
					 reg1_t	:= byte0(2 downto 0);  -- dest reg is AL or AX (depend w_reg)
					 sub_state := decer;
					 state 	  := set_reg_h;				 
					 
		 -----------------<PUSH>---------------------
				when "01010---" =>	--0x50 0x57   -- PUSH AX,BX,CX,DX,SP,BP,SI,DI
					 w_reg 	  := '1'; -- it is for ax,bx,cx,dx,sp,bp,si,di
					 d_reg     := '0';
					 reg1_t	  := byte0(2 downto 0);  -- dest reg
					 sub_state := pusher;
					 state 	  := set_reg_h;
					 				
		-----------------<POP>---------------------
				when "01011---" =>	--058 0x5f   -- POP AX,BX,CX,DX,SP,BP,SI,DI
					 w_reg 	   := '1'; -- it is for ax,bx,cx,dx,sp,bp,si,di
					 d_reg      := '1';
					 num_byte   := 2;
					 reg1_t	   := byte0(2 downto 0);  -- dest reg
 					 sub_state  := poper;
					 ram_rw_en	:= '1';
					 state	   := read_byte;
					 addr_mem_rw:= SP;
					 rtnstate	:= detect_operate;
					 
				when x"8F" => -- POP Ev 
				  d_reg 		:= '0'; 
				  w_reg 		:= '1';
				  num_byte  := 1;
				  ram_rw_en	:= '1';
				  addr_mem_rw:= SP;
				  state	   := read_byte;
				  rtnstate 	:= POP; 
				  
	----------------------<CONDITIONAL JUMP>------------------------
				when "0111----" =>	-- x70 x7f
					w_reg := '0';
					state := cond_jump;

					 
			---------------<GRP1>---------------------
				when "100000--" =>		  -- 0x80 to 0x83 -- ADD,OR,ADC,SBB,AND,SUB,XOR,CMP * BL,CL,DL <- 1B
					 W_reg	:= byte0 (0); 
					 s_reg	:= byte0 (1);
					 num_byte := 1;	-- read Argument Addressing
					 state 	:= READ_BYTE;
					 rtnstate := detect_gpr1;	
					 
			---------------<NOP>---------------------	
				when x"90" => -- NOP
					state := next_byte;
					
			---------------<CBW>---------------------	
				when x"98" => -- CBW
					if (AL(7) = '1') then
						AH := x"ff";
					else
					   AH := x"00";
					end if;
					
			---------------<CWD>---------------------	
				when x"99" => -- CWD
					if (AH(7) = '1') then
						DX := x"ffff";
					else
					   DX := x"0000";
					end if;	
					
					
			---------------<PUSHF>---------------------	
				when x"9C" => -- PUSH Flag reg
					 w_reg 	  := '1'; -- because only word can push
					 d_reg     := '0';
					 byte1	  := x"00";	-- void and no work
					 byte0	  := flag;
					 sub_state := pusher;
					 state 	  := detect_operate;
					 
			---------------<POPF>---------------------	
				when x"9D" => -- POP Flag reg
					 num_byte   := 2;
					 ram_rw_en	:= '1';
					 state	   := read_byte;
					 addr_mem_rw:= SP;
					 rtnstate	:= POPF;
					 
			----------------------<MOV AX>----------------------
				when "1010000-" => -- 0xA0 0xA1 (e.g. MOV al,[41h])
					 w_reg := byte0(0); -- word or byte
					 d_reg := '1'; -- mem to reg
					 num_byte:= 2; -- the paramete is address memory (2byte)
					 state := read_byte;
					 rm_t := "110"; -- immediate (const) address memory --use in read_addr_mem block
					 m_reg := "00";
					 rtnstate := read_addr_mem;
					 sub_state := mover;
					 exstate := detect_operate;
					 
				when "1010001-" => -- 0xA2 0xA3 (e.g. mov [43h],ax)
					 w_reg := byte0(0); -- word or byte
					 d_reg := '0'; -- reg to mem
					 num_byte:= 2; -- the paramete is address memory (2byte)
					 state := read_byte;
					 rm_t := "110"; -- immediate (const) address memory --use in read_addr_mem block
					 m_reg := "00";
					 rtnstate := read_addr_mem;
					 sub_state := mover;
					 reg1_t := iAX;
					 exstate := set_reg_h;
			-----------------------<MOVS>-----------------------
				when "1010010-" =>	--0xA4 0xA5 -- MOVS BW
					if (repz_en = '1') then
						if (cx /= zeros_16) then IP:=std_logic_vector(unsigned(IP) - 2); cx:=std_logic_vector (unsigned (cx) - 1); bool:='1'; else bool:='0'; end if;
						repz_en := '0';
					else bool := '1'; end if;
					if (bool = '1') then
						w_reg := byte0(0);
						if (w_reg = '1') then num_byte := 2; else num_byte := 1; end if;
						ram_rw_en	:= '1';
						addr_mem_rw := std_logic_vector (resize (unsigned (DS&SI),16)); -- source
						if (flag(7) = '0')then SI := std_logic_vector (unsigned (SI) + num_byte); else SI:= std_logic_vector (unsigned (SI) - num_byte);end if;
						state	      := read_byte;
						rtnstate    := MOVS;
					else state:=next_byte;
					end if;

			-----------------------<CMPS>-----------------------
				when "1010011-" =>	--0xA6 0xA7 -- CMPS BW
					if (repz_en = '1') then
						if (cx /= zeros_16) then cx:=std_logic_vector (unsigned (cx) - 1); bool:='1'; else bool:='0'; end if;
					else bool := '1'; end if;
					if (bool = '1') then
						w_reg := byte0(0);
						if (w_reg = '1') then num_byte := 2; else num_byte := 1; end if;
						ram_rw_en	:= '1';
						addr_mem_rw := std_logic_vector (resize (unsigned (DS&SI),16)); -- source
						if (flag(7) = '0')then SI := std_logic_vector (unsigned (SI) + num_byte); else SI:= std_logic_vector (unsigned (SI) - num_byte);end if;
						state	      := read_byte;
						rtnstate    := CMPS;
						exstate		:= REP;
					else state:=next_byte;
					end if;
			-----------------------<STOS>-----------------------
				when "1010101-" =>	--0xAA 0xAB -- STOSB
					if (repz_en = '1') then
						if (cx /= zeros_16) then IP:=std_logic_vector(unsigned(IP) - 2); cx:=std_logic_vector (unsigned (cx) - 1); bool:='1'; else bool:='0'; end if;
						repz_en := '0';
					else bool := '1'; end if;
					if (bool = '1') then
						w_reg := byte0(0);
						byte0 := AL;
						byte1 := AH;
						if (w_reg = '1') then num_byte := 2; else num_byte := 1; end if;
						ram_rw_en	:= '1';
						addr_mem_rw := std_logic_vector (resize (unsigned (ES&DI),16));
						addr_mem_rw	:= std_logic_vector (unsigned (addr_mem_rw) - 1); -- default to Write
						if (flag(7) = '0')then DI := std_logic_vector (unsigned (DI) + num_byte); else DI:= std_logic_vector (unsigned (DI) - num_byte);end if;
						state	      := Write_byte; 
						rtnstate    := next_byte;
					else state:=next_byte;
					end if;
			-----------------------<LODS>-----------------------
				when "1010110-" =>	--0xAC 0xAD-- LODS BW
					if (repz_en = '1') then
						if (cx /= zeros_16) then IP:=std_logic_vector(unsigned(IP) - 2); cx:=std_logic_vector (unsigned (cx) - 1); bool:='1'; else bool:='0'; end if;
						repz_en := '0';
					else bool := '1'; end if;
					if (bool = '1') then
						w_reg 	   := byte0(0); -- byte
						d_reg      := '1'; 
						if (w_reg = '1') then num_byte := 2; else num_byte := 1; end if;
						reg1_t	   := iAL;  -- dest reg AX = AL (depend w_reg)
						sub_state  := mover;
						ram_rw_en	:= '1';
						state	   := read_byte;
						addr_mem_rw:= std_logic_vector (resize (unsigned (DS&SI),16));
						if (flag(7) = '0')then SI := std_logic_vector (unsigned (SI) + num_byte); else SI:= std_logic_vector (unsigned (SI) - num_byte);end if;
						rtnstate	:= detect_operate;
					else state:=next_byte;
					end if;
			-----------------------<SCAN>-----------------------
				when "1010111-" =>	--0xAE 0xAF-- SCAS BW
					if (repz_en = '1') then
						if (cx /= zeros_16) then cx:=std_logic_vector (unsigned (cx) - 1); bool:='1'; else bool:='0'; end if;
					else bool := '1'; end if;
					if (bool = '1') then
						w_reg	:= byte0 (0); 
						if (w_reg = '1') then num_byte := 2; else num_byte := 1; end if;
						reg_h (15 downto 0) := AX;
						ram_rw_en	:= '1';
						 addr_mem_rw := std_logic_vector (resize (unsigned (ES&DI),16));
						if (flag(7) = '0')then DI := std_logic_vector (unsigned (DI) + num_byte); else DI:= std_logic_vector (unsigned (DI) - num_byte);end if;
						state 	:= READ_BYTE;
						rtnstate := COMP;
					else state:=next_byte;
					end if;
			---------------<GRP4  - DEC INC>---------------------
				when x"FE" =>		  -- 0xFE  DEC.INC al,bl,cl,dl
					 W_reg	:= '0'; -- only byte
					 d_reg := '1';
					 num_byte := 1;	-- read Argument Addressing
					 state 	:= READ_BYTE;
					 rtnstate := detect_gpr4;
					 
			-----------------<GRP5 >---------------------
				when x"FF" =>		  -- 0xFF  INC - DEC - CALL -CALL -JMP -JMP(Mp) -PUSH
					 num_byte := 1;	-- read Argument Addressing
					 state 	:= READ_BYTE;
					 rtnstate := detect_gpr5;		
			-------------------<MOV reg to reg>----------------------
				when "100010--" =>		  -- 0x88 to 0x8B  -- MOV reg to reg (e.g. mov bl,cl)
					 W_reg	:= byte0 (0); 
					 D_reg	:= byte0 (1); 
					 num_byte := 1;	-- read Argument Addressing
					 state 	:= READ_BYTE;
					 sub_state := mover;
					 rtnstate  := detect_addr;
					 exstate    := set_reg_h;
					 
			---------------------<RET>----------------------
				when x"C3" =>		 -- RET
					 num_byte 	   := 2;
					 addr_mem_rw:= SP;
					 ram_rw_en	:= '1';
					 state	   := read_byte;
					 rtnstate	:= RET;					 

			-------------------<MOV const to const>----------------------
				when "1100011-" =>		  -- 0xC6 to 0xC7  -- MOV const to const (e.g. mov [21h],67h)
					 W_reg	:= byte0 (0); 
				    num_byte := 1;  -- parameter is byte
					 d_reg := '0';
					 state 	:= READ_BYTE;
					 rtnstate := const_to_mem;	
--					 exstate	 := Assign;

		 -----------------<JMP>---------------------
				when x"EB" =>	 -- jmp	 
					 num_byte := 1;	-- read Argument Addressing
					 w_reg := '0';
					 state 	:= READ_BYTE;
					 rtnstate := jump; 
					 
		 -----------------<LOOP>---------------------
			 when "111000--" =>	 -- E0 E3 -- LOOPNZ - LOOPZ - LOOP
					 cx := std_logic_vector (unsigned (cx)-1);
					 case byte0(1 downto 0) is
						when "00" => if (cx /= zeros_16 and flag(1) = '0') then bool := '1'; else bool := '0'; end if; -- LOOPNZ
						when "01" => if (cx /= zeros_16 and flag(1) = '1') then bool := '1'; else bool := '0'; end if; -- LOOPZ
						when "10" => if (cx /= zeros_16)						   then bool := '1'; else bool := '0'; end if; -- LOOP
						when "11" => if (cx  = zeros_16)					      then bool := '1'; else bool := '0'; end if; -- JCXZ
						when others => null;
					 end case;
					 if (bool = '1') then
						 num_byte := 1;	
						 w_reg := '0';
						 state 	:= READ_BYTE;
						 rtnstate := jump; 
					 else
						 IP	:= std_logic_vector (unsigned (IP)+1); 
						 state:= next_byte;
					 end if;	
					 
				
			-------------------<REP>----------------------
				when x"F2" =>	 -- REP (REPNZ - REPNE)
					 repnz_en := '1';
					 state := next_byte;
				when x"F3" =>	 -- REP (REPZ - REPE)
					 repz_en := '1';
					 state := next_byte;

					 
			-------------------<MOV reg to reg>----------------------
				when x"F4" =>	 -- halted (stop cpu)
					 state := halt;
					 
			-------------------<CLC - Clear Carry>----------------------
				when x"F5" =>	 -- CMC - Clear Carry
					 flag(0) := not flag(0);
					 state := next_byte;
				when x"F8" =>	 -- CLC - Clear Carry
					 flag(0) := '0';
					 state := next_byte;
				when x"F9" =>	-- STC - Set Carry
					 flag(0) := '1';
					 state := next_byte;
				when x"FA" =>	-- CLI - Clear Interrupt
					 flag(6) := '0';
					 state := next_byte;
				when x"FB" =>	-- STI - Set Interrupt
					 flag(6) := '1';
					 state := next_byte;
				when x"FC" =>	-- CLD - Clear Direction
					 flag(7) := '0';
					 state := next_byte;
				when x"FD" =>	-- STD - Set Direction
					 flag(7) := '1';
					 state := next_byte;
					 
				when others =>
					num_byte := 1;
				   state 	:= READ_BYTE;
				   rtnstate := detect_inst;
				end case;
				val_const_bit := '0';

			when INTRRUPT =>     ----------------------------------------<INTRRUPT>-------------------------------
				case byte0 is
					 when x"63" =>		-- int LED
							LED_v := AL(3 downto 0);
							state 	:= Next_Byte;
					  when x"21" => -- int 21h
							case AX(15 downto 8) is
								when x"02" => -- show char
									char <= DX(6 downto 0);
--									LED_v := DX(3 downto 0);
									state := show_char;
									rtnstate:= next_byte;
								when others => state 	:= Next_Byte;
							end case;
							
							
					  when others => state 	:= Next_Byte;
			   end case;
				 				 
			when const_to_mem =>	 ----------------------------------------<const_to_mem>-------------------------------
				m_reg    := m_reg_0;
				rm_t     := byte0 (2 downto 0); 
				reg_t    := byte0 (5 downto 3); 
				reg1_t   := reg_t;
				
			  if (m_reg = "00" and rm_t = "110") then  num_byte := 2; else num_byte := to_integer (unsigned (m_reg));end if; -- direct address memory	
			  if (w_reg = '1') then num_byte := num_byte +2; else num_byte := num_byte +1; end if;
			  state 			 := read_byte;
			  rtnstate 		 := read_addr_mem;  -- calculate new address (adress with offset) and read value
			  exstate 		 := detect_operate;   -- it go to write_byte block finaly 
			  val_const_bit := '1';
				 
			when detect_addr =>	----------------------------------------<detect_addr>-------------------------------
				m_reg := m_reg_0;
				if (m_reg = "11" ) then 
					reg_t := byte0 (2 downto 0); -- in this case reg_t and rm_t is Displaced (in 8086 instruction) = source
					rm_t := byte0 (5 downto 3); -- = destination
					reg1_t := rm_t;				  -- (2 downto 0)  (e.g.: 11 000 001 CL -> AL)
					state    := set_val_reg;	-- read reg_t val 
					rtnstate := set_reg_h;		-- read reg1_t val
				else	
				
				 rm_t     := byte0 (2 downto 0); 
				 reg_t    := byte0 (5 downto 3); 
				 reg1_t   := reg_t;
			    if (m_reg = "00" and rm_t = "110") then  num_byte := 2; else num_byte := to_integer (unsigned (m_reg));end if; -- direct address memory	or no
				 state := read_byte;
				 rtnstate   := read_addr_mem; -- read frome diffrent address (not IP)
--				 exstate    := set_reg_h; -- read frome diffrent address (not IP)
				end if;
				val_const_bit := '0';
				
				
			when read_addr_mem =>	-- read byte from a diffrent address (memory)
				   if (w_reg = '1') then num_byte := 2; else num_byte := 1; end if; -- parameter is byte or word
					case rm_t is	-- (2 downto 0)  (e.g.: 11 000 001 CL -> AL)
						when "000" => addr_mem_rw	 := std_logic_vector (unsigned(BX(8 downto 0))+unsigned(SI(8 downto 0)));
						when "001" => addr_mem_rw	 := std_logic_vector (unsigned(BX(8 downto 0))+unsigned(DI(8 downto 0)));
						when "010" => addr_mem_rw   := std_logic_vector (unsigned(BP(8 downto 0))+unsigned(SI(8 downto 0)));
						when "011" => addr_mem_rw	 := std_logic_vector (unsigned(BP(8 downto 0))+unsigned(DI(8 downto 0)));
						when "100" => addr_mem_rw	 := SI;
						when "101" => addr_mem_rw	 := DI; 
						when "110" => 					if (m_reg = "00") then addr_mem_rw:=(byte1&byte0); else addr_mem_rw := BP;  end if;
						when "111" => addr_mem_rw	 := BX; 
						when others => null;
					end case;
				
					 if (m_reg = "01") then addr_mem_rw := std_logic_vector (unsigned(addr_mem_rw(8 downto 0))+unsigned(byte0));
					 elsif (m_reg = "10") then addr_mem_rw := std_logic_vector (unsigned(addr_mem_rw(8 downto 0))+unsigned(byte1&byte0));
					 end if;
					 
					 ram_rw_en	:= '1';
					 state	:= read_byte;
					 rtnstate:= exstate; 			 

			when set_reg_h =>
				case w_reg&reg1_t (2 downto 0) is	-- (2 downto 0)  (e.g.: 11 000 001 CL -> AL)
					when '1'&iAX => reg_h (7 downto 0)  := AL; reg_h (15 downto 8) := AH;
					when '1'&iBX => reg_h (7 downto 0)  := BL; reg_h (15 downto 8) := BH;
					when '1'&iCX => reg_h (7 downto 0)  := CL; reg_h (15 downto 8) := CH;
					when '1'&iDX => reg_h (7 downto 0)  := DL; reg_h (15 downto 8) := DH;
					when '0'&iAL => reg_h (7 downto 0)  := AL;
					when '0'&iBL => reg_h (7 downto 0)  := BL;
					when '0'&iCL => reg_h (7 downto 0)  := CL;
					when '0'&iDL => reg_h (7 downto 0)  := DL;
					when '0'&iAH => reg_h (7 downto 0)  := AH;
					when '0'&iBH => reg_h (7 downto 0)  := BH;
					when '0'&iCH => reg_h (7 downto 0)  := CH;
					when '0'&iDH => reg_h (7 downto 0)  := DH;
					when others => null;
				end case;	
				   state := detect_operate;
					
					 
			when set_val_reg =>
				case w_reg&reg_t (2 downto 0) is	-- (2 downto 0)  (e.g.: 11 000 001 CL -> AL)
					when '1'&iAX => byte0 := AL; byte1 := AH;
					when '1'&iBX => byte0 := BL; byte1 := BH;
					when '1'&iCX => byte0 := CL; byte1 := CH;
					when '1'&iDX => byte0 := DL; byte1 := DH;
					when '0'&iAL => byte0 := AL;
					when '0'&iBL => byte0 := BL;
					when '0'&iCL => byte0 := CL;
					when '0'&iDL => byte0 := DL;
					when '0'&iAH => byte0 := AH;
					when '0'&iBH => byte0 := BH;
					when '0'&iCH => byte0 := CH;
					when '0'&iDH => byte0 := DH;
					when others => null;
				end case;
				if (m_reg = "11" ) then state := set_reg_h;
				else state := detect_operate;end if;
				
			when Cond_Jump => -- Conditional Jump		
					case byte0 (3 downto 0) is
					 when "0000" => if (flag(3)  = '1') then bool := '1'; else bool := '0'; end if; -- JO  (not appropriate)
					 when "0001" => if (flag(3) /= '1') then bool := '1'; else bool := '0'; end if; -- JNO (not appropriate) 
					 when "0010" => if (flag(0)  = '1' and flag(1) = '0') then bool := '1'; else bool := '0'; end if; -- JB   <  (unsigned)
					 when "0110" => if (flag(0) = '1' or flag(1) = '1') then bool := '1'; else bool := '0'; end if; --LED_V := LED_V or "0010"; -- JBE  <= (unsigned)
					 when "0111" => if (flag(0) = '0'  and flag(1)  = '0') then bool := '1'; else bool := '0'; end if; -- JA  >  (unsigned)
					 when "0011" => if (flag(0)  = '0' or  flag(1) = '1') then bool := '1'; else bool := '0'; end if; -- JAE  >= (unsigned)
					 when "0100" => if (flag(1)  = '1') then bool := '1'; else bool := '0'; end if; -- JZ (not appropriate)
					 when "0101" => if (flag(1)  = '0') then bool := '1'; else bool := '0'; end if; -- JNZ (not appropriate)
					 when "1000" => if (flag(2)  = '1') then bool := '1'; else bool := '0'; end if; -- JS (not appropriate)
					 when "1001" => if (flag(2) = '0')  then bool := '1'; else bool := '0'; end if; -- JNS (not appropriate)
					 when "1010" => if (flag(4) = '1')then bool := '1'; else bool := '0'; end if; -- JPE (not appropriate)
					 when "1011" => if (flag(4) = '0')then bool := '1'; else bool := '0'; end if; -- JPO (JNP) (not appropriate)
					 when "1100" => if ((flag(2) /= flag(3)) and (flag(1)  = '1')) then bool := '1'; else bool := '0'; end if; -- JL  (signed)
					 when "1101" => if ((flag(2)  = flag(3)) or  (flag(1)  = '1')) then bool := '1'; else bool := '0'; end if; -- JGE (signed)
					 when "1110" => if ((flag(2) /= flag(3)) or  (flag(1)  = '1')) then bool := '1'; else bool := '0'; end if; -- JLE (signed)
					 when "1111" => if ((flag(2)  = flag(3)) and (flag(1)  = '0')) then bool := '1'; else bool := '0'; end if; -- JG  (signed)
					 when others => null;
					end case;
				if (bool = '1') then 
				  num_byte := 1;
				  state := read_byte;
				  rtnstate := jump;
				else
					IP	  := std_logic_vector (unsigned (IP)+1);
					state := next_byte;
				end if;		

			
			when Jump => 	-----------------------------------------<Jump>-----------------------------
				if (w_reg = '0') then -- sign
					if (byte0 (7) = '1' ) then byte1 := x"ff"; else byte1 := x"00"; end if;
				end if;
				IP	:= std_logic_vector (unsigned (IP) + unsigned(byte1&byte0));
				state := next_byte;
				
			when Call => 	-------------------------------------<Call>-------------------------------------
				d_reg := '0'; -- write to mem
				addr_mem_rw := IP;
				IP	:= std_logic_vector (unsigned (IP) + unsigned (byte1&byte0));
				byte1 := (others => '0');
				byte0	:= addr_mem_rw(7 downto 0);
				byte1 := std_logic_vector (resize (unsigned (addr_mem_rw(NUMBER_MEMORY_BIT'length-1 downto 8)),8)); -- NOW it is 1 bit because Memory address is 9 bit
				state := detect_operate;
				sub_state := pusher;		
				cheng_reg_h_byte := '1'; -- to write in mem (detect_operare Block)
			
				
			when RET => ----------------------------<RET>--------------------------------
				SP := std_logic_vector (unsigned (SP)+2);
				IP := (byte1&byte0);
				state := next_byte;
				
			when POP  => --------------------<POP Ev>--------------------------
				reg_h (15 downto 0) := byte1&byte0;
				SP := std_logic_vector (unsigned (SP)+2);
				num_byte := 1;
				state 	:= read_byte;
				sub_state:= mover; -- void and it dont work (because d_reg=0)
				rtnstate := detect_addr;
				exstate  := detect_operate;
				
			when POPF => -------------------------<POP Flag>----------------------
				flag := byte0;
				SP := std_logic_vector (unsigned (SP)+2);
				state := next_byte;
				
			when MOVS => ----------------------------------<Mov String>----------------
				   if (w_reg = '1') then num_byte := 2; else num_byte := 1; end if;
					ram_rw_en	:= '1';
					addr_mem_rw := std_logic_vector (resize (unsigned (ES&DI),16)); -- dest
					addr_mem_rw	:= std_logic_vector (unsigned (addr_mem_rw) - 1); -- default to Write
					if (flag(7) = '0')then DI := std_logic_vector (unsigned (DI) + num_byte); else DI:= std_logic_vector (unsigned (DI) - num_byte);end if;
					state	      := Write_byte;
					rtnstate    := next_byte;
					
			when CMPS => ----------------------------------<CMP String>----------------
					reg_h(15 downto 0) := byte1&byte0;
				   if (w_reg = '1') then num_byte := 2; else num_byte := 1; end if;
					ram_rw_en	:= '1';
					addr_mem_rw := std_logic_vector (resize (unsigned (ES&DI),16)); -- dest
					if (flag(7) = '0')then DI := std_logic_vector (unsigned (DI) + num_byte); else DI:= std_logic_vector (unsigned (DI) - num_byte);end if;
					state	      := read_byte;					
					rtnstate 	:= COMP; 
					
			when COMP =>	--------------------------<Compare>------------------
					if (w_reg = '0') then
						flag(0) := reg_h (7) xor byte0 (7);	
						reg_h (8 downto 0) := std_logic_vector (unsigned(reg_h(7 downto 0))-unsigned(byte0));
						flag(0) :=  flag(0) xor reg_h (8);	
						flag(3) := reg_h (8) xor reg_h (7);
						if (reg_h (7) = '1') then flag(2) := '1'; else flag(2) := '0'; end if;
						if (reg_h (7 downto 0) = "00000000") then flag(1) := '1'; else flag(1) := '0'; end if; 
				  else
						flag(0) := reg_h (15) xor byte1 (7);	
						reg_h (16 downto 0) := std_logic_vector (unsigned(reg_h (15 downto 0))-unsigned(byte1&byte0));
						flag(0) := flag(0) xor reg_h (16);	
						flag(3) := reg_h (16) xor reg_h (15);
						if (reg_h (15) = '1') then flag(2) := '1'; else flag(2) := '0'; end if;
						if (reg_h (15 downto 0) = zeros_16) then flag(1) := '1'; else flag(1) := '0'; end if; 
					end if;					
				   state := exstate;
			 		
			when REP =>
				if (repz_en = '1') then
					if (flag(1) = '1') then
					   repz_en := '0';
						IP	:= std_logic_vector (unsigned (IP) -2);
					end if;
				elsif (repnz_en = '1') then
					if (flag(1) = '0') then
						repnz_en:= '0';
						IP	:= std_logic_vector (unsigned (IP) -2);
					end if;
				end if;
				state := next_byte;
				
			when show_char => -------------------<Show char>----------------------
					Xchar	<= std_logic_vector (unsigned(Xchar)+1);
					if (Xchar = "1010000") then
						Xchar	<= (others => '0');
						Ychar	<= std_logic_vector (unsigned(Ychar)+1);
					end if;
					state := rtnstate;
					
		   when detect_gpr1 =>    -----------------------------------<detect_gpr1>-------------------------------
			 byte1 := x"00";
				case byte0 (5 downto 3) is -- show operate
				  when "000" => -- ADD
						sub_state := adder;
				  when "001" => -- OR
						sub_state := orer;
					when "100" => -- AND
						sub_state := ander;
					when "101" => -- SUB
						sub_state := suber;
					when "111" => -- CMP
						sub_state := suber;
						compare := '1';
				  when others => null;
				end case;
					
			  if (m_reg_0 = "00") then -- const to const (e.g. add [60h],2)
				  d_reg := '0';
				  state := const_to_mem;
--				  sub_state:= adder;
			  else -- Certainly it is num to reg (e.g. add bl,2)
			   if ((NOT s_reg and w_reg) = '1') then num_byte := 2; else num_byte := 1; end if;
				d_reg := '1';
				state := Read_Byte;
				rtnstate := set_reg_h;
			  end if;

		   when detect_gpr4 =>    -----------------------------------<detect_gpr4>-------------------------------
				case byte0 (5 downto 3) is -- show operate
				  when "000" => -- INC
						sub_state := incer;
				  when "001" => -- DEC
						sub_state := decer;
				  when others => null;
				end case;
				
				if (m_reg_0 = "11" )then d_reg := '1'; else d_reg := '0'; end if; 
				  w_reg := '0';
				  state 	   := detect_addr; 
				  cheng_reg_h_byte	:= '1';

				  when detect_gpr5 =>    -----------------------------------<detect_gpr5>-------------------------------
				case byte0 (5 downto 3) is -- show operate
				  when "110" => -- PUSH
						sub_state := pusher;
				  when others => null;
				end case;
				
				if (m_reg_0 = "11" )then d_reg := '1'; else d_reg := '0'; end if;
				  w_reg := '1';
				  state 	   := detect_addr; 
				  exstate := detect_operate;
				  cheng_reg_h_byte	:= '1';
			  
			when Next_Byte =>		---------------------------<init read Next Byte>------------------------------
				num_byte := 1;	-- it has 1 parameter so read one byte
				byte0 := x"00"; byte1 := x"00"; byte2 := x"00";byte3 := x"00";
				state 	:= READ_BYTE;
				rtnstate := Detect_Inst;
				
			 when detect_operate =>	-------------------------------<detect_operate>--------------------
			 	if (val_const_bit = '1') then 
					reg_h (15 downto 0) := byte1&byte0; 
				  if (m_reg = "10") then  byte0 := byte2; byte1 := byte3;	elsif (m_reg = "01") then byte0 := byte1; byte1 := byte2; elsif (rm_t = "110")then byte0 := byte2; byte1 := byte3; end if; -- m_reg = "00" -> haven't any offset then byte0 and byte1 are ready now
				end if;
				
				if (cheng_reg_h_byte = '1') then
					reg_h (15 downto 0) := byte1&byte0; 
					cheng_reg_h_byte := '0';
				end if;
				
			 if (w_reg = '0') then
			   flag(0) := reg_h (7) xor byte0 (7);	
			 	case sub_state is
					when adder => reg_h (8 downto 0) := std_logic_vector (resize (unsigned(reg_h(7 downto 0)),9)+resize (unsigned(byte0),9)); -- 1 bit carry_flag
					when incer => reg_h (8 downto 0) := std_logic_vector (resize (unsigned(reg_h(7 downto 0)),9)+1); -- 1 bit carry_flag
					when decer => reg_h (8 downto 0) := std_logic_vector (resize (unsigned(reg_h(7 downto 0)),9)-1); -- 1 bit carry_flag
					when adcer => if (flag(0) = '1') then reg_h (8 downto 0) := std_logic_vector (unsigned(reg_h(7 downto 0))+unsigned(byte0)+1); else reg_h (8 downto 0) := std_logic_vector (unsigned(reg_h(7 downto 0))+unsigned(byte0)); end if;-- 1 bit carry_flag
					when suber => reg_h (8 downto 0) := std_logic_vector (resize (unsigned(reg_h(7 downto 0)),9)-resize (unsigned(byte0),9));
					when sbber => if (flag(0) = '1') then reg_h (8 downto 0) := std_logic_vector (unsigned(reg_h(7 downto 0))-unsigned(byte0)-1); else reg_h (8 downto 0) := std_logic_vector (unsigned(reg_h(7 downto 0))-unsigned(byte0)); end if;-- 1 bit carry_flag
					when muler => reg_h (8 downto 0) := std_logic_vector (unsigned(reg_h(7 downto 0))*unsigned(byte0));
					when ander => reg_h (8 downto 0) := reg_h (7 downto 0) and byte0;
					when xorer => reg_h (8 downto 0) := reg_h (7 downto 0) xor byte0;
					when orer  => reg_h (8 downto 0) := reg_h (7 downto 0) or  byte0;
					when mover => if (d_reg = '1')then reg_h(7 downto 0) := byte0; end if; null;
					when others => null; 
				end case;
				flag(0) :=  flag(0) xor reg_h (8);	
				flag(3) := reg_h (8) xor reg_h (7);
				if (reg_h (7) = '1') then flag(2) := '1'; else flag(2) := '0'; end if;
				if (reg_h (7 downto 0) = "00000000") then flag(1) := '1'; else flag(1) := '0'; end if; 
			else
				flag(0) := reg_h (15) xor byte1 (7);	
			   case sub_state is
			 		when adder  => reg_h (16 downto 0) := std_logic_vector (unsigned(reg_h (15 downto 0))+unsigned(byte1&byte0));
			 		when incer  => reg_h (16 downto 0) := std_logic_vector (unsigned(reg_h (15 downto 0))+1);
			 		when decer  => reg_h (16 downto 0) := std_logic_vector (unsigned(reg_h (15 downto 0))-1);
			 		when adcer  => if (flag(0) = '1' )then reg_h (16 downto 0) := std_logic_vector (unsigned(reg_h (15 downto 0))+unsigned(byte1&byte0)+1); else reg_h (16 downto 0) := std_logic_vector (unsigned(reg_h (15 downto 0))+unsigned(byte1&byte0)); end if;
					when suber  => reg_h (16 downto 0) := std_logic_vector (unsigned(reg_h (15 downto 0))-unsigned(byte1&byte0));
			 		when sbber  => if (flag(0) = '1' )then reg_h (16 downto 0) := std_logic_vector (unsigned(reg_h (15 downto 0))-unsigned(byte1&byte0)-1); else reg_h (16 downto 0) := std_logic_vector (unsigned(reg_h (15 downto 0))-unsigned(byte1&byte0)); end if;
					when muler  => reg_h (16 downto 0) := std_logic_vector (unsigned(reg_h (15 downto 0))*unsigned(byte1&byte0));
					when ander  => reg_h (16 downto 0) := reg_h (15 downto 0) and (byte1&byte0);
					when xorer  => reg_h (16 downto 0) := reg_h (15 downto 0) xor (byte1&byte0);
					when orer   => reg_h (16 downto 0) := reg_h (15 downto 0) or  (byte1&byte0);
					when pusher =>  addr_mem_rw := SP; SP := std_logic_vector (unsigned (SP)-2); -- in belw lines num_byte less addr_mem_rw so 2 less addr_mem_rw so we dont dec 2 from SP  
					when poper  =>  SP := std_logic_vector (unsigned (SP)+2); reg_h (15 downto 0) := byte1&byte0;
					when mover => if (d_reg = '1')then reg_h (15 downto 0) := byte1&byte0; end if; null;
					when others => null;
				end case;	 
				flag(0) := flag(0) xor reg_h (16);	
				flag(3) := reg_h (16) xor reg_h (15);
				if (reg_h (15) = '1') then flag(2) := '1'; else flag(2) := '0'; end if;
				if (reg_h (15 downto 0) = zeros_16) then flag(1) := '1'; else flag(1) := '0'; end if; 
			 end if;
			 
			state 	:= Next_Byte;	

 
			if (compare = '0') then
			byte0 := reg_h(7 downto 0); byte1:= reg_h(15 downto 8); 
			if (d_reg = '0') then
				if (w_reg = '1') then num_byte := 2; else num_byte := 1; end if; -- parameter is byte or word
				ram_rw_en	:= '1';
				addr_mem_rw	:= std_logic_vector (unsigned (addr_mem_rw)-num_byte-1);	-- possetive -1 for : default for writting - num_byte : because addr_mem_rw added when reading byte or word in Previously block (read_addr_mem block)
				state       := write_byte;
				rtnstate	   := next_byte;
					
			 else
				case w_reg&reg1_t is
					when '1'&iAX => AX := reg_h (15 downto 0);
					when '1'&iBX => BX := reg_h (15 downto 0);
					when '1'&iCX => CX := reg_h (15 downto 0);
					when '1'&iDX => DX := reg_h (15 downto 0);
					when '1'&iSP => SP := reg_h (15 downto 0);
					when '1'&iBP => BP := reg_h (15 downto 0);
					when '1'&iSI => SI := reg_h (15 downto 0);
					when '1'&iDI => DI := reg_h (15 downto 0);
					when '0'&iAL => AL := reg_h (7 downto 0);
					when '0'&iBL => BL := reg_h (7 downto 0);
					when '0'&iCL => CL := reg_h (7 downto 0);
					when '0'&iDL => DL := reg_h (7 downto 0);
					when '0'&iAH => AH := reg_h (15 downto 8);
					when '0'&iBH => BH := reg_h (15 downto 8);
					when '0'&iCH => CH := reg_h (15 downto 8);
					when '0'&iDH => DH := reg_h (15 downto 8);
					when others => null;
				end case;	
			end if;
			end if;
		compare := '0';
			
			when halt =>
			  null;
			  
			when Init =>	----------------------------------------------<Init>--------------------------------
			  cnt_bit := 512;	-- Read 512 Byte (1 sector)
			  main_mem_wr_en (0) <= '1';
			  num_byte	:= 1;		-- read 1 byte from sd to ram (main memory)
			  state := Read_Sector;
			  IP := (others => '1'); -- because in "Read_Sector" Block it inc 1 and then become 0000 to write first block ram else it write in secound ram's block
			  num_byte_v	:=0;
			  ram_rw_en := '0';
			  d_reg := '1';
			  flag := "00000000";
			  SP	:= x"FFFE"; -- (0-2)
			  
			when Read_Sector =>	-- read First Sector of SD Card (512 byte)----------------------<Read_Sector>-----------
			  if (sd_c_hndShk = '1') then
					if (cnt_bit /= 0) then
					  main_mem_data_in <= sd_data_out;
					  sd_h_hndShk <= '1';
					  cnt_bit	:= cnt_bit - 1;
				     IP := std_logic_vector (unsigned (IP) + 1);
					 else
					  main_mem_wr_en (0) <= '0';
					  state	:= Read_Byte;
					  rtnstate	:= detect_inst;
					  IP := (others => '0');
					  end if;
		     else
			   sd_h_hndShk <= '0'; 
		    end if;
		  end case;
		  if (ram_rw_en = '0') then 
		  	main_mem_addr	 <= IP(NUMBER_MEMORY_BIT'length-1 downto 0); else main_mem_addr<=addr_mem_rw(NUMBER_MEMORY_BIT'length-1 downto 0); end if;
		  	LED	<= LED_v;
		 end if;
		end if;
	end process;
	
	process (clk_i)
	begin
	if rising_edge (clk_i) then
	
	ClockPulse	<= std_logic_vector (unsigned (ClockPulse)+1);
	 if (ClockPulse = "1111111111111111") then
	   CLKPorcessor	<= not CLKPorcessor;
	 end if;
	end if;
	end process;
	
	NOTreset_i <= not reset_i;
	
	
--		  process (clk_i)
--		  	 variable CounterTime : std_logic_vector (19 downto 0):= (others => '0');
--	  begin
--	  if rising_edge (clk_i) then
--	  CounterTime	:= std_logic_vector (unsigned(CounterTime) + 1);
--	    if (CounterTime = "00000000000000000000") then
--	    end if;
--	  end if;
--	  end process;
	  
end Behavioral;
---------------NEW
// VHDL entity s, as the project stores it:
--**********************************************************************
-- Copyright 2012 by XESS Corp <http://www.xess.com>.
-- This program is free software: you can redistribute it and/or modify
-- it under the terms of the GNU General Public License as published by
-- the Free Software Foundation, either version 3 of the License, or
-- (at your option) any later version.
--
-- This program is distributed in the hope that it will be useful,
-- but WITHOUT ANY WARRANTY; without even the implied warranty of
-- MERCHANTABILITY or FITNESS FOR A PARTICULAR PURPOSE.  See the
-- GNU General Public License for more details.
--
-- You should have received a copy of the GNU General Public License
-- along with this program.  If not, see <http://www.gnu.org/licenses/>.
--**********************************************************************

--*********************************************************************
-- SD MEMORY CARD INTERFACE
--
-- Reads/writes a single or multiple blocks of data to/from an SD Flash card.
-- 
-- Based on work by by Steven J. Merrifield, June 2008:
-- http : //stevenmerrifield.com/tools/sd.vhd
-- 
-- Most of what I learned about interfacing to SD/SDHC cards came from here:
-- http://elm-chan.org/docs/mmc/mmc_e.html
--
-- OPERATION
--
--     Set-up:
--         First of all, you have to give the controller a clock signal on the clk_i 
--         input with a higher frequency than the serial clock sent to the SD card 
--         through the sclk_o output. You can set generic parameters for the 
--         controller to tell it the master clock frequency (100 MHz), the SCLK 
--         frequency for initialization (400 KHz), the SCLK frequency for normal 
--         operation (25 MHz), the size of data sectors in the Flash memory (512 bytes),
--         and the type of card (either SD or SDHC). I typically use a 100 MHz 
--         clock if I'm running an SD card with a 25 Mbps serial data stream. 
--       
--     Initialize it:
--         Pulsing the reset_i input high and then bringing it low again will make 
--         the controller initialize the SD card so it will work in SPI mode. 
--         Basically, it sends the card the commands CMD0, CMD8 and then ACMD41 (which
--         is CMD55 followed by CMD41). The busy_o output will be high during the 
--         initialization and will go low once it is done. 
--        
--         After the initialization command sequence, the SD card will send back an R1
--         response byte. If only the IDLE bit of the R1 response is set, then the 
--         controller will repeatedly re-try the ACMD41 command while busy_o remains 
--         high. 
--        
--         If any other bit of the R1 response is set, then an error occurred. The 
--         controller will stall, lower busy_o, and output the R1 response code on the
--         error_o bus. You'll have to pulse reset_i to unfreeze the controller. 
--     
--         If the R1 response is all zeroes (i.e., no errors occurred during the 
--         initialization), then the controller will lower busy_o and wait for a 
--         read or write operation from the host. The controller will only accept new
--         operations when busy_o is low.
--     
--     Write data:
--         To write a data block to the SD card, the address of a block is placed 
--         on the addr_i input bus and the wr_i input is raised. The address and 
--         write strobe can be removed once busy_o goes high to indicate the write 
--         operation is underway. The data to be written to the SD card is passed as 
--         follows: 
--     
--         1. The controller requests a byte of data by raising the hndShk_o output.
--         2. The host applies the next byte to the data_i input bus and raises the 
--            hndShk_i input.
--         3. The controller accepts the byte and lowers the hndShk_o output.
--         4. The host lowers the hndShk_i input.
--     
--         This sequence of steps is repeated until all BLOCK_SIZE_G bytes of the 
--         data block are passed from the host to the controller. Once all the data 
--         is passed, the sector on the SD card will be written and the busy_o output 
--         will be lowered. 
--     
--     Read data:
--         To read a block of data from the SD card, the address of a block is 
--         placed on the addr_i input bus and the rd_i input is raised. The address 
--         and read strobe can be removed once busy_o goes high to indicate the read 
--         operation is underway. The data read from the SD card is passed to the 
--         host as follows: 
--     
--         1. The controller raises the hndShk_o output when the next data byte is available.
--         2. The host reads the byte from the data_o output bus and raises the hndShk_i input.
--         3. The controller lowers the hndShk_o output.
--         4. The host lowers the hndShk_i input.
--     
--         This sequence of steps is repeated until all BLOCK_SIZE_G bytes of the 
--         data block are passed from the controller to the host. Once all the data 
--         is read, the busy_o output will be lowered.
--     
--     Handle errors:
--         If an error is detected during either a read or write operation, then the
--         controller will stall, lower busy_o, and output an error code on the 
--         error_o bus. You'll have to pulse reset_i to unfreeze the controller. That 
--         may seem a bit excessive, but it does guarantee that you can't ignore any 
--         errors that occur.
--
-- TODO:
--
--     * Implement multi-block read and write commands.
--     * Allow host to send/receive SPI commands/data directly to
--       the SD card through the controller.
-- *********************************************************************


library ieee;
use ieee.std_logic_1164.all;
use ieee.numeric_std.all;
use work.CommonPckg.all;

package SdCardPckg is

  type CardType_t is (SD_CARD_E, SDHC_CARD_E);  -- Define the different types of SD cards.

  component SdCardCtrl is
    generic (
      FREQ_G          : real       := 50.0;  -- Master clock frequency (MHz).
      INIT_SPI_FREQ_G : real       := 0.4;  -- Slow SPI clock freq. during initialization (MHz).
      SPI_FREQ_G      : real       := 25.0;  -- Operational SPI freq. to the SD card (MHz).
      BLOCK_SIZE_G    : natural    := 512;  -- Number of bytes in an SD card block or sector.
      CARD_TYPE_G     : CardType_t := SD_CARD_E  -- Type of SD card connected to this controller.
      );
    port (
      -- Host-side interface signals.
      clk_i      : in  std_logic;       -- Master clock.
      reset_i    : in  std_logic                     := NO;  -- active-high, synchronous  reset.
      rd_i       : in  std_logic                     := NO;  -- active-high read block request.
      wr_i       : in  std_logic                     := NO;  -- active-high write block request.
      continue_i : in  std_logic                     := NO;  -- If true, inc address and continue R/W.
      addr_i     : in  std_logic_vector(31 downto 0) := x"00000000";  -- Block address.
      data_i     : in  std_logic_vector(7 downto 0)  := x"00";  -- Data to write to block.
      data_o     : out std_logic_vector(7 downto 0)  := x"00";  -- Data read from block.
      busy_o     : out std_logic;  -- High when controller is busy performing some operation.
      hndShk_i   : in  std_logic;  -- High when host has data to give or has taken data.
      hndShk_o   : out std_logic;  -- High when controller has taken data or has data to give.
      error_o    : out std_logic_vector(15 downto 0) := (others => NO);
      -- I/O signals to the external SD card.
      cs_bo      : out std_logic                     := HI;  -- Active-low chip-select.
      sclk_o     : out std_logic                     := LO;  -- Serial clock to SD card.
      mosi_o     : out std_logic                     := HI;  -- Serial data output to SD card.
      miso_i     : in  std_logic                     := ZERO  -- Serial data input from SD card.
      );
  end component;

end package;


library ieee;
use ieee.math_real.all;
use ieee.std_logic_1164.all;
use ieee.numeric_std.all;
use work.CommonPckg.all;
use work.SdCardPckg.all;

entity SdCardCtrl is
  generic (
    FREQ_G          : real       := 50.0;     -- Master clock frequency (MHz).
    INIT_SPI_FREQ_G : real       := 0.4;  -- Slow SPI clock freq. during initialization (MHz).
    SPI_FREQ_G      : real       := 25.0;  -- Operational SPI freq. to the SD card (MHz).
    BLOCK_SIZE_G    : natural    := 512;  -- Number of bytes in an SD card block or sector.
    CARD_TYPE_G     : CardType_t := SD_CARD_E  -- Type of SD card connected to this controller.
    );
  port (
    -- Host-side interface signals.
    clk_i      : in  std_logic;         -- Master clock.
    reset_i    : in  std_logic                     := NO;  -- active-high, synchronous  reset.
    rd_i       : in  std_logic                     := NO;  -- active-high read block request.
    wr_i       : in  std_logic                     := NO;  -- active-high write block request.
    continue_i : in  std_logic                     := NO;  -- If true, inc address and continue R/W.
    addr_i     : in  std_logic_vector(31 downto 0) := x"00000000";  -- Block address.
    data_i     : in  std_logic_vector(7 downto 0)  := x"00";  -- Data to write to block.
    data_o     : out std_logic_vector(7 downto 0)  := x"00";  -- Data read from block.
    busy_o     : out std_logic;  -- High when controller is busy performing some operation.
    hndShk_i   : in  std_logic;  -- High when host has data to give or has taken data.
    hndShk_o   : out std_logic;  -- High when controller has taken data or has data to give.
    error_o    : out std_logic_vector(15 downto 0) := (others => NO);
	 LED			: out std_logic_vector(3 downto 0)  := (others => NO);
    -- I/O signals to the external SD card.
    cs_bo      : out std_logic                     := HI;  -- Active-low chip-select.
    sclk_o     : out std_logic                     := LO;  -- Serial clock to SD card.
    mosi_o     : out std_logic                     := HI;  -- Serial data output to SD card.
    miso_i     : in  std_logic                     := ZERO  -- Serial data input from SD card.
    );
end entity;



architecture arch of SdCardCtrl is

  signal sclk_r   : std_logic := ZERO;  -- Register output drives SD card clock.
  signal hndShk_r : std_logic := NO;  -- Register output drives handshake output to host.
  signal LEDr  		: std_logic_vector(3 downto 0) := (others => NO);
begin
  
  process(clk_i)  -- FSM process for the SD card controller.

    type FsmState_t is (    -- States of the SD card controller FSM.
      START_INIT,  -- Send initialization clock pulses to the deselected SD card.    
      SEND_CMD0,                        -- Put the SD card in the IDLE state.
      CHK_CMD0_RESPONSE,    -- Check card's R1 response to the CMD0.
      SEND_CMD8,   -- This command is needed to initialize SDHC cards.
      GET_CMD8_RESPONSE,                -- Get the R7 response to CMD8.
      SEND_CMD55,                       -- Send CMD55 to the SD card. 
      SEND_CMD41,                       -- Send CMD41 to the SD card.
      CHK_ACMD41_RESPONSE,  -- Check if the SD card has left the IDLE state.     
      WAIT_FOR_HOST_RW,  -- Wait for the host to issue a read or write command.
      RD_BLK,    -- Read a block of data from the SD card.
      WR_BLK,    -- Write a block of data to the SD card.
      WR_WAIT,   -- Wait for SD card to finish writing the data block.
      START_TX,                         -- Start sending command/data.
      TX_BITS,   -- Shift out remaining command/data bits.
      GET_CMD_RESPONSE,  -- Get the R1 response of the SD card to a command.
      RX_BITS,   -- Receive response/data from the SD card.
      DESELECT,  -- De-select the SD card and send some clock pulses (Must enter with sclk at zero.)
      PULSE_SCLK,  -- Issue some clock pulses. (Must enter with sclk at zero.)
      REPORT_ERROR                      -- Report error and stall until reset.
      );
    variable state_v    : FsmState_t := START_INIT;  -- Current state of the FSM.
    variable rtnState_v : FsmState_t;  -- State FSM returns to when FSM subroutine completes.

    -- Timing constants based on the master clock frequency and the SPI SCLK frequencies.
    constant CLKS_PER_INIT_SCLK_C      : real    := FREQ_G / INIT_SPI_FREQ_G;
    constant CLKS_PER_SCLK_C           : real    := FREQ_G / SPI_FREQ_G;
    constant MAX_CLKS_PER_SCLK_C       : real    := realmax(CLKS_PER_INIT_SCLK_C, CLKS_PER_SCLK_C);
    constant MAX_CLKS_PER_SCLK_PHASE_C : natural := integer(round(MAX_CLKS_PER_SCLK_C / 2.0));
    constant INIT_SCLK_PHASE_PERIOD_C  : natural := integer(round(CLKS_PER_INIT_SCLK_C / 2.0));
    constant SCLK_PHASE_PERIOD_C       : natural := integer(round(CLKS_PER_SCLK_C / 2.0));
    constant DELAY_BETWEEN_BLOCK_RW_C  : natural := SCLK_PHASE_PERIOD_C;

    -- Registers for generating slow SPI SCLK from the faster master clock.
    variable clkDivider_v     : natural range 0 to MAX_CLKS_PER_SCLK_PHASE_C;  -- Holds the SCLK period.
    variable sclkPhaseTimer_v : natural range 0 to MAX_CLKS_PER_SCLK_PHASE_C;  -- Counts down to zero, then SCLK toggles.

    constant NUM_INIT_CLKS_C : natural := 160;  -- Number of initialization clocks to SD card.
    variable bitCnt_v        : natural range 0 to NUM_INIT_CLKS_C;  -- Tx/Rx bit counter.

    constant CRC_SZ_C    : natural := 2;  -- Number of CRC bytes for read/write blocks.
    -- When reading blocks of data, get 0xFE + [DATA_BLOCK] + [CRC].
    constant RD_BLK_SZ_C : natural := 1 + BLOCK_SIZE_G + CRC_SZ_C;
    -- When writing blocks of data, send 0xFF + 0xFE + [DATA BLOCK] + [CRC] then receive response byte.
    constant WR_BLK_SZ_C : natural := 1 + 1 + BLOCK_SIZE_G + CRC_SZ_C + 1;
    variable byteCnt_v   : natural range 0 to IntMax(WR_BLK_SZ_C, RD_BLK_SZ_C);  -- Tx/Rx byte counter.

    -- Command bytes for various SD card operations.
    subtype Cmd_t is std_logic_vector(7 downto 0);
    constant CMD0_C          : Cmd_t := std_logic_vector(to_unsigned(16#40# + 0, Cmd_t'length));
    constant CMD8_C          : Cmd_t := std_logic_vector(to_unsigned(16#40# + 8, Cmd_t'length));
    constant CMD55_C         : Cmd_t := std_logic_vector(to_unsigned(16#40# + 55, Cmd_t'length));
    constant CMD41_C         : Cmd_t := std_logic_vector(to_unsigned(16#40# + 41, Cmd_t'length));
    constant READ_BLK_CMD_C  : Cmd_t := std_logic_vector(to_unsigned(16#40# + 17, Cmd_t'length));
    constant WRITE_BLK_CMD_C : Cmd_t := std_logic_vector(to_unsigned(16#40# + 24, Cmd_t'length));

    -- Except for CMD0 and CMD8, SD card ops don't need a CRC, so use a fake one for that slot in the command.
    constant FAKE_CRC_C : std_logic_vector(7 downto 0) := x"FF";

    variable addr_v : unsigned(addr_i'range);  -- Address of current block for R/W operations.

    -- Maximum Tx to SD card consists of command + address + CRC. Data Tx is just a single byte.
    variable tx_v : std_logic_vector(CMD0_C'length + addr_v'length + FAKE_CRC_C'length - 1 downto 0);  -- Data/command to SD card.
    alias txCmd_v is tx_v;              -- Command transmission shift register.
    alias txData_v is tx_v(tx_v'high downto tx_v'high - data_i'length + 1);  -- Data byte transmission shift register.

    variable rx_v               : std_logic_vector(data_i'range);  -- Data/response byte received from SD card.
    -- Various response codes.
    subtype Response_t is std_logic_vector(rx_v'range);
    constant ACTIVE_NO_ERRORS_C : Response_t := "00000000";  -- Normal R1 code after initialization.
    constant IDLE_NO_ERRORS_C   : Response_t := "00000001";  -- Normal R1 code after CMD0.
    constant DATA_ACCEPTED_C    : Response_t := "---00101";  -- SD card accepts data block from host.
    constant DATA_REJ_CRC_C     : Response_t := "---01011";  -- SD card rejects data block from host due to CRC error.
    constant DATA_REJ_WERR_C    : Response_t := "---01101";  -- SD card rejects data block from host due to write error.
    -- Various tokens.
    subtype Token_t is std_logic_vector(rx_v'range);
    constant NO_TOKEN_C         : Token_t    := x"FF";  -- Received before the SD card responds to a block read command.
    constant START_TOKEN_C      : Token_t    := x"FE";  -- Starting byte preceding a data block.

    -- Flags that are set/cleared to affect the operation of the FSM.
    variable getCmdResponse_v : boolean;  -- When true, get R1 response to command sent to SD card.
    variable rtnData_v        : boolean;  -- When true, signal to host when a data byte arrives from SD card.
    variable doDeselect_v     : boolean;  -- When true, de-select SD card after a command is issued.
    
  begin
    if rising_edge(clk_i) then

      if reset_i = YES then             -- Perform a reset.
        state_v          := START_INIT;  -- Send the FSM to the initialization entry-point.
        sclkPhaseTimer_v := 0;  -- Don't delay the initialization right after reset.
        busy_o           <= YES;  -- Busy while the SD card interface is being initialized.

      elsif sclkPhaseTimer_v /= 0 then
        -- Setting the clock phase timer to a non-zero value delays any further actions
        -- and generates the slower SPI clock from the faster master clock.
        sclkPhaseTimer_v := sclkPhaseTimer_v - 1;

        -- Clock phase timer has reached zero, so check handshaking sync. between host and controller.

        -- Handshaking lets the host control the flow of data to/from the SD card controller.
        -- Handshaking between the SD card controller and the host proceeds as follows:
        --   1: Controller raises its handshake and waits.
        --   2: Host sees controller handshake and raises its handshake in acknowledgement.
        --   3: Controller sees host handshake acknowledgement and lowers its handshake.
        --   4: Host sees controller lower its handshake and removes its handshake.
        --
        -- Handshaking is bypassed when the controller FSM is initializing the SD card.
        
      elsif state_v /= START_INIT and hndShk_r = HI and hndShk_i = LO then
        null;            -- Waiting for the host to acknowledge handshake.
      elsif state_v /= START_INIT and hndShk_r = HI and hndShk_i = HI then
        txData_v := data_i;             -- Get any data passed from the host.
        hndShk_r <= LO;  -- The host acknowledged, so lower the controller handshake.
      elsif state_v /= START_INIT and hndShk_r = LO and hndShk_i = HI then
        null;            -- Waiting for the host to lower its handshake.
      elsif (state_v = START_INIT) or (hndShk_r = LO and hndShk_i = LO) then
        -- Both handshakes are low, so the controller operations can proceed.
        
        busy_o <= YES;  -- Busy by default. Only false when waiting for R/W from host or stalled by error.
			LEDr (3 downto 0) <= "0001";
        case state_v is
          
          when START_INIT =>  -- Deselect the SD card and send it a bunch of clock pulses with MOSI high.
            error_o          <= (others => ZERO);  -- Clear error flags.
            clkDivider_v     := INIT_SCLK_PHASE_PERIOD_C - 1;  -- Use slow SPI clock freq during init.
            sclkPhaseTimer_v := INIT_SCLK_PHASE_PERIOD_C - 1;  -- and set the duration of the next clock phase.
            sclk_r           <= LO;     -- Start with low clock to the SD card.
            hndShk_r         <= LO;     -- Initialize handshake signal.
            addr_v           := (others => ZERO);  -- Initialize address.
            rtnData_v        := false;  -- No data is returned to host during initialization.
            bitCnt_v         := NUM_INIT_CLKS_C;  -- Generate this many clock pulses.
            state_v          := DESELECT;  -- De-select the SD card and pulse SCLK.
            rtnState_v       := SEND_CMD0;  -- Then go to this state after the clock pulses are done.
				LEDr (3 downto 0) <= "0010"; --nabood
            
          when SEND_CMD0 =>             -- Put the SD card in the IDLE state.
            cs_bo            <= LO;     -- Enable the SD card.
            txCmd_v          := CMD0_C & x"00000000" & x"95";  -- 0x95 is the correct CRC for this command.
            bitCnt_v         := txCmd_v'length;  -- Set bit counter to the size of the command.
            getCmdResponse_v := true;  -- Sending a command that generates a response.
            doDeselect_v     := true;  -- De-select SD card after this command finishes.
            state_v          := START_TX;  -- Go to FSM subroutine to send the command.
            rtnState_v       := CHK_CMD0_RESPONSE;  -- Then check the response to the command.
				LEDr (3 downto 0) <= "0010"; -- Nabood
            
          when CHK_CMD0_RESPONSE =>  -- Check card's R1 response to the CMD0.
            if rx_v = IDLE_NO_ERRORS_C then
              state_v := SEND_CMD8;  -- Continue init if SD card is in IDLE state with no errors
            else
              state_v := SEND_CMD0;     -- Otherwise, try CMD0 again.
            end if;
            LEDr (3 downto 0) <= "0011";
				
          when SEND_CMD8 =>  -- This command is needed to initialize SDHC cards.
            cs_bo            <= LO;     -- Enable the SD card.
            txCmd_v          := CMD8_C & x"000001aa" & x"87";  -- 0x87 is the correct CRC for this command.
            bitCnt_v         := txCmd_v'length;  -- Set bit counter to the size of the command.
            getCmdResponse_v := true;  -- Sending a command that generates a response.
            doDeselect_v     := false;  -- Don't de-select, need to get the R7 response sent from the SD card.
            state_v          := START_TX;  -- Go to FSM subroutine to send the command.
            rtnState_v       := GET_CMD8_RESPONSE;  -- Then go to this state after the command is sent.
            LEDr (3 downto 0) <= "0100";
				
          when GET_CMD8_RESPONSE =>     -- Get the R7 response to CMD8.
            cs_bo            <= LO;  -- The SD card should already be enabled, but let's be explicit.
            bitCnt_v         := 31;     -- Four bytes (32 bits) in R7 response.
            getCmdResponse_v := false;  -- Not sending a command that generates a response.
            doDeselect_v     := true;  -- De-select card to end the command after getting the four bytes.
            state_v          := RX_BITS;  -- Go to FSM subroutine to get the R7 response.
            rtnState_v       := SEND_CMD55;  -- Then go here (we don't care what the actual R7 response is).
				LEDr (3 downto 0) <= "0101";

          when SEND_CMD55 =>  -- Send CMD55 as preamble of ACMD41 initialization command.
            cs_bo            <= LO;     -- Enable the SD card.
            txCmd_v          := CMD55_C & x"00000000" & FAKE_CRC_C;
            bitCnt_v         := txCmd_v'length;  -- Set bit counter to the size of the command.
            getCmdResponse_v := true;  -- Sending a command that generates a response.
            doDeselect_v     := true;  -- De-select SD card after this command finishes.
            state_v          := START_TX;  -- Go to FSM subroutine to send the command.
            rtnState_v       := SEND_CMD41;  -- Then go to this state after the command is sent.
		      LEDr (3 downto 0) <= "0110";
            
          when SEND_CMD41 =>  -- Send the SD card the initialization command.
            cs_bo            <= LO;     -- Enable the SD card.
            txCmd_v          := CMD41_C & x"40000000" & FAKE_CRC_C;
            bitCnt_v         := txCmd_v'length;  -- Set bit counter to the size of the command.
            getCmdResponse_v := true;  -- Sending a command that generates a response.
            doDeselect_v     := true;  -- De-select SD card after this command finishes.
            state_v          := START_TX;  -- Go to FSM subroutine to send the command.
            rtnState_v       := CHK_ACMD41_RESPONSE;  -- Then check the response to the command.
				LEDr (3 downto 0) <= "0111";
            
          when CHK_ACMD41_RESPONSE =>
            -- The CMD55, CMD41 sequence should cause the SD card to leave the IDLE state
            -- and become ready for SPI read/write operations. If still IDLE, then repeat the CMD55, CMD41 sequence.
            -- If one of the R1 error flags is set, then report the error and stall.
            if rx_v = ACTIVE_NO_ERRORS_C then   -- Not IDLE, no errors.
              state_v := WAIT_FOR_HOST_RW;  -- Start processing R/W commands from the host.
            elsif rx_v = IDLE_NO_ERRORS_C then  -- Still IDLE but no errors. 
              state_v := SEND_CMD55;    -- Repeat the CMD55, CMD41 sequence.
            else                        -- Some error occurred.
              state_v := REPORT_ERROR;  -- Report the error and stall.
            end if;
				LEDr (3 downto 0) <= "1000";
            
          when WAIT_FOR_HOST_RW =>  -- Wait for the host to read or write a block of data from the SD card.
            clkDivider_v     := SCLK_PHASE_PERIOD_C - 1;  -- Set SPI clock frequency for normal operation.
            getCmdResponse_v := true;  -- Get R1 response to any commands issued to the SD card.
            if rd_i = YES then  -- send READ command and address to the SD card.
              cs_bo <= LO;              -- Enable the SD card.
              if continue_i = YES then  -- Multi-block read. Use stored address.
                if CARD_TYPE_G = SD_CARD_E then  -- SD cards use byte-addressing, 
                  addr_v := addr_v + BLOCK_SIZE_G;  -- so add block-size to get next block address.
                else                    -- SDHC cards use block-addressing,
                  addr_v := addr_v + 1;  -- so just increment current block address.
                end if;
                txCmd_v := READ_BLK_CMD_C & std_logic_vector(addr_v) & FAKE_CRC_C;
              else                      -- Single-block read.
                txCmd_v := READ_BLK_CMD_C & addr_i & FAKE_CRC_C;  -- Use address supplied by host.
                addr_v  := unsigned(addr_i);  -- Store address for multi-block operations.
              end if;
              bitCnt_v   := txCmd_v'length;  -- Set bit counter to the size of the command.
              byteCnt_v  := RD_BLK_SZ_C;
              state_v    := START_TX;  -- Go to FSM subroutine to send the command.
              rtnState_v := RD_BLK;  -- Then go to this state to read the data block.
            elsif wr_i = YES then  -- send WRITE command and address to the SD card.
              cs_bo <= LO;              -- Enable the SD card.
              if continue_i = YES then  -- Multi-block write. Use stored address.
                if CARD_TYPE_G = SD_CARD_E then  -- SD cards use byte-addressing, 
                  addr_v := addr_v + BLOCK_SIZE_G;  -- so add block-size to get next block address.
                else                    -- SDHC cards use block-addressing,
                  addr_v := addr_v + 1;  -- so just increment current block address.
                end if;
                txCmd_v := WRITE_BLK_CMD_C & std_logic_vector(addr_v) & FAKE_CRC_C;
              else                      -- Single-block write.
                txCmd_v := WRITE_BLK_CMD_C & addr_i & FAKE_CRC_C;  -- Use address supplied by host.
                addr_v  := unsigned(addr_i);  -- Store address for multi-block operations.
              end if;
              bitCnt_v   := txCmd_v'length;  -- Set bit counter to the size of the command.
              byteCnt_v  := WR_BLK_SZ_C;    -- Set number of bytes to write.
              state_v    := START_TX;  -- Go to this FSM subroutine to send the command ...
              rtnState_v := WR_BLK;  -- then go to this state to write the data block.
            else              -- Do nothing and wait for command from host.
              cs_bo   <= HI;            -- Deselect the SD card.
              busy_o  <= NO;  -- SD card interface is waiting for R/W from host, so it's not busy.
              state_v := WAIT_FOR_HOST_RW;  -- Keep waiting for command from host.
            end if;
				LEDr (3 downto 0) <= "1001";

          when RD_BLK =>          -- Read a block of data from the SD card.
            -- Some default values for these...
            rtnData_v  := false;  -- Data is only returned to host in one place.
            bitCnt_v   := rx_v'length - 1;   -- Receiving byte-sized data.
            state_v    := RX_BITS;      -- Call the bit receiver routine.
            rtnState_v := RD_BLK;   -- Return here when done receiving a byte.
            if byteCnt_v = RD_BLK_SZ_C then  -- Initial read to prime the pump.
              byteCnt_v := byteCnt_v - 1;
            elsif byteCnt_v = RD_BLK_SZ_C -1 then  -- Then look for the data block start token.
              if rx_v = NO_TOKEN_C then  -- Receiving 0xFF means the card hasn't responded yet. Keep trying.
                null;
              elsif rx_v = START_TOKEN_C then
                rtnData_v := true;  -- Found the start token, so now start returning data byes to the host.
                byteCnt_v := byteCnt_v - 1;
              else  -- Getting anything else means something strange has happened.
                state_v := REPORT_ERROR;
              end if;
            elsif byteCnt_v >= 3 then  -- Now bytes of data from the SD card are received.
              rtnData_v := true;        -- Return this data to the host.
              byteCnt_v := byteCnt_v - 1;
            elsif byteCnt_v = 2 then  -- Receive the 1st CRC byte at the end of the data block.
              byteCnt_v := byteCnt_v - 1;
            elsif byteCnt_v = 1 then    -- Receive the 2nd
              byteCnt_v := byteCnt_v - 1;
            else    -- Reading is done, so deselect the SD card.
              sclk_r     <= LO;
              bitCnt_v   := 2;
              state_v    := DESELECT;
              rtnState_v := WAIT_FOR_HOST_RW;
            end if;
				LEDr (3 downto 0) <= "1010";
            
          when WR_BLK =>             -- Write a block of data to the SD card.
            -- Some default values for these...
            getCmdResponse_v := false;  -- Sending data bytes so there's no command response from SD card.
            bitCnt_v         := txData_v'length;  -- Transmitting byte-sized data.
            state_v          := START_TX;  -- Call the bit transmitter routine.
            rtnState_v       := WR_BLK;  -- Return here when done transmitting a byte.
            if byteCnt_v = WR_BLK_SZ_C then
              txData_v := NO_TOKEN_C;  -- Hold MOSI high for one byte before data block goes out.
            elsif byteCnt_v = WR_BLK_SZ_C - 1 then     -- Send start token.
              txData_v := START_TOKEN_C;   -- Starting token for data block.
            elsif byteCnt_v >= 4 then   -- Now send bytes in the data block.
              hndShk_r <= HI;           -- Signal host to provide data.
            -- The transmit shift register is loaded with data from host in the handshaking section above.
            elsif byteCnt_v = 3 or byteCnt_v = 2 then  -- Send two phony CRC bytes at end of packet.
              txData_v := FAKE_CRC_C;
            elsif byteCnt_v = 1 then
              bitCnt_v   := rx_v'length - 1;
              state_v    := RX_BITS;  -- Get response of SD card to the write operation.
              rtnState_v := WR_WAIT;
            else                        -- Check received response byte.
              if std_match(rx_v, DATA_ACCEPTED_C) then  -- Data block was accepted.
                state_v := WR_WAIT;  -- Wait for the SD card to finish writing the data into Flash.
              else                      -- Data block was rejected.
                error_o(15 downto 8) <= rx_v;
                state_v              := REPORT_ERROR;  -- Report the error.
              end if;
            end if;
            byteCnt_v := byteCnt_v - 1;
				LEDr (3 downto 0) <= "1011";
            
          when WR_WAIT =>  -- Wait for SD card to finish writing the data block.
            -- The SD card will pull MISO low while it is busy, and raise it when it is done.
            sclk_r           <= not sclk_r;    -- Toggle the SPI clock...
            sclkPhaseTimer_v := clkDivider_v;  -- and set the duration of the next clock phase.
            if sclk_r = HI and miso_i = HI then  -- Data block has been written, so deselect the SD card.
              bitCnt_v   := 2;
              state_v    := DESELECT;
              rtnState_v := WAIT_FOR_HOST_RW;
            end if;
				LEDr (3 downto 0) <= "1100";
            
          when START_TX =>
            -- Start sending command/data by lowering SCLK and outputing MSB of command/data
            -- so it has plenty of setup before the rising edge of SCLK.
            sclk_r           <= LO;  -- Lower the SCLK (although it should already be low).
            sclkPhaseTimer_v := clkDivider_v;  -- Set the duration of the low SCLK.
            mosi_o           <= tx_v(tx_v'high);  -- Output MSB of command/data.
            tx_v             := tx_v(tx_v'high-1 downto 0) & ONE;  -- Shift command/data register by one bit.
            bitCnt_v         := bitCnt_v - 1;  -- The first bit has been sent, so decrement bit counter.
            state_v          := TX_BITS;  -- Go here to shift out the rest of the command/data bits.
				LEDr (3 downto 0) <= "1101";
            
          when TX_BITS =>  -- Shift out remaining command/data bits and (possibly) get response from SD card.
            sclk_r           <= not sclk_r;    -- Toggle the SPI clock...
            sclkPhaseTimer_v := clkDivider_v;  -- and set the duration of the next clock phase.
            if sclk_r = HI then
              -- SCLK is going to be flipped from high to low, so output the next command/data bit
              -- so it can setup while SCLK is low.
              if bitCnt_v /= 0 then  -- Keep sending bits until the bit counter hits zero.
                mosi_o   <= tx_v(tx_v'high);
                tx_v     := tx_v(tx_v'high-1 downto 0) & ONE;
                bitCnt_v := bitCnt_v - 1;
              else
                if getCmdResponse_v then
                  state_v  := GET_CMD_RESPONSE;  -- Get a response to the command from the SD card.
                  bitCnt_v := Response_t'length - 1;  -- Length of the expected response.
                else
                  state_v          := rtnState_v;  -- Return to calling state (no need to get a response).
                  sclkPhaseTimer_v := 0;  -- Clear timer so next SPI op can begin ASAP with SCLK low.
                end if;
              end if;
            end if;
				LEDr (3 downto 0) <= "1110";

          when GET_CMD_RESPONSE =>  -- Get the response of the SD card to a command.
            if sclk_r = HI and miso_i = LO then  -- MISO will be held high by SD card until 1st bit of R1 response, which is 0.
              -- Shift in the MSB bit of the response.
              rx_v     := rx_v(rx_v'high-1 downto 0) & miso_i;
              bitCnt_v := bitCnt_v - 1;
              state_v  := RX_BITS;  -- Now receive the reset of the response.
            end if;
            sclk_r           <= not sclk_r;    -- Toggle the SPI clock...
            sclkPhaseTimer_v := clkDivider_v;  -- and set the duration of the next clock phase.
				LEDr (3 downto 0) <= "1010";
				
          when RX_BITS =>               -- Receive bits from the SD card.
            if sclk_r = HI then    -- Bits enter after the rising edge of SCLK.
              rx_v := rx_v(rx_v'high-1 downto 0) & miso_i;
              if bitCnt_v /= 0 then     -- More bits left to receive.
                bitCnt_v := bitCnt_v - 1;
              else                      -- Last bit has been received.
                if rtnData_v then       -- Send the received data to the host.
                  data_o   <= rx_v;     -- Output received data to the host.
                  hndShk_r <= HI;  -- Signal to the host that the data is ready.
                end if;
                if doDeselect_v then
                  bitCnt_v := 1;
                  state_v  := DESELECT;  -- De-select SD card before returning.
                else
                  state_v := rtnState_v;  -- Otherwise, return to calling state without de-selecting.
                end if;
              end if;
            end if;
            sclk_r           <= not sclk_r;    -- Toggle the SPI clock...
            sclkPhaseTimer_v := clkDivider_v;  -- and set the duration of the next clock phase.
            LEDr (3 downto 0) <= "0000";
				
          when DESELECT =>  -- De-select the SD card and send some clock pulses (Must enter with sclk at zero.)
            doDeselect_v     := false;  -- Once the de-select is done, clear the flag that caused it.
            cs_bo            <= HI;     -- De-select the SD card.
            mosi_o           <= HI;  -- Keep the data input of the SD card pulled high.
            state_v          := PULSE_SCLK;  -- Pulse the clock so the SD card will see the de-select.
            sclk_r           <= LO;  -- Clock is set low so the next rising edge will see the new CS and MOSI
            sclkPhaseTimer_v := clkDivider_v;  -- Set the duration of the next clock phase.
            LEDr (3 downto 0) <= "0001";
				
          when PULSE_SCLK =>  -- Issue some clock pulses. (Must enter with sclk at zero.)
            if sclk_r = HI then
              if bitCnt_v /= 0 then
                bitCnt_v := bitCnt_v - 1;
              else  -- Return to the calling routine when the pulse counter reaches zero.
                state_v := rtnState_v;
              end if;
            end if;
            sclk_r           <= not sclk_r;    -- Toggle the SPI clock...
            sclkPhaseTimer_v := clkDivider_v;  -- and set the duration of the next clock phase.
            LEDr (3 downto 0) <= "0010";  --nabood
				
          when REPORT_ERROR =>  -- Report the error code and stall here until a reset occurs.
            error_o(rx_v'range) <= rx_v;  -- Output the SD card response as the error code.
            busy_o              <= NO;  -- Not busy.
				LEDr (3 downto 0) <= "0011";
				
          when others =>
            state_v := WAIT_FOR_HOST_RW;
				LEDr (3 downto 0) <= "0100"; -- hamin bood
        end case;
      end if;
    end if;
  end process;

  sclk_o   <= sclk_r;    -- Output the generated SPI clock for the SD card.
  hndShk_o <= hndShk_r;  -- Output the generated handshake to the host.
  LED (3 downto 0) <= LEDr (3 downto 0);
end architecture;




--**********************************************************************
-- This module connects the SD card controller interface to a HostIoToDut
-- interface so the controller can be tested from a PC over a USB link.
--**********************************************************************

// VHDL entity v, as the project stores it:
library IEEE;
use IEEE.STD_LOGIC_1164.ALL;

--use IEEE.STD_LOGIC_UNSIGNED.ALL;
use ieee.numeric_std.all;

entity MyVGA is
  port ( CLK_50MHz: in std_logic;
			Xchar : std_logic_vector(6 downto 0);
			Ychar : std_logic_vector(4 downto 0);
			char : std_logic_vector(6 downto 0);
         VS: out std_logic;
			HS: out std_logic;
			RED: out std_logic;
			GREEN: out std_logic;
			BLUE: out std_logic
  );
end MyVGA;

architecture Behavioral of MyVGA is
  -- VGA Definitions starts
  constant HDisplayArea: integer:= 640; -- horizontal display area
  constant HLimit: integer:= 800; -- maximum horizontal amount (limit)
  constant HFrontPorch: integer:= 16; -- h. front porch
  constant HBackPorch: integer:= 48;	-- h. back porch
  constant HSyncWidth: integer:= 96;	-- h. pulse width
  
  constant VDisplayArea: integer:= 480; -- vertical display area
  constant VLimit: integer:= 525; -- maximum vertical amount (limit)
  constant VFrontPorch: integer:= 10;	-- v. front porch
  constant VBackPorch: integer:= 33;	-- v. back porch
  constant VSyncWidth: integer:= 2;	-- v. pulse width  
    
  signal Clk_25MHz: std_logic := '0';  
  signal HBlank, VBlank, Blank: std_logic := '0';
    
	 
  signal CurrentHPos: std_logic_vector(10 downto 0) := (others => '0'); -- goes to 1100100000 = 800
  signal CurrentVPos: std_logic_vector(10 downto 0) := (others => '0'); -- goes to 1000001101 = 525
  signal ScanlineX, ScanlineY: std_logic_vector(10 downto 0);
  

  signal ColorOutput: std_logic_vector(2 downto 0);
  -- VGA Definitions end
  
    signal CounterX: std_logic_vector(9 downto 0) := (others => '0'); -- goes to 1100100000 = 680
    signal CounterY: std_logic_vector(8 downto 0) := (others => '0'); -- goes to 1100100000 = 512
	 
	 signal CounterTime : std_logic_vector (19 downto 0):= (others => '0');
	 signal ADDR_ROM :STD_LOGIC_VECTOR(6 DOWNTO 0);
	 signal DATA_OUT_ROM: STD_LOGIC_VECTOR(63 DOWNTO 0);
	
COMPONENT ram
  PORT (
    clka : IN STD_LOGIC;
    wea : IN STD_LOGIC_VECTOR(0 DOWNTO 0);
    addra : IN STD_LOGIC_VECTOR(14 DOWNTO 0);
    dina : IN STD_LOGIC_VECTOR(7 DOWNTO 0);
    douta : OUT STD_LOGIC_VECTOR(7 DOWNTO 0)
  );
END COMPONENT;

COMPONENT VGACHAR
  PORT (
    clka : IN STD_LOGIC;
    addra : IN STD_LOGIC_VECTOR(6 DOWNTO 0);
    douta : OUT STD_LOGIC_VECTOR(63 DOWNTO 0)
  );
END COMPONENT;

  
signal WEn : STD_LOGIC_VECTOR(0 DOWNTO 0);
signal VGA_ADDR_RAM :STD_LOGIC_VECTOR(14 DOWNTO 0);
signal VGA_DATA_IN_RAM	:STD_LOGIC_VECTOR(7 DOWNTO 0);
signal VGA_DATA_OUT_RAM: STD_LOGIC_VECTOR(7 DOWNTO 0);


signal Echar : std_logic_vector(6 downto 0) := std_logic_vector(unsigned(char)- x"20");


type Characters is Array (15 downto 0) of std_logic_vector (7 downto 0);
signal ROMchar :Characters;


begin

VGA_RAM : ram
  PORT MAP (
    clka => CLK_50MHz,
    wea => WEn,
    addra => VGA_ADDR_RAM,
    dina => VGA_DATA_IN_RAM,
    douta => VGA_DATA_OUT_RAM
  );
  
  VGA_CHAR : VGACHAR
  PORT MAP (
    clka => CLK_50MHz,
    addra => ADDR_ROM,
    douta => DATA_OUT_ROM
  );
  
  Generate25MHz: process (CLK_50MHz)
  begin
    if rising_edge(CLK_50MHz) then
	   Clk_25MHz <= not Clk_25MHz;	 end if;
  end process Generate25MHz;
    		

  VGAPosition: process (Clk_25MHz)
  begin
    if rising_edge(Clk_25MHz) then
	   if unsigned(CurrentHPos) < HLimit-1 then
		  CurrentHPos <= std_logic_vector (unsigned(CurrentHPos) + 1);
		else
		  if unsigned(CurrentVPos) < VLimit-1 then
		    CurrentVPos <=  std_logic_vector (unsigned(CurrentVPos) + 1);
		  else
		    CurrentVPos <= (others => '0'); -- reset Vertical Position
		  end if;
		  CurrentHPos <= (others => '0'); -- reset Horizontal Position
		end if;
	 end if;
  end process VGAPosition;

  -- Timing definition for HSync, VSync and Blank (http://tinyvga.com/vga-timing/640x480@60Hz)
     HS <= '0' when unsigned(CurrentHPos) < HSyncWidth else
	        '1';
	  
	  VS <= '0' when unsigned(CurrentVPos) < VSyncWidth else
	        '1';
	  
	  HBlank <= '0' when (unsigned(CurrentHPos) >= HSyncWidth + HFrontPorch) and (unsigned(CurrentHPos) < HSyncWidth + HFrontPorch + HDisplayArea) else
	           '1';
				  
	  VBlank <= '0' when (unsigned(CurrentVPos) >= VSyncWidth + VFrontPorch) and (unsigned(CurrentVPos) < VSyncWidth + VFrontPorch + VDisplayArea) else
	           '1';				  
	  
	  Blank <= '1' when HBlank = '1' or VBlank = '1' else
	           '0';
	  
	  ScanlineX <= std_logic_vector(unsigned(CurrentHPos) - HSyncWidth - HFrontPorch) when Blank = '0' else
	               (others => '0');

	  ScanlineY <= std_logic_vector(unsigned(CurrentVPos) - VSyncWidth - VFrontPorch) when Blank = '0' else
	               (others => '0');	

     RED <= ColorOutput(2) when Blank = '0' else
            '0';	  
     GREEN <= ColorOutput(1) when Blank = '0' else
            '0';				
     BLUE <= ColorOutput(0) when Blank = '0' else
            '0';		
	  
	  
	ADDR_ROM	<= std_logic_vector (unsigned(char)-32);	-- begin from 32 to 128 so we decease 32 from ASCII char
	
	VGA_DATA_IN_RAM <= ROMchar (to_integer(unsigned(ScanlineY(3 downto 0)))) when std_logic_vector (unsigned(ScanlineX)/8) =  "0000" & Xchar and std_logic_vector (unsigned(ScanlineY)/16) =  "000000" & Ychar else
	"00000000";
	
	 WEn (0) <= '1' when std_logic_vector (unsigned(ScanlineX)/8) =  "0000" & Xchar and std_logic_vector (unsigned(ScanlineY)/16) =  "000000" & Ychar else
		'0';
	 
 	VGA_ADDR_RAM	<= std_logic_vector((unsigned(ScanlineY (7 downto 0))*80) + (unsigned(ScanlineX)/8));
	
   ColorOutput <= "010" when VGA_DATA_OUT_RAM(to_integer(unsigned(ScanlineX(2 downto 0)))) = '1' else
                 "000";
		 
	 
--	  char	<= "1001101";
	  
--	  process (CLK_50MHz)
--	  begin
--	  if rising_edge (CLK_50MHz) then
--		 if (Xchar = "1010000") then
--				Xchar	<= (others => '0');
--				Ychar	<= std_logic_vector (unsigned(Ychar)+1);
--	    end if;
--	  end if;
--	  end process;
  
  
  	ROMchar (7)  <=  DATA_OUT_ROM(07 downto 00);
	ROMchar (6)  <=  DATA_OUT_ROM(15 downto 08);
	ROMchar (5)  <=  DATA_OUT_ROM(23 downto 16);
	ROMchar (4)  <=  DATA_OUT_ROM(31 downto 24);
	ROMchar (3)  <=  DATA_OUT_ROM(39 downto 32);
	ROMchar (2)  <=  DATA_OUT_ROM(47 downto 40);
	ROMchar (1)  <=  DATA_OUT_ROM(55 downto 48);
	ROMchar (0)  <=  DATA_OUT_ROM(63 downto 56);
	
  
end Behavioral;

// VHDL entity sdc, as the project stores it:
--**********************************************************************
-- Copyright 2012 by XESS Corp <http://www.xess.com>.
-- This program is free software: you can redistribute it and/or modify
-- it under the terms of the GNU General Public License as published by
-- the Free Software Foundation, either version 3 of the License, or
-- (at your option) any later version.
--
-- This program is distributed in the hope that it will be useful,
-- but WITHOUT ANY WARRANTY; without even the implied warranty of
-- MERCHANTABILITY or FITNESS FOR A PARTICULAR PURPOSE.  See the
-- GNU General Public License for more details.
--
-- You should have received a copy of the GNU General Public License
-- along with this program.  If not, see <http://www.gnu.org/licenses/>.
--**********************************************************************

--*********************************************************************
-- SD MEMORY CARD INTERFACE
--
-- Reads/writes a single or multiple blocks of data to/from an SD Flash card.
-- 
-- Based on work by by Steven J. Merrifield, June 2008:
-- http : //stevenmerrifield.com/tools/sd.vhd
-- 
-- Most of what I learned about interfacing to SD/SDHC cards came from here:
-- http://elm-chan.org/docs/mmc/mmc_e.html
--
-- OPERATION
--
--     Set-up:
--         First of all, you have to give the controller a clock signal on the clk_i 
--         input with a higher frequency than the serial clock sent to the SD card 
--         through the sclk_o output. You can set generic parameters for the 
--         controller to tell it the master clock frequency (100 MHz), the SCLK 
--         frequency for initialization (400 KHz), the SCLK frequency for normal 
--         operation (25 MHz), the size of data sectors in the Flash memory (512 bytes),
--         and the type of card (either SD or SDHC). I typically use a 100 MHz 
--         clock if I'm running an SD card with a 25 Mbps serial data stream. 
--       
--     Initialize it:
--         Pulsing the reset_i input high and then bringing it low again will make 
--         the controller initialize the SD card so it will work in SPI mode. 
--         Basically, it sends the card the commands CMD0, CMD8 and then ACMD41 (which
--         is CMD55 followed by CMD41). The busy_o output will be high during the 
--         initialization and will go low once it is done. 
--        
--         After the initialization command sequence, the SD card will send back an R1
--         response byte. If only the IDLE bit of the R1 response is set, then the 
--         controller will repeatedly re-try the ACMD41 command while busy_o remains 
--         high. 
--        
--         If any other bit of the R1 response is set, then an error occurred. The 
--         controller will stall, lower busy_o, and output the R1 response code on the
--         error_o bus. You'll have to pulse reset_i to unfreeze the controller. 
--     
--         If the R1 response is all zeroes (i.e., no errors occurred during the 
--         initialization), then the controller will lower busy_o and wait for a 
--         read or write operation from the host. The controller will only accept new
--         operations when busy_o is low.
--     
--     Write data:
--         To write a data block to the SD card, the address of a block is placed 
--         on the addr_i input bus and the wr_i input is raised. The address and 
--         write strobe can be removed once busy_o goes high to indicate the write 
--         operation is underway. The data to be written to the SD card is passed as 
--         follows: 
--     
--         1. The controller requests a byte of data by raising the hndShk_o output.
--         2. The host applies the next byte to the data_i input bus and raises the 
--            hndShk_i input.
--         3. The controller accepts the byte and lowers the hndShk_o output.
--         4. The host lowers the hndShk_i input.
--     
--         This sequence of steps is repeated until all BLOCK_SIZE_G bytes of the 
--         data block are passed from the host to the controller. Once all the data 
--         is passed, the sector on the SD card will be written and the busy_o output 
--         will be lowered. 
--     
--     Read data:
--         To read a block of data from the SD card, the address of a block is 
--         placed on the addr_i input bus and the rd_i input is raised. The address 
--         and read strobe can be removed once busy_o goes high to indicate the read 
--         operation is underway. The data read from the SD card is passed to the 
--         host as follows: 
--     
--         1. The controller raises the hndShk_o output when the next data byte is available.
--         2. The host reads the byte from the data_o output bus and raises the hndShk_i input.
--         3. The controller lowers the hndShk_o output.
--         4. The host lowers the hndShk_i input.
--     
--         This sequence of steps is repeated until all BLOCK_SIZE_G bytes of the 
--         data block are passed from the controller to the host. Once all the data 
--         is read, the busy_o output will be lowered.
--     
--     Handle errors:
--         If an error is detected during either a read or write operation, then the
--         controller will stall, lower busy_o, and output an error code on the 
--         error_o bus. You'll have to pulse reset_i to unfreeze the controller. That 
--         may seem a bit excessive, but it does guarantee that you can't ignore any 
--         errors that occur.
--
-- TODO:
--
--     * Implement multi-block read and write commands.
--     * Allow host to send/receive SPI commands/data directly to
--       the SD card through the controller.
-- *********************************************************************


library ieee;
use ieee.std_logic_1164.all;
use ieee.numeric_std.all;
use work.CommonPckg.all;

package SdCardPckg is

  type CardType_t is (SD_CARD_E, SDHC_CARD_E);  -- Define the different types of SD cards.

  component SdCardCtrl is
    generic (
      FREQ_G          : real       := 50.0;  -- Master clock frequency (MHz).
      INIT_SPI_FREQ_G : real       := 0.4;  -- Slow SPI clock freq. during initialization (MHz).
      SPI_FREQ_G      : real       := 25.0;  -- Operational SPI freq. to the SD card (MHz).
      BLOCK_SIZE_G    : natural    := 512;  -- Number of bytes in an SD card block or sector.
      CARD_TYPE_G     : CardType_t := SD_CARD_E  -- Type of SD card connected to this controller.
      );
    port (
      -- Host-side interface signals.
      clk_i      : in  std_logic;       -- Master clock.
      reset_i    : in  std_logic                     := NO;  -- active-high, synchronous  reset.
      rd_i       : in  std_logic                     := NO;  -- active-high read block request.
      wr_i       : in  std_logic                     := NO;  -- active-high write block request.
      continue_i : in  std_logic                     := NO;  -- If true, inc address and continue R/W.
      addr_i     : in  std_logic_vector(31 downto 0) := x"00000000";  -- Block address.
      data_i     : in  std_logic_vector(7 downto 0)  := x"00";  -- Data to write to block.
      data_o     : out std_logic_vector(7 downto 0)  := x"00";  -- Data read from block.
      busy_o     : out std_logic;  -- High when controller is busy performing some operation.
      hndShk_i   : in  std_logic;  -- High when host has data to give or has taken data.
      hndShk_o   : out std_logic;  -- High when controller has taken data or has data to give.
      error_o    : out std_logic_vector(15 downto 0) := (others => NO);
      -- I/O signals to the external SD card.
      cs_bo      : out std_logic                     := HI;  -- Active-low chip-select.
      sclk_o     : out std_logic                     := LO;  -- Serial clock to SD card.
      mosi_o     : out std_logic                     := HI;  -- Serial data output to SD card.
      miso_i     : in  std_logic                     := ZERO  -- Serial data input from SD card.
      );
  end component;

end package;


library ieee;
use ieee.math_real.all;
use ieee.std_logic_1164.all;
use ieee.numeric_std.all;
use work.CommonPckg.all;
use work.SdCardPckg.all;

entity SdCardCtrl is
  generic (
    FREQ_G          : real       := 50.0;     -- Master clock frequency (MHz).
    INIT_SPI_FREQ_G : real       := 0.4;  -- Slow SPI clock freq. during initialization (MHz).
    SPI_FREQ_G      : real       := 25.0;  -- Operational SPI freq. to the SD card (MHz).
    BLOCK_SIZE_G    : natural    := 512;  -- Number of bytes in an SD card block or sector.
    CARD_TYPE_G     : CardType_t := SD_CARD_E  -- Type of SD card connected to this controller.
    );
  port (
    -- Host-side interface signals.
    clk_i      : in  std_logic;         -- Master clock.
    reset_i    : in  std_logic                     := NO;  -- active-high, synchronous  reset.
    rd_i       : in  std_logic                     := NO;  -- active-high read block request.
    wr_i       : in  std_logic                     := NO;  -- active-high write block request.
    continue_i : in  std_logic                     := NO;  -- If true, inc address and continue R/W.
    addr_i     : in  std_logic_vector(31 downto 0) := x"00000000";  -- Block address.
    data_i     : in  std_logic_vector(7 downto 0)  := x"00";  -- Data to write to block.
    data_o     : out std_logic_vector(7 downto 0)  := x"00";  -- Data read from block.
    busy_o     : out std_logic;  -- High when controller is busy performing some operation.
    hndShk_i   : in  std_logic;  -- High when host has data to give or has taken data.
    hndShk_o   : out std_logic;  -- High when controller has taken data or has data to give.
    error_o    : out std_logic_vector(15 downto 0) := (others => NO);
	 LED			: out std_logic_vector(3 downto 0)  := (others => NO);
    -- I/O signals to the external SD card.
    cs_bo      : out std_logic                     := HI;  -- Active-low chip-select.
    sclk_o     : out std_logic                     := LO;  -- Serial clock to SD card.
    mosi_o     : out std_logic                     := HI;  -- Serial data output to SD card.
    miso_i     : in  std_logic                     := ZERO  -- Serial data input from SD card.
    );
end entity;



architecture arch of SdCardCtrl is

  signal sclk_r   : std_logic := ZERO;  -- Register output drives SD card clock.
  signal hndShk_r : std_logic := NO;  -- Register output drives handshake output to host.
  signal LEDr  		: std_logic_vector(3 downto 0) := (others => NO);
begin
  
  process(clk_i)  -- FSM process for the SD card controller.

    type FsmState_t is (    -- States of the SD card controller FSM.
      START_INIT,  -- Send initialization clock pulses to the deselected SD card.    
      SEND_CMD0,                        -- Put the SD card in the IDLE state.
      CHK_CMD0_RESPONSE,    -- Check card's R1 response to the CMD0.
      SEND_CMD8,   -- This command is needed to initialize SDHC cards.
      GET_CMD8_RESPONSE,                -- Get the R7 response to CMD8.
      SEND_CMD55,                       -- Send CMD55 to the SD card. 
      SEND_CMD41,                       -- Send CMD41 to the SD card.
      CHK_ACMD41_RESPONSE,  -- Check if the SD card has left the IDLE state.     
      WAIT_FOR_HOST_RW,  -- Wait for the host to issue a read or write command.
      RD_BLK,    -- Read a block of data from the SD card.
      WR_BLK,    -- Write a block of data to the SD card.
      WR_WAIT,   -- Wait for SD card to finish writing the data block.
      START_TX,                         -- Start sending command/data.
      TX_BITS,   -- Shift out remaining command/data bits.
      GET_CMD_RESPONSE,  -- Get the R1 response of the SD card to a command.
      RX_BITS,   -- Receive response/data from the SD card.
      DESELECT,  -- De-select the SD card and send some clock pulses (Must enter with sclk at zero.)
      PULSE_SCLK,  -- Issue some clock pulses. (Must enter with sclk at zero.)
      REPORT_ERROR                      -- Report error and stall until reset.
      );
    variable state_v    : FsmState_t := START_INIT;  -- Current state of the FSM.
    variable rtnState_v : FsmState_t;  -- State FSM returns to when FSM subroutine completes.

    -- Timing constants based on the master clock frequency and the SPI SCLK frequencies.
    constant CLKS_PER_INIT_SCLK_C      : real    := FREQ_G / INIT_SPI_FREQ_G;
    constant CLKS_PER_SCLK_C           : real    := FREQ_G / SPI_FREQ_G;
    constant MAX_CLKS_PER_SCLK_C       : real    := realmax(CLKS_PER_INIT_SCLK_C, CLKS_PER_SCLK_C);
    constant MAX_CLKS_PER_SCLK_PHASE_C : natural := integer(round(MAX_CLKS_PER_SCLK_C / 2.0));
    constant INIT_SCLK_PHASE_PERIOD_C  : natural := integer(round(CLKS_PER_INIT_SCLK_C / 2.0));
    constant SCLK_PHASE_PERIOD_C       : natural := integer(round(CLKS_PER_SCLK_C / 2.0));
    constant DELAY_BETWEEN_BLOCK_RW_C  : natural := SCLK_PHASE_PERIOD_C;

    -- Registers for generating slow SPI SCLK from the faster master clock.
    variable clkDivider_v     : natural range 0 to MAX_CLKS_PER_SCLK_PHASE_C;  -- Holds the SCLK period.
    variable sclkPhaseTimer_v : natural range 0 to MAX_CLKS_PER_SCLK_PHASE_C;  -- Counts down to zero, then SCLK toggles.

    constant NUM_INIT_CLKS_C : natural := 160;  -- Number of initialization clocks to SD card.
    variable bitCnt_v        : natural range 0 to NUM_INIT_CLKS_C;  -- Tx/Rx bit counter.

    constant CRC_SZ_C    : natural := 2;  -- Number of CRC bytes for read/write blocks.
    -- When reading blocks of data, get 0xFE + [DATA_BLOCK] + [CRC].
    constant RD_BLK_SZ_C : natural := 1 + BLOCK_SIZE_G + CRC_SZ_C;
    -- When writing blocks of data, send 0xFF + 0xFE + [DATA BLOCK] + [CRC] then receive response byte.
    constant WR_BLK_SZ_C : natural := 1 + 1 + BLOCK_SIZE_G + CRC_SZ_C + 1;
    variable byteCnt_v   : natural range 0 to IntMax(WR_BLK_SZ_C, RD_BLK_SZ_C);  -- Tx/Rx byte counter.

    -- Command bytes for various SD card operations.
    subtype Cmd_t is std_logic_vector(7 downto 0);
    constant CMD0_C          : Cmd_t := std_logic_vector(to_unsigned(16#40# + 0, Cmd_t'length));
    constant CMD8_C          : Cmd_t := std_logic_vector(to_unsigned(16#40# + 8, Cmd_t'length));
    constant CMD55_C         : Cmd_t := std_logic_vector(to_unsigned(16#40# + 55, Cmd_t'length));
    constant CMD41_C         : Cmd_t := std_logic_vector(to_unsigned(16#40# + 41, Cmd_t'length));
    constant READ_BLK_CMD_C  : Cmd_t := std_logic_vector(to_unsigned(16#40# + 17, Cmd_t'length));
    constant WRITE_BLK_CMD_C : Cmd_t := std_logic_vector(to_unsigned(16#40# + 24, Cmd_t'length));

    -- Except for CMD0 and CMD8, SD card ops don't need a CRC, so use a fake one for that slot in the command.
    constant FAKE_CRC_C : std_logic_vector(7 downto 0) := x"FF";

    variable addr_v : unsigned(addr_i'range);  -- Address of current block for R/W operations.

    -- Maximum Tx to SD card consists of command + address + CRC. Data Tx is just a single byte.
    variable tx_v : std_logic_vector(CMD0_C'length + addr_v'length + FAKE_CRC_C'length - 1 downto 0);  -- Data/command to SD card.
    alias txCmd_v is tx_v;              -- Command transmission shift register.
    alias txData_v is tx_v(tx_v'high downto tx_v'high - data_i'length + 1);  -- Data byte transmission shift register.

    variable rx_v               : std_logic_vector(data_i'range);  -- Data/response byte received from SD card.
    -- Various response codes.
    subtype Response_t is std_logic_vector(rx_v'range);
    constant ACTIVE_NO_ERRORS_C : Response_t := "00000000";  -- Normal R1 code after initialization.
    constant IDLE_NO_ERRORS_C   : Response_t := "00000001";  -- Normal R1 code after CMD0.
    constant DATA_ACCEPTED_C    : Response_t := "---00101";  -- SD card accepts data block from host.
    constant DATA_REJ_CRC_C     : Response_t := "---01011";  -- SD card rejects data block from host due to CRC error.
    constant DATA_REJ_WERR_C    : Response_t := "---01101";  -- SD card rejects data block from host due to write error.
    -- Various tokens.
    subtype Token_t is std_logic_vector(rx_v'range);
    constant NO_TOKEN_C         : Token_t    := x"FF";  -- Received before the SD card responds to a block read command.
    constant START_TOKEN_C      : Token_t    := x"FE";  -- Starting byte preceding a data block.

    -- Flags that are set/cleared to affect the operation of the FSM.
    variable getCmdResponse_v : boolean;  -- When true, get R1 response to command sent to SD card.
    variable rtnData_v        : boolean;  -- When true, signal to host when a data byte arrives from SD card.
    variable doDeselect_v     : boolean;  -- When true, de-select SD card after a command is issued.
    
  begin
    if rising_edge(clk_i) then

      if reset_i = YES then             -- Perform a reset.
        state_v          := START_INIT;  -- Send the FSM to the initialization entry-point.
        sclkPhaseTimer_v := 0;  -- Don't delay the initialization right after reset.
        busy_o           <= YES;  -- Busy while the SD card interface is being initialized.

      elsif sclkPhaseTimer_v /= 0 then
        -- Setting the clock phase timer to a non-zero value delays any further actions
        -- and generates the slower SPI clock from the faster master clock.
        sclkPhaseTimer_v := sclkPhaseTimer_v - 1;

        -- Clock phase timer has reached zero, so check handshaking sync. between host and controller.

        -- Handshaking lets the host control the flow of data to/from the SD card controller.
        -- Handshaking between the SD card controller and the host proceeds as follows:
        --   1: Controller raises its handshake and waits.
        --   2: Host sees controller handshake and raises its handshake in acknowledgement.
        --   3: Controller sees host handshake acknowledgement and lowers its handshake.
        --   4: Host sees controller lower its handshake and removes its handshake.
        --
        -- Handshaking is bypassed when the controller FSM is initializing the SD card.
        
      elsif state_v /= START_INIT and hndShk_r = HI and hndShk_i = LO then
        null;            -- Waiting for the host to acknowledge handshake.
      elsif state_v /= START_INIT and hndShk_r = HI and hndShk_i = HI then
        txData_v := data_i;             -- Get any data passed from the host.
        hndShk_r <= LO;  -- The host acknowledged, so lower the controller handshake.
      elsif state_v /= START_INIT and hndShk_r = LO and hndShk_i = HI then
        null;            -- Waiting for the host to lower its handshake.
      elsif (state_v = START_INIT) or (hndShk_r = LO and hndShk_i = LO) then
        -- Both handshakes are low, so the controller operations can proceed.
        
        busy_o <= YES;  -- Busy by default. Only false when waiting for R/W from host or stalled by error.
			LEDr (3 downto 0) <= "0001";
        case state_v is
          
          when START_INIT =>  -- Deselect the SD card and send it a bunch of clock pulses with MOSI high.
            error_o          <= (others => ZERO);  -- Clear error flags.
            clkDivider_v     := INIT_SCLK_PHASE_PERIOD_C - 1;  -- Use slow SPI clock freq during init.
            sclkPhaseTimer_v := INIT_SCLK_PHASE_PERIOD_C - 1;  -- and set the duration of the next clock phase.
            sclk_r           <= LO;     -- Start with low clock to the SD card.
            hndShk_r         <= LO;     -- Initialize handshake signal.
            addr_v           := (others => ZERO);  -- Initialize address.
            rtnData_v        := false;  -- No data is returned to host during initialization.
            bitCnt_v         := NUM_INIT_CLKS_C;  -- Generate this many clock pulses.
            state_v          := DESELECT;  -- De-select the SD card and pulse SCLK.
            rtnState_v       := SEND_CMD0;  -- Then go to this state after the clock pulses are done.
				LEDr (3 downto 0) <= "0010"; --nabood
            
          when SEND_CMD0 =>             -- Put the SD card in the IDLE state.
            cs_bo            <= LO;     -- Enable the SD card.
            txCmd_v          := CMD0_C & x"00000000" & x"95";  -- 0x95 is the correct CRC for this command.
            bitCnt_v         := txCmd_v'length;  -- Set bit counter to the size of the command.
            getCmdResponse_v := true;  -- Sending a command that generates a response.
            doDeselect_v     := true;  -- De-select SD card after this command finishes.
            state_v          := START_TX;  -- Go to FSM subroutine to send the command.
            rtnState_v       := CHK_CMD0_RESPONSE;  -- Then check the response to the command.
				LEDr (3 downto 0) <= "0010"; -- Nabood
            
          when CHK_CMD0_RESPONSE =>  -- Check card's R1 response to the CMD0.
            if rx_v = IDLE_NO_ERRORS_C then
              state_v := SEND_CMD8;  -- Continue init if SD card is in IDLE state with no errors
            else
              state_v := SEND_CMD0;     -- Otherwise, try CMD0 again.
            end if;
            LEDr (3 downto 0) <= "0011";
				
          when SEND_CMD8 =>  -- This command is needed to initialize SDHC cards.
            cs_bo            <= LO;     -- Enable the SD card.
            txCmd_v          := CMD8_C & x"000001aa" & x"87";  -- 0x87 is the correct CRC for this command.
            bitCnt_v         := txCmd_v'length;  -- Set bit counter to the size of the command.
            getCmdResponse_v := true;  -- Sending a command that generates a response.
            doDeselect_v     := false;  -- Don't de-select, need to get the R7 response sent from the SD card.
            state_v          := START_TX;  -- Go to FSM subroutine to send the command.
            rtnState_v       := GET_CMD8_RESPONSE;  -- Then go to this state after the command is sent.
            LEDr (3 downto 0) <= "0100";
				
          when GET_CMD8_RESPONSE =>     -- Get the R7 response to CMD8.
            cs_bo            <= LO;  -- The SD card should already be enabled, but let's be explicit.
            bitCnt_v         := 31;     -- Four bytes (32 bits) in R7 response.
            getCmdResponse_v := false;  -- Not sending a command that generates a response.
            doDeselect_v     := true;  -- De-select card to end the command after getting the four bytes.
            state_v          := RX_BITS;  -- Go to FSM subroutine to get the R7 response.
            rtnState_v       := SEND_CMD55;  -- Then go here (we don't care what the actual R7 response is).
				LEDr (3 downto 0) <= "0101";

          when SEND_CMD55 =>  -- Send CMD55 as preamble of ACMD41 initialization command.
            cs_bo            <= LO;     -- Enable the SD card.
            txCmd_v          := CMD55_C & x"00000000" & FAKE_CRC_C;
            bitCnt_v         := txCmd_v'length;  -- Set bit counter to the size of the command.
            getCmdResponse_v := true;  -- Sending a command that generates a response.
            doDeselect_v     := true;  -- De-select SD card after this command finishes.
            state_v          := START_TX;  -- Go to FSM subroutine to send the command.
            rtnState_v       := SEND_CMD41;  -- Then go to this state after the command is sent.
		      LEDr (3 downto 0) <= "0110";
            
          when SEND_CMD41 =>  -- Send the SD card the initialization command.
            cs_bo            <= LO;     -- Enable the SD card.
            txCmd_v          := CMD41_C & x"40000000" & FAKE_CRC_C;
            bitCnt_v         := txCmd_v'length;  -- Set bit counter to the size of the command.
            getCmdResponse_v := true;  -- Sending a command that generates a response.
            doDeselect_v     := true;  -- De-select SD card after this command finishes.
            state_v          := START_TX;  -- Go to FSM subroutine to send the command.
            rtnState_v       := CHK_ACMD41_RESPONSE;  -- Then check the response to the command.
				LEDr (3 downto 0) <= "0111";
            
          when CHK_ACMD41_RESPONSE =>
            -- The CMD55, CMD41 sequence should cause the SD card to leave the IDLE state
            -- and become ready for SPI read/write operations. If still IDLE, then repeat the CMD55, CMD41 sequence.
            -- If one of the R1 error flags is set, then report the error and stall.
            if rx_v = ACTIVE_NO_ERRORS_C then   -- Not IDLE, no errors.
              state_v := WAIT_FOR_HOST_RW;  -- Start processing R/W commands from the host.
            elsif rx_v = IDLE_NO_ERRORS_C then  -- Still IDLE but no errors. 
              state_v := SEND_CMD55;    -- Repeat the CMD55, CMD41 sequence.
            else                        -- Some error occurred.
              state_v := REPORT_ERROR;  -- Report the error and stall.
            end if;
				LEDr (3 downto 0) <= "1000";
            
          when WAIT_FOR_HOST_RW =>  -- Wait for the host to read or write a block of data from the SD card.
            clkDivider_v     := SCLK_PHASE_PERIOD_C - 1;  -- Set SPI clock frequency for normal operation.
            getCmdResponse_v := true;  -- Get R1 response to any commands issued to the SD card.
            if rd_i = YES then  -- send READ command and address to the SD card.
              cs_bo <= LO;              -- Enable the SD card.
              if continue_i = YES then  -- Multi-block read. Use stored address.
                if CARD_TYPE_G = SD_CARD_E then  -- SD cards use byte-addressing, 
                  addr_v := addr_v + BLOCK_SIZE_G;  -- so add block-size to get next block address.
                else                    -- SDHC cards use block-addressing,
                  addr_v := addr_v + 1;  -- so just increment current block address.
                end if;
                txCmd_v := READ_BLK_CMD_C & std_logic_vector(addr_v) & FAKE_CRC_C;
              else                      -- Single-block read.
                txCmd_v := READ_BLK_CMD_C & addr_i & FAKE_CRC_C;  -- Use address supplied by host.
                addr_v  := unsigned(addr_i);  -- Store address for multi-block operations.
              end if;
              bitCnt_v   := txCmd_v'length;  -- Set bit counter to the size of the command.
              byteCnt_v  := RD_BLK_SZ_C;
              state_v    := START_TX;  -- Go to FSM subroutine to send the command.
              rtnState_v := RD_BLK;  -- Then go to this state to read the data block.
            elsif wr_i = YES then  -- send WRITE command and address to the SD card.
              cs_bo <= LO;              -- Enable the SD card.
              if continue_i = YES then  -- Multi-block write. Use stored address.
                if CARD_TYPE_G = SD_CARD_E then  -- SD cards use byte-addressing, 
                  addr_v := addr_v + BLOCK_SIZE_G;  -- so add block-size to get next block address.
                else                    -- SDHC cards use block-addressing,
                  addr_v := addr_v + 1;  -- so just increment current block address.
                end if;
                txCmd_v := WRITE_BLK_CMD_C & std_logic_vector(addr_v) & FAKE_CRC_C;
              else                      -- Single-block write.
                txCmd_v := WRITE_BLK_CMD_C & addr_i & FAKE_CRC_C;  -- Use address supplied by host.
                addr_v  := unsigned(addr_i);  -- Store address for multi-block operations.
              end if;
              bitCnt_v   := txCmd_v'length;  -- Set bit counter to the size of the command.
              byteCnt_v  := WR_BLK_SZ_C;    -- Set number of bytes to write.
              state_v    := START_TX;  -- Go to this FSM subroutine to send the command ...
              rtnState_v := WR_BLK;  -- then go to this state to write the data block.
            else              -- Do nothing and wait for command from host.
              cs_bo   <= HI;            -- Deselect the SD card.
              busy_o  <= NO;  -- SD card interface is waiting for R/W from host, so it's not busy.
              state_v := WAIT_FOR_HOST_RW;  -- Keep waiting for command from host.
            end if;
				LEDr (3 downto 0) <= "1001";

          when RD_BLK =>          -- Read a block of data from the SD card.
            -- Some default values for these...
            rtnData_v  := false;  -- Data is only returned to host in one place.
            bitCnt_v   := rx_v'length - 1;   -- Receiving byte-sized data.
            state_v    := RX_BITS;      -- Call the bit receiver routine.
            rtnState_v := RD_BLK;   -- Return here when done receiving a byte.
            if byteCnt_v = RD_BLK_SZ_C then  -- Initial read to prime the pump.
              byteCnt_v := byteCnt_v - 1;
            elsif byteCnt_v = RD_BLK_SZ_C -1 then  -- Then look for the data block start token.
              if rx_v = NO_TOKEN_C then  -- Receiving 0xFF means the card hasn't responded yet. Keep trying.
                null;
              elsif rx_v = START_TOKEN_C then
                rtnData_v := true;  -- Found the start token, so now start returning data byes to the host.
                byteCnt_v := byteCnt_v - 1;
              else  -- Getting anything else means something strange has happened.
                state_v := REPORT_ERROR;
              end if;
            elsif byteCnt_v >= 3 then  -- Now bytes of data from the SD card are received.
              rtnData_v := true;        -- Return this data to the host.
              byteCnt_v := byteCnt_v - 1;
            elsif byteCnt_v = 2 then  -- Receive the 1st CRC byte at the end of the data block.
              byteCnt_v := byteCnt_v - 1;
            elsif byteCnt_v = 1 then    -- Receive the 2nd
              byteCnt_v := byteCnt_v - 1;
            else    -- Reading is done, so deselect the SD card.
              sclk_r     <= LO;
              bitCnt_v   := 2;
              state_v    := DESELECT;
              rtnState_v := WAIT_FOR_HOST_RW;
            end if;
				LEDr (3 downto 0) <= "1010";
            
          when WR_BLK =>             -- Write a block of data to the SD card.
            -- Some default values for these...
            getCmdResponse_v := false;  -- Sending data bytes so there's no command response from SD card.
            bitCnt_v         := txData_v'length;  -- Transmitting byte-sized data.
            state_v          := START_TX;  -- Call the bit transmitter routine.
            rtnState_v       := WR_BLK;  -- Return here when done transmitting a byte.
            if byteCnt_v = WR_BLK_SZ_C then
              txData_v := NO_TOKEN_C;  -- Hold MOSI high for one byte before data block goes out.
            elsif byteCnt_v = WR_BLK_SZ_C - 1 then     -- Send start token.
              txData_v := START_TOKEN_C;   -- Starting token for data block.
            elsif byteCnt_v >= 4 then   -- Now send bytes in the data block.
              hndShk_r <= HI;           -- Signal host to provide data.
            -- The transmit shift register is loaded with data from host in the handshaking section above.
            elsif byteCnt_v = 3 or byteCnt_v = 2 then  -- Send two phony CRC bytes at end of packet.
              txData_v := FAKE_CRC_C;
            elsif byteCnt_v = 1 then
              bitCnt_v   := rx_v'length - 1;
              state_v    := RX_BITS;  -- Get response of SD card to the write operation.
              rtnState_v := WR_WAIT;
            else                        -- Check received response byte.
              if std_match(rx_v, DATA_ACCEPTED_C) then  -- Data block was accepted.
                state_v := WR_WAIT;  -- Wait for the SD card to finish writing the data into Flash.
              else                      -- Data block was rejected.
                error_o(15 downto 8) <= rx_v;
                state_v              := REPORT_ERROR;  -- Report the error.
              end if;
            end if;
            byteCnt_v := byteCnt_v - 1;
				LEDr (3 downto 0) <= "1011";
            
          when WR_WAIT =>  -- Wait for SD card to finish writing the data block.
            -- The SD card will pull MISO low while it is busy, and raise it when it is done.
            sclk_r           <= not sclk_r;    -- Toggle the SPI clock...
            sclkPhaseTimer_v := clkDivider_v;  -- and set the duration of the next clock phase.
            if sclk_r = HI and miso_i = HI then  -- Data block has been written, so deselect the SD card.
              bitCnt_v   := 2;
              state_v    := DESELECT;
              rtnState_v := WAIT_FOR_HOST_RW;
            end if;
				LEDr (3 downto 0) <= "1100";
            
          when START_TX =>
            -- Start sending command/data by lowering SCLK and outputing MSB of command/data
            -- so it has plenty of setup before the rising edge of SCLK.
            sclk_r           <= LO;  -- Lower the SCLK (although it should already be low).
            sclkPhaseTimer_v := clkDivider_v;  -- Set the duration of the low SCLK.
            mosi_o           <= tx_v(tx_v'high);  -- Output MSB of command/data.
            tx_v             := tx_v(tx_v'high-1 downto 0) & ONE;  -- Shift command/data register by one bit.
            bitCnt_v         := bitCnt_v - 1;  -- The first bit has been sent, so decrement bit counter.
            state_v          := TX_BITS;  -- Go here to shift out the rest of the command/data bits.
				LEDr (3 downto 0) <= "1101";
            
          when TX_BITS =>  -- Shift out remaining command/data bits and (possibly) get response from SD card.
            sclk_r           <= not sclk_r;    -- Toggle the SPI clock...
            sclkPhaseTimer_v := clkDivider_v;  -- and set the duration of the next clock phase.
            if sclk_r = HI then
              -- SCLK is going to be flipped from high to low, so output the next command/data bit
              -- so it can setup while SCLK is low.
              if bitCnt_v /= 0 then  -- Keep sending bits until the bit counter hits zero.
                mosi_o   <= tx_v(tx_v'high);
                tx_v     := tx_v(tx_v'high-1 downto 0) & ONE;
                bitCnt_v := bitCnt_v - 1;
              else
                if getCmdResponse_v then
                  state_v  := GET_CMD_RESPONSE;  -- Get a response to the command from the SD card.
                  bitCnt_v := Response_t'length - 1;  -- Length of the expected response.
                else
                  state_v          := rtnState_v;  -- Return to calling state (no need to get a response).
                  sclkPhaseTimer_v := 0;  -- Clear timer so next SPI op can begin ASAP with SCLK low.
                end if;
              end if;
            end if;
				LEDr (3 downto 0) <= "1110";

          when GET_CMD_RESPONSE =>  -- Get the response of the SD card to a command.
            if sclk_r = HI and miso_i = LO then  -- MISO will be held high by SD card until 1st bit of R1 response, which is 0.
              -- Shift in the MSB bit of the response.
              rx_v     := rx_v(rx_v'high-1 downto 0) & miso_i;
              bitCnt_v := bitCnt_v - 1;
              state_v  := RX_BITS;  -- Now receive the reset of the response.
            end if;
            sclk_r           <= not sclk_r;    -- Toggle the SPI clock...
            sclkPhaseTimer_v := clkDivider_v;  -- and set the duration of the next clock phase.
				LEDr (3 downto 0) <= "1010";
				
          when RX_BITS =>               -- Receive bits from the SD card.
            if sclk_r = HI then    -- Bits enter after the rising edge of SCLK.
              rx_v := rx_v(rx_v'high-1 downto 0) & miso_i;
              if bitCnt_v /= 0 then     -- More bits left to receive.
                bitCnt_v := bitCnt_v - 1;
              else                      -- Last bit has been received.
                if rtnData_v then       -- Send the received data to the host.
                  data_o   <= rx_v;     -- Output received data to the host.
                  hndShk_r <= HI;  -- Signal to the host that the data is ready.
                end if;
                if doDeselect_v then
                  bitCnt_v := 1;
                  state_v  := DESELECT;  -- De-select SD card before returning.
                else
                  state_v := rtnState_v;  -- Otherwise, return to calling state without de-selecting.
                end if;
              end if;
            end if;
            sclk_r           <= not sclk_r;    -- Toggle the SPI clock...
            sclkPhaseTimer_v := clkDivider_v;  -- and set the duration of the next clock phase.
            LEDr (3 downto 0) <= "0000";
				
          when DESELECT =>  -- De-select the SD card and send some clock pulses (Must enter with sclk at zero.)
            doDeselect_v     := false;  -- Once the de-select is done, clear the flag that caused it.
            cs_bo            <= HI;     -- De-select the SD card.
            mosi_o           <= HI;  -- Keep the data input of the SD card pulled high.
            state_v          := PULSE_SCLK;  -- Pulse the clock so the SD card will see the de-select.
            sclk_r           <= LO;  -- Clock is set low so the next rising edge will see the new CS and MOSI
            sclkPhaseTimer_v := clkDivider_v;  -- Set the duration of the next clock phase.
            LEDr (3 downto 0) <= "0001";
				
          when PULSE_SCLK =>  -- Issue some clock pulses. (Must enter with sclk at zero.)
            if sclk_r = HI then
              if bitCnt_v /= 0 then
                bitCnt_v := bitCnt_v - 1;
              else  -- Return to the calling routine when the pulse counter reaches zero.
                state_v := rtnState_v;
              end if;
            end if;
            sclk_r           <= not sclk_r;    -- Toggle the SPI clock...
            sclkPhaseTimer_v := clkDivider_v;  -- and set the duration of the next clock phase.
            LEDr (3 downto 0) <= "0010";  --nabood
				
          when REPORT_ERROR =>  -- Report the error code and stall here until a reset occurs.
            error_o(rx_v'range) <= rx_v;  -- Output the SD card response as the error code.
            busy_o              <= NO;  -- Not busy.
				LEDr (3 downto 0) <= "0011";
				
          when others =>
            state_v := WAIT_FOR_HOST_RW;
				LEDr (3 downto 0) <= "0100"; -- hamin bood
        end case;
      end if;
    end if;
  end process;

  sclk_o   <= sclk_r;    -- Output the generated SPI clock for the SD card.
  hndShk_o <= hndShk_r;  -- Output the generated handshake to the host.
  LED (3 downto 0) <= LEDr (3 downto 0);
end architecture;




--**********************************************************************
-- This module connects the SD card controller interface to a HostIoToDut
-- interface so the controller can be tested from a PC over a USB link.
--**********************************************************************
